// Logisim project RapidRoll.circ as structural Verilog
module principal (
  input  in_1,
  output [6:0] out_2
);

  wire _11_10, and_15_out, and_18_out, and_19_out, and_21_out, and_23_out, and_24_out, and_27_out,
       and_28_out, and_30_out, and_32_out, and_33_out, and_34_out, and_35_out, and_36_out, and_37_out,
       and_38_out, and_39_out, Cho1, Cho2, Cho3, Cho4, Cho5, Cho6, Cho7, Cho8, Cho9, Cho10, Cho11, Cho12,
       Cho13, Cho14, Cho15, Cho16, ckey, clkor, clock_2_out, clock_3_out, clock_4_out, cnt, comparator_1_eq,
       comparator_2_eq, comparator_4_eq, cont1, d_ff_1_q, d_ff_3_q, d_ff_4_q, d_ff_5_q, d_ff_6_q, d_ff_7_q,
       d_ff_8_q, d_ff_9_q, d_ff_10_q, d_ff_11_q, d_ff_12_q, d_ff_13_q, d_ff_14_q, d_ff_15_q, d_ff_16_q,
       d_ff_17_q, d_ff_18_q, Ena, Gano, Gover_a, Gover_b, Mayor100, Next, not_2_out, or1, or2, or_1_out,
       or_10_out, or_20_out, or_21_out, or_22_out, or_25_out, or_27_out, or_29_out, or_31_out, or_34_out,
       or_35_out, or_37_out, or_39_out, or_42_out, or_45_out, or_46_out, or_48_out, or_50_out, or_52_out,
       or_55_out, or_56_out, or_58_out, Rese, Reset, Rs1, Rs2, Rs3, Rs4, Rs5, Rs6, Rs7, Rs8, Rs9, Rs10, Rs11,
       Rs12, Rs13, Rs14, Rs15, Rs16, Sal, Sal1, Sal2, Sal3, Sal4, Sal5, Sal6, Sal7, Sal8, Sal9, Sal10, Sal11,
       Sal12, Sal13, Sal14, Sal15, Sal16, Salida, sir, undriven;
  wire [0:0] Direccion;
  wire [3:0] ldig, rdig;
  wire [7:0] adder_1_out, adder_2_out, counter_1_q, counter_3_q, multiplexer_1_out, R, reg1, RESTO;
  wire [7:4] divider_1_out, divider_1_rem;
  wire [31:0] _1, _2, _3, _4, _5, _6, _7, _8, _9, _10, _11, _12, _13, _14, _15, _16, a, and_1_out, and_2_out,
       and_4_out, and_6_out, and_7_out, and_8_out, and_9_out, and_10_out, and_12_out, and_13_out, and_14_out,
       and_17_out, and_20_out, and_22_out, and_25_out, and_26_out, b, barreraspel_1_out_2,
       barreraspel_2_out_2, barreraspel_3_out_2, barreraspel_4_out_2, barreraspel_5_out_2,
       barreraspel_6_out_2, barreraspel_7_out_2, barreraspel_8_out_2, barreraspel_9_out_2,
       barreraspel_10_out_2, barreraspel_11_out_2, barreraspel_12_out_2, barreraspel_13_out_2,
       barreraspel_14_out_2, barreraspel_15_out_2, barreraspel_16_out_2, c, ca, cb, cc, cd, ce, cf, cg, ch,
       ci, cj, ck, cl, cm, cn, co, counter_2_q, cp, d, e, f, g, h, i, j, k, l, m, n, o, or_9_out, P, p_t,
       Pan, pantalla_game_over_1__0, pantalla_game_over_1__1, pantalla_game_over_1__2,
       pantalla_game_over_1__3, pantalla_game_over_1__4, random_1_out;

  \var  var_1 (.Col(and_1_out), .salida(Rs1));
  assign and_1_out = barreraspel_1_out_2 & p_t;  // AND_Gate and_1, 32 bits wide
  BarrerasPEL barreraspel_1 (.Entrada(_1), .out_2(barreraspel_1_out_2));
  or or_1 (or_1_out, Gano, Mayor100);
  assign _1 = cp | P;  // OR_Gate or_2, 32 bits wide
  assign _2 = co | o;  // OR_Gate or_3, 32 bits wide
  D_Flip_Flop d_ff_1 (.Q(d_ff_1_q), .preset(or_1_out));  // open: clk, D, Qn, en, reset
  assign _3 = cn | n;  // OR_Gate or_4, 32 bits wide
  assign _4 = cm | m;  // OR_Gate or_5, 32 bits wide
  assign and_2_out = barreraspel_2_out_2 & p_t;  // AND_Gate and_2, 32 bits wide
  BarrerasPEL barreraspel_2 (.Entrada(_2), .out_2(barreraspel_2_out_2));
  Pantalla_Game_Over pantalla_game_over_1 (
    .GAMEOVER(Gover_a), .GANOUSER(Gover_b), ._0(pantalla_game_over_1__0), ._1(pantalla_game_over_1__1),
    ._2(pantalla_game_over_1__2), ._3(pantalla_game_over_1__3), ._4(pantalla_game_over_1__4));
  DotMatrix #(.inputtype("row"), .matrixcols(32), .matrixrows(5)) dotmatrix_1 (
    .row0(pantalla_game_over_1__0), .row1(pantalla_game_over_1__1), .row2(pantalla_game_over_1__2),
    .row3(pantalla_game_over_1__3), .row4(pantalla_game_over_1__4));
  not not_1 (Gover_b, d_ff_1_q);
  assign _6 = ck | k;  // OR_Gate or_6, 32 bits wide
  assign _5 = cl | l;  // OR_Gate or_7, 32 bits wide
  assign _7 = cj | j;  // OR_Gate or_8, 32 bits wide
  assign or_9_out = ca | cb | cc | cd | ce | cf | cg | ch | ci | cj | ck | cl | cm | cn | co | cp;  // OR_Gate or_9, 32 bits wide
  Random #(.width(32)) random_1 (.clk(in_1), .out(random_1_out));  // open: next, clr
  \var  var_2 (.Col(and_2_out), .salida(Rs2));
  or or_10 (or_10_out, Rs1, Rs2, Rs3, Rs4, Rs5, Rs6, Rs7, Rs8, Rs9, Rs10, Rs11, Rs12, Rs13, Rs14, Rs15, Rs16);
  DotMatrix #(.matrixcols(16), .matrixrows(32)) dotmatrix_2 (
    .col0(_1), .col1(_2), .col2(_3), .col3(_4), .col4(_5), .col5(_6), .col6(_7), .col7(_8), .col8(_9),
    .col9(_10), .col10(_11), .col11(_12), .col12(_13), .col13(_14), .col14(_15), .col15(_16));
  Keyboard keyboard_1 (.clk(ckey), .data(out_2));  // open: re, clr, avail
  assign _8 = ci | i;  // OR_Gate or_11, 32 bits wide
  assign _9 = ch | h;  // OR_Gate or_12, 32 bits wide
  assign _10 = cg | g;  // OR_Gate or_13, 32 bits wide
  assign p_t = or_9_out & random_1_out;  // AND_Gate and_3, 32 bits wide
  assign and_4_out = barreraspel_3_out_2 & p_t;  // AND_Gate and_4, 32 bits wide
  BarrerasPEL barreraspel_3 (.Entrada(_3), .out_2(barreraspel_3_out_2));
  and and_5 (Reset, or_10_out, 1'b1);
  D_Flip_Flop d_ff_2 (.Q(Gover_a), .preset(Reset));  // open: clk, D, Qn, en, reset
  assign _11 = cf | f;  // OR_Gate or_14, 32 bits wide
  assign _12 = ce | e;  // OR_Gate or_15, 32 bits wide
  \var  var_3 (.Col(and_4_out), .salida(Rs3));
  Hex_Digit_Display hex_digit_display_1 (.value(ldig));  // open: dp
  DotMatrix #(.matrixcols(1), .matrixrows(32), .dotshape("circle")) dotmatrix_3 (.col0(p_t));
  assign _13 = cd | d;  // OR_Gate or_16, 32 bits wide
  assign _14 = cc | c;  // OR_Gate or_17, 32 bits wide
  assign _15 = cb | b;  // OR_Gate or_18, 32 bits wide
  Hex_Digit_Display hex_digit_display_2 (.value(rdig));  // open: dp
  Button Comenzar (.out(Rese));
  Button Crear_Personaje (.out(Next));
  assign _16 = ca | a;  // OR_Gate or_19, 32 bits wide
  \var  var_4 (.Col(and_6_out), .salida(Rs4));
  assign and_6_out = barreraspel_4_out_2 & p_t;  // AND_Gate and_6, 32 bits wide
  BarrerasPEL barreraspel_4 (.Entrada(_4), .out_2(barreraspel_4_out_2));
  \var  var_5 (.Col(and_7_out), .salida(Rs5));
  assign and_7_out = barreraspel_5_out_2 & p_t;  // AND_Gate and_7, 32 bits wide
  BarrerasPEL barreraspel_5 (.Entrada(_5), .out_2(barreraspel_5_out_2));
  assign and_8_out = barreraspel_6_out_2 & p_t;  // AND_Gate and_8, 32 bits wide
  BarrerasPEL barreraspel_6 (.Entrada(_6), .out_2(barreraspel_6_out_2));
  \var  var_6 (.Col(and_8_out), .salida(Rs6));
  \var  var_7 (.Col(and_9_out), .salida(Rs7));
  assign and_9_out = barreraspel_7_out_2 & p_t;  // AND_Gate and_9, 32 bits wide
  BarrerasPEL barreraspel_7 (.Entrada(_7), .out_2(barreraspel_7_out_2));
  player player (
    .Reloj(ckey), .en(Ena), .in_4({_11_10, Direccion[0]}), .one(a), .two(b), .three(c), .six(f), .five(e),
    .seven(g), .eight(h), .nine(i), .ten(j), .eleven(k), .twelve(l), .thirteen(m), .fourteen(n), .fifteen(o),
    .sixteen(P), .four(d), .Teclado(or_21_out), .in_5(Next));
  codificador codificador_1 (
    .out_8(cp), .out_9(co), .out_13(cn), .out_6(cm), .out_4(cl), .out_15(ck), .out_18(cj), .out_17(ci),
    .out_10(ch), .out_16(cg), .out_3(cf), .out_11(ce), .out_14(cd), .out_7(cc), .out_12(cb), .out_5(ca),
    .clk(clkor), .Reset(or_20_out));
  \var  var_8 (.Col(and_10_out), .salida(Rs8));
  assign and_10_out = barreraspel_8_out_2 & p_t;  // AND_Gate and_10, 32 bits wide
  BarrerasPEL barreraspel_8 (.Entrada(_8), .out_2(barreraspel_8_out_2));
  Comparator #(.width(4)) comparator_1 (.a(rdig), .b(4'b1001), .eq(comparator_1_eq));  // open: gt, lt
  and and_11 (Gano, comparator_1_eq, comparator_2_eq);
  Comparator #(.width(4)) comparator_2 (.a(ldig), .b(4'b1001), .eq(comparator_2_eq));  // open: gt, lt
  or or_20 (or_20_out, Gano, Mayor100, Reset);
  Adder adder_1 (.a(reg1), .b(8'h1), .out(adder_1_out));  // open: cin, cout
  Adder adder_2 (.a(8'ha), .b(reg1), .out(adder_2_out));  // open: cin, cout
  Comparator #(.width(1)) comparator_3 (.a(1'b1), .b(sir), .eq(or1));  // open: gt, lt
  or or_21 (or_21_out, Reset, Mayor100, Gano);
  Clock #(.highDuration(6)) clock_1 (.out(ckey));
  assign and_12_out = barreraspel_9_out_2 & p_t;  // AND_Gate and_12, 32 bits wide
  BarrerasPEL barreraspel_9 (.Entrada(_9), .out_2(barreraspel_9_out_2));
  Multiplexer #(.width(8)) multiplexer_1 (
    .in0(adder_1_out), .in1(adder_2_out), .out(multiplexer_1_out), .sel(sir), .en(or_22_out));
  or or_22 (or_22_out, sir, cont1);
  assign Pan = a | b | c | d | e | f | g | h | i | j | k | l | m | n | o | P;  // OR_Gate or_23, 32 bits wide
  Counter counter_1 (.count(cnt), .Q(counter_1_q), .clk(clock_2_out), .clr(sir));  // open: load, D, carry
  Clock #(.lowDuration(2)) clock_2 (.out(clock_2_out));
  \var  var_9 (.Col(and_12_out), .salida(Rs9));
  Register register_1 (.D(multiplexer_1_out), .Q(reg1), .clk(clock_3_out), .clr(or_25_out));  // open: en
  Clock #(.highDuration(6)) clock_3 (.out(clock_3_out));
  or or_24 (Salida, Sal, sir);
  Comparator comparator_4 (.a(counter_1_q), .b(8'h5), .eq(comparator_4_eq), .lt(cnt));  // open: gt
  or or_25 (or_25_out, Gano, Mayor100, Reset);
  Comparator #(.width(1)) comparator_5 (.a(1'b1), .b(Sal), .eq(or2));  // open: gt, lt
  Comparator #(.width(32)) comparator_6 (.a(32'hc0000000), .b(Pan), .eq(sir));  // open: gt, lt
  // Probe on {_11_10, Direccion[0]}
  teclado teclado_1 (
    .e6(out_2[6]), .e5(out_2[5]), .e4(out_2[4]), .e3(out_2[3]), .e2(out_2[2]), .e1(out_2[1]), .e0(out_2[0]),
    .s1(_11_10), .s0(Direccion[0]));
  \var  var_10 (.Col(and_13_out), .salida(Rs10));
  assign and_13_out = barreraspel_10_out_2 & p_t;  // AND_Gate and_13, 32 bits wide
  BarrerasPEL barreraspel_10 (.Entrada(_10), .out_2(barreraspel_10_out_2));
  Divider divider_1 (.a(reg1), .b(8'ha), .out({divider_1_out, ldig}), .rem({divider_1_rem, rdig}));  // open: upper
  Clock #(.lowDuration(6)) clock_4 (.out(clock_4_out));
  \var  var_11 (.Col(and_14_out), .salida(Rs11));
  assign and_14_out = barreraspel_11_out_2 & p_t;  // AND_Gate and_14, 32 bits wide
  BarrerasPEL barreraspel_11 (.Entrada(_11), .out_2(barreraspel_11_out_2));
  Comparator comparator_7 (.a(reg1), .b(8'h63), .gt(Mayor100));  // open: eq, lt
  Counter #(.width(32), .max('hffffffff)) counter_2 (
    .D(counter_2_q), .Q(counter_2_q), .clk(and_15_out), .clr(not_2_out));  // open: load, count, carry
  not not_2 (not_2_out, Sal);
  and and_15 (and_15_out, clock_4_out, Sal);
  and and_16 (clkor, cnt, ckey);
  Comparator #(.width(32)) comparator_8 (.a(counter_2_q), .b(32'h1), .eq(cont1));  // open: gt, lt
  assign and_17_out = barreraspel_12_out_2 & p_t;  // AND_Gate and_17, 32 bits wide
  BarrerasPEL barreraspel_12 (.Entrada(_12), .out_2(barreraspel_12_out_2));
  \var  var_12 (.Col(and_17_out), .salida(Rs12));
  or or_26 (Sal1, _11_10, d_ff_3_q);
  or or_27 (or_27_out, Rese, and_21_out);
  or or_28 (Sal13, _11_10, d_ff_4_q);
  or or_29 (or_29_out, Rese, and_18_out);
  and and_18 (and_18_out, ~Cho13, _11_10);  // AND_Gate
  or or_30 (Sal12, _11_10, d_ff_5_q);
  or or_31 (or_31_out, Rese, and_19_out);
  and and_19 (and_19_out, ~Cho13, _11_10);  // AND_Gate
  BarreraSegura barrerasegura_1 (.Entrada(_2), .Salida(Cho2));
  BarreraSegura barrerasegura_2 (.Entrada(_1), .Salida(Cho1));
  BarreraSegura barrerasegura_3 (.Entrada(_13), .Salida(Cho13));
  \var  var_13 (.Col(and_20_out), .salida(Rs13));
  assign and_20_out = barreraspel_13_out_2 & p_t;  // AND_Gate and_20, 32 bits wide
  BarrerasPEL barreraspel_13 (.Entrada(_13), .out_2(barreraspel_13_out_2));
  D_Flip_Flop d_ff_3 (.Q(d_ff_3_q), .preset(or_27_out), .reset(Cho1));  // open: clk, D, Qn, en
  and and_21 (and_21_out, ~Cho13, _11_10);  // AND_Gate
  D_Flip_Flop d_ff_4 (.Q(d_ff_4_q), .preset(or_29_out), .reset(Cho13));  // open: clk, D, Qn, en
  D_Flip_Flop d_ff_5 (.Q(d_ff_5_q), .preset(or_31_out), .reset(Cho12));  // open: clk, D, Qn, en
  BarreraSegura barrerasegura_4 (.Entrada(_3), .Salida(Cho3));
  BarreraSegura barrerasegura_5 (.Entrada(_4), .Salida(Cho4));
  BarreraSegura barrerasegura_6 (.Entrada(_14), .Salida(Cho14));
  \var  var_14 (.Col(and_22_out), .salida(Rs14));
  assign and_22_out = barreraspel_14_out_2 & p_t;  // AND_Gate and_22, 32 bits wide
  BarrerasPEL barreraspel_14 (.Entrada(_14), .out_2(barreraspel_14_out_2));
  or or_32 (Sal11, _11_10, d_ff_7_q);
  BarreraSegura barrerasegura_7 (.Entrada(_5), .Salida(Cho5));
  BarreraSegura barrerasegura_8 (.Entrada(_15), .Salida(Cho15));
  or or_33 (Sal14, _11_10, d_ff_6_q);
  or or_34 (or_34_out, Rese, and_23_out);
  and and_23 (and_23_out, ~Cho13, _11_10);  // AND_Gate
  or or_35 (or_35_out, Rese, and_24_out);
  and and_24 (and_24_out, ~Cho13, _11_10);  // AND_Gate
  BarreraSegura barrerasegura_9 (.Entrada(_7), .Salida(Cho7));
  BarreraSegura barrerasegura_10 (.Entrada(_6), .Salida(Cho6));
  BarreraSegura barrerasegura_11 (.Entrada(_16), .Salida(Cho16));
  assign and_25_out = barreraspel_15_out_2 & p_t;  // AND_Gate and_25, 32 bits wide
  BarrerasPEL barreraspel_15 (.Entrada(_15), .out_2(barreraspel_15_out_2));
  D_Flip_Flop d_ff_6 (.Q(d_ff_6_q), .preset(or_34_out), .reset(Cho14));  // open: clk, D, Qn, en
  D_Flip_Flop d_ff_7 (.Q(d_ff_7_q), .preset(or_35_out), .reset(Cho11));  // open: clk, D, Qn, en
  BarreraSegura barrerasegura_12 (.Entrada(_8), .Salida(Cho8));
  \var  var_15 (.Col(and_25_out), .salida(Rs15));
  or or_36 (Sal2, _11_10, d_ff_8_q);
  or or_37 (or_37_out, Rese, and_27_out);
  or or_38 (Sal10, _11_10, d_ff_9_q);
  BarreraSegura barrerasegura_13 (.Entrada(_9), .Salida(Cho9));
  assign and_26_out = barreraspel_16_out_2 & p_t;  // AND_Gate and_26, 32 bits wide
  BarrerasPEL barreraspel_16 (.Entrada(_15), .out_2(barreraspel_16_out_2));
  D_Flip_Flop d_ff_8 (.Q(d_ff_8_q), .preset(or_37_out), .reset(Cho2));  // open: clk, D, Qn, en
  and and_27 (and_27_out, ~Cho1, _11_10);  // AND_Gate
  or or_39 (or_39_out, Rese, and_28_out);
  and and_28 (and_28_out, ~Cho13, _11_10);  // AND_Gate
  BarreraSegura barrerasegura_14 (.Entrada(_11), .Salida(Cho11));
  BarreraSegura barrerasegura_15 (.Entrada(_10), .Salida(Cho10));
  or or_40 (Sal, Cho1, Cho2, Cho3, Cho4, Cho5, Cho6, Cho7, Cho8, Cho9, Cho10, Cho11, Cho12, Cho13, Cho14, Cho15, Cho16);
  \var  var_16 (.Col(and_26_out), .salida(Rs16));
  D_Flip_Flop d_ff_9 (.Q(d_ff_9_q), .preset(or_39_out), .reset(Cho10));  // open: clk, D, Qn, en
  BarreraSegura barrerasegura_16 (.Entrada(_12), .Salida(Cho12));
  or or_41 (Sal3, _11_10, d_ff_10_q);
  or or_42 (or_42_out, Rese, and_30_out);
  or or_43 (Sal9, _11_10, d_ff_11_q);
  or or_44 (Sal15, _11_10, d_ff_12_q);
  Counter counter_3 (.count(undriven), .Q(counter_3_q), .clk(undriven), .clr(Reset));  // open: load, D, carry
  // AND_Gate and_29 is placed but not wired
  D_Flip_Flop d_ff_10 (.Q(d_ff_10_q), .preset(or_42_out), .reset(Cho3));  // open: clk, D, Qn, en
  and and_30 (and_30_out, ~Cho13, _11_10);  // AND_Gate
  and and_31 (Ena, Sal1, Sal2, Sal3, Sal4, Sal5, Sal6, Sal7, Sal8, Sal9, Sal10, Sal11, Sal12, Sal13, Sal14, Sal15, Sal16);
  D_Flip_Flop d_ff_11 (.Q(d_ff_11_q), .preset(or_45_out), .reset(Cho9));  // open: clk, D, Qn, en
  or or_45 (or_45_out, Rese, and_32_out);
  and and_32 (and_32_out, ~Cho13, _11_10);  // AND_Gate
  or or_46 (or_46_out, Rese, and_33_out);
  and and_33 (and_33_out, ~Cho13, _11_10);  // AND_Gate
  Divider divider_2 (.a(counter_3_q), .b(8'ha), .out(R), .rem(RESTO));  // open: upper
  D_Flip_Flop d_ff_12 (.Q(d_ff_12_q), .preset(or_46_out), .reset(Cho15));  // open: clk, D, Qn, en
  // Probe on R
  or or_47 (Sal4, _11_10, d_ff_13_q);
  or or_48 (or_48_out, Rese, and_34_out);
  and and_34 (and_34_out, ~Cho13, _11_10);  // AND_Gate
  or or_49 (Sal8, _11_10, d_ff_14_q);
  or or_50 (or_50_out, Rese, and_35_out);
  or or_51 (Sal16, _11_10, d_ff_15_q);
  D_Flip_Flop d_ff_13 (.Q(d_ff_13_q), .preset(or_48_out), .reset(Cho4));  // open: clk, D, Qn, en
  D_Flip_Flop d_ff_14 (.Q(d_ff_14_q), .preset(or_50_out), .reset(Cho8));  // open: clk, D, Qn, en
  and and_35 (and_35_out, ~Cho13, _11_10);  // AND_Gate
  or or_52 (or_52_out, Rese, and_36_out);
  and and_36 (and_36_out, ~Cho13, _11_10);  // AND_Gate
  or or_53 (Sal5, _11_10, d_ff_16_q);
  or or_54 (Sal6, _11_10, d_ff_17_q);
  D_Flip_Flop d_ff_15 (.Q(d_ff_15_q), .preset(or_52_out), .reset(Cho16));  // open: clk, D, Qn, en
  or or_55 (or_55_out, Rese, and_37_out);
  and and_37 (and_37_out, ~Cho13, _11_10);  // AND_Gate
  or or_56 (or_56_out, Rese, and_38_out);
  and and_38 (and_38_out, ~Cho13, _11_10);  // AND_Gate
  or or_57 (Sal7, _11_10, d_ff_18_q);
  or or_58 (or_58_out, Rese, and_39_out);
  and and_39 (and_39_out, ~Cho13, _11_10);  // AND_Gate
  D_Flip_Flop d_ff_16 (.Q(d_ff_16_q), .preset(or_55_out), .reset(Cho5));  // open: clk, D, Qn, en
  D_Flip_Flop d_ff_17 (.Q(d_ff_17_q), .preset(or_56_out), .reset(Cho6));  // open: clk, D, Qn, en
  D_Flip_Flop d_ff_18 (.Q(d_ff_18_q), .preset(or_58_out), .reset(Cho7));  // open: clk, D, Qn, en

  // Other names for the same wires on the sheet: Direccion[1] = _11_10; key2[6:0] = out_2; p1[31:0] = a; p2[31:0] = b;
  //   p3[31:0] = c; p4[31:0] = d; p5[31:0] = e; p6[31:0] = f; p7[31:0] = g; p8[31:0] = h; p9[31:0] = i; p10[31:0] = j;
  //   p11[31:0] = k; p12[31:0] = l; p13[31:0] = m; p14[31:0] = n; p15[31:0] = o; p16[31:0] = P

  // Notes on the sheet:
  //   Instrucciones:
  //   1. Activar el reloj a una frecuencia de 128 Hz
  //   2. Presionar el botón "Crear Personaje"
  //   3. Presionar el botón "Comenzar"
  //   4.Hacer clic sobre "Teclado" para mover
  //   a la derecha con D, izquierda con A
  //   Rapid Roll
  //   Teclado
  //   Puntaje
  //   By
  //   Juan Bojato
  //   Juan Buelvas
  //   Jesús Santiago
endmodule

module codificador (
  input  clk,
  input  Reset,
  output [31:0] out_3,
  output [31:0] out_4,
  output [31:0] out_5,
  output [31:0] out_6,
  output [31:0] out_7,
  output [31:0] out_8,
  output [31:0] out_9,
  output [31:0] out_10,
  output [31:0] out_11,
  output [31:0] out_12,
  output [31:0] out_13,
  output [31:0] out_14,
  output [31:0] out_15,
  output [31:0] out_16,
  output [31:0] out_17,
  output [31:0] out_18
);

  wire _2_12, a11, a12, a13, a14, a15, a16, a17, a18, a19, a20, a21, a22, a23, a24, a25, a26, a27, a28, a29,
       a30, barreras_1_out_3, barreras_1_out_4, barreras_1_out_5, barreras_1_out_6, barreras_1_out_7,
       barreras_1_out_8, barreras_1_out_9, barreras_1_out_10, barreras_1_out_11, barreras_1_out_12;
  wire [3:0] random_1_out, random_2_out, random_3_out, random_4_out, random_5_out, random_6_out,
       random_7_out, random_8_out, random_9_out, random_10_out, random_11_out, random_12_out, random_13_out,
       random_14_out, random_15_out, random_16_out, random_17_out, random_18_out, random_19_out,
       random_20_out, random_21_out, random_22_out, random_23_out, random_24_out, random_25_out,
       random_26_out, random_27_out, random_28_out, random_29_out, random_30_out, random_31_out,
       random_32_out;
  wire [15:0] bit_extender_1_out, bit_extender_2_out, bit_extender_3_out, bit_extender_4_out,
       bit_extender_5_out, bit_extender_6_out, bit_extender_7_out, bit_extender_8_out, bit_extender_9_out,
       bit_extender_10_out, bit_extender_11_out, bit_extender_12_out, bit_extender_13_out,
       bit_extender_14_out, bit_extender_15_out, bit_extender_16_out, bit_extender_17_out,
       bit_extender_18_out, bit_extender_19_out, bit_extender_20_out, bit_extender_21_out,
       bit_extender_22_out, bit_extender_23_out, bit_extender_24_out, bit_extender_25_out,
       bit_extender_26_out, bit_extender_27_out, bit_extender_28_out, bit_extender_29_out,
       bit_extender_30_out, bit_extender_31_out, bit_extender_32_out, v1, v2, v3, v4, v5, v6, v7, v8, v9,
       v10, v11, v12, v13, v14, v15, v16, v17, v18, v19, v20, v21, v22, v23, v24, v25, v26, v27, v28, v29,
       v30, v31, v32;

  barreras barreras_1 (
    .clk(clk), .out_3(barreras_1_out_3), .out_4(barreras_1_out_4), .out_5(barreras_1_out_5),
    .out_6(barreras_1_out_6), .out_7(barreras_1_out_7), .out_8(barreras_1_out_8), .out_9(barreras_1_out_9),
    .out_10(barreras_1_out_10), .out_11(barreras_1_out_11), .out_12(barreras_1_out_12), .out_13(a11),
    .out_14(a12), .out_15(a13), .out_16(a14), .out_17(a15), .out_18(a16), .out_19(a17), .out_20(a18),
    .out_21(a19), .out_22(a20), .out_23(a21), .out_24(a22), .out_25(a23), .out_26(a24), .out_27(a25),
    .out_28(a26), .out_29(a27), .out_30(a28), .out_31(a29), .out_32(a30), .Reset(Reset));  // open: out_33, out_34
  assign bit_extender_1_out = {{15{barreras_1_out_3}}, barreras_1_out_3};  // Bit_Extender bit_extender_1
  assign bit_extender_2_out = {{15{barreras_1_out_4}}, barreras_1_out_4};  // Bit_Extender bit_extender_2
  assign bit_extender_3_out = {{15{barreras_1_out_5}}, barreras_1_out_5};  // Bit_Extender bit_extender_3
  assign bit_extender_4_out = {{15{barreras_1_out_6}}, barreras_1_out_6};  // Bit_Extender bit_extender_4
  assign bit_extender_5_out = {{15{barreras_1_out_7}}, barreras_1_out_7};  // Bit_Extender bit_extender_5
  assign bit_extender_6_out = {{15{barreras_1_out_8}}, barreras_1_out_8};  // Bit_Extender bit_extender_6
  assign bit_extender_7_out = {{15{barreras_1_out_9}}, barreras_1_out_9};  // Bit_Extender bit_extender_7
  assign bit_extender_8_out = {{15{barreras_1_out_10}}, barreras_1_out_10};  // Bit_Extender bit_extender_8
  assign bit_extender_9_out = {{15{barreras_1_out_11}}, barreras_1_out_11};  // Bit_Extender bit_extender_9
  assign bit_extender_10_out = {{15{barreras_1_out_12}}, barreras_1_out_12};  // Bit_Extender bit_extender_10
  assign bit_extender_11_out = {{15{a11}}, a11};  // Bit_Extender bit_extender_11
  assign bit_extender_12_out = {{15{a12}}, a12};  // Bit_Extender bit_extender_12
  assign bit_extender_13_out = {{15{a13}}, a13};  // Bit_Extender bit_extender_13
  assign bit_extender_14_out = {{15{a14}}, a14};  // Bit_Extender bit_extender_14
  assign bit_extender_15_out = {{15{a15}}, a15};  // Bit_Extender bit_extender_15
  assign bit_extender_16_out = {{15{a16}}, a16};  // Bit_Extender bit_extender_16
  assign bit_extender_17_out = {{15{a17}}, a17};  // Bit_Extender bit_extender_17
  assign bit_extender_18_out = {{15{a18}}, a18};  // Bit_Extender bit_extender_18
  assign bit_extender_19_out = {{15{a19}}, a19};  // Bit_Extender bit_extender_19
  assign bit_extender_20_out = {{15{a20}}, a20};  // Bit_Extender bit_extender_20
  assign bit_extender_21_out = {{15{a21}}, a21};  // Bit_Extender bit_extender_21
  assign bit_extender_22_out = {{15{a22}}, a22};  // Bit_Extender bit_extender_22
  assign bit_extender_23_out = {{15{a23}}, a23};  // Bit_Extender bit_extender_23
  assign bit_extender_24_out = {{15{a24}}, a24};  // Bit_Extender bit_extender_24
  assign bit_extender_25_out = {{15{a25}}, a25};  // Bit_Extender bit_extender_25
  assign bit_extender_26_out = {{15{a26}}, a26};  // Bit_Extender bit_extender_26
  assign bit_extender_27_out = {{15{a27}}, a27};  // Bit_Extender bit_extender_27
  assign bit_extender_28_out = {{15{a28}}, a28};  // Bit_Extender bit_extender_28
  assign bit_extender_29_out = {{15{a29}}, a29};  // Bit_Extender bit_extender_29
  assign bit_extender_30_out = {{15{a30}}, a30};  // Bit_Extender bit_extender_30
  assign bit_extender_31_out = {{15{1'b0}}, 1'b0};  // Bit_Extender bit_extender_31
  assign bit_extender_32_out = {{15{1'b0}}, 1'b0};  // Bit_Extender bit_extender_32
  assign {out_5[0], out_12[0], out_7[0], out_14[0], out_11[0], out_3[0], out_16[0], out_10[0], out_17[0], out_18[0], out_15[0], out_4[0], out_6[0], out_13[0], out_9[0], out_8[0]} = bit_extender_1_out & v1;  // AND_Gate and_1, 16 bits wide
  assign {out_5[1], out_12[1], out_7[1], out_14[1], out_11[1], out_3[1], out_16[1], out_10[1], out_17[1], out_18[1], out_15[1], out_4[1], out_6[1], out_13[1], out_9[1], out_8[1]} = bit_extender_2_out & v2;  // AND_Gate and_2, 16 bits wide
  assign {out_5[2], out_12[2], out_7[2], out_14[2], out_11[2], out_3[2], out_16[2], out_10[2], out_17[2], out_18[2], out_15[2], out_4[2], out_6[2], out_13[2], out_9[2], out_8[2]} = bit_extender_3_out & v3;  // AND_Gate and_3, 16 bits wide
  assign {out_5[3], out_12[3], out_7[3], out_14[3], out_11[3], out_3[3], out_16[3], out_10[3], out_17[3], out_18[3], out_15[3], out_4[3], out_6[3], out_13[3], out_9[3], out_8[3]} = bit_extender_4_out & v4;  // AND_Gate and_4, 16 bits wide
  assign {out_5[4], out_12[4], out_7[4], out_14[4], out_11[4], out_3[4], out_16[4], out_10[4], out_17[4], out_18[4], out_15[4], out_4[4], out_6[4], out_13[4], out_9[4], out_8[4]} = bit_extender_5_out & v5;  // AND_Gate and_5, 16 bits wide
  assign {out_5[5], out_12[5], out_7[5], out_14[5], out_11[5], out_3[5], out_16[5], out_10[5], out_17[5], out_18[5], out_15[5], out_4[5], out_6[5], out_13[5], out_9[5], out_8[5]} = bit_extender_6_out & v6;  // AND_Gate and_6, 16 bits wide
  assign {out_5[6], out_12[6], out_7[6], out_14[6], out_11[6], out_3[6], out_16[6], out_10[6], out_17[6], out_18[6], out_15[6], out_4[6], out_6[6], out_13[6], out_9[6], out_8[6]} = bit_extender_7_out & v7;  // AND_Gate and_7, 16 bits wide
  assign {out_5[7], out_12[7], out_7[7], out_14[7], out_11[7], out_3[7], out_16[7], out_10[7], out_17[7], out_18[7], out_15[7], out_4[7], out_6[7], out_13[7], out_9[7], out_8[7]} = bit_extender_8_out & v8;  // AND_Gate and_8, 16 bits wide
  assign {out_5[8], out_12[8], out_7[8], out_14[8], out_11[8], out_3[8], out_16[8], out_10[8], out_17[8], out_18[8], out_15[8], out_4[8], out_6[8], out_13[8], out_9[8], out_8[8]} = bit_extender_9_out & v9;  // AND_Gate and_9, 16 bits wide
  assign {out_5[9], out_12[9], out_7[9], out_14[9], out_11[9], out_3[9], out_16[9], out_10[9], out_17[9], out_18[9], out_15[9], out_4[9], out_6[9], out_13[9], out_9[9], out_8[9]} = bit_extender_10_out & v10;  // AND_Gate and_10, 16 bits wide
  assign {out_5[10], out_12[10], out_7[10], out_14[10], out_11[10], out_3[10], out_16[10], out_10[10], out_17[10], out_18[10], out_15[10], out_4[10], out_6[10], out_13[10], out_9[10], out_8[10]} = bit_extender_11_out & v11;  // AND_Gate and_11, 16 bits wide
  assign {out_5[11], out_12[11], out_7[11], out_14[11], out_11[11], out_3[11], out_16[11], out_10[11], out_17[11], out_18[11], out_15[11], out_4[11], out_6[11], _2_12, out_9[11], out_8[11]} = bit_extender_12_out & v12;  // AND_Gate and_12, 16 bits wide
  assign {out_5[12], out_12[12], out_7[12], out_14[12], out_11[12], out_3[12], out_16[12], out_10[12], out_17[12], out_18[12], out_15[12], out_4[12], out_6[12], out_13[12], out_9[12], out_8[12]} = bit_extender_13_out & v13;  // AND_Gate and_13, 16 bits wide
  assign {out_5[13], out_12[13], out_7[13], out_14[13], out_11[13], out_3[13], out_16[13], out_10[13], out_17[13], out_18[13], out_15[13], out_4[13], out_6[13], out_13[13], out_9[13], out_8[13]} = bit_extender_14_out & v14;  // AND_Gate and_14, 16 bits wide
  assign {out_5[14], out_12[14], out_7[14], out_14[14], out_11[14], out_3[14], out_16[14], out_10[14], out_17[14], out_18[14], out_15[14], out_4[14], out_6[14], out_13[14], out_9[14], out_8[14]} = bit_extender_15_out & v15;  // AND_Gate and_15, 16 bits wide
  assign {out_5[15], out_12[15], out_7[15], out_14[15], out_11[15], out_3[15], out_16[15], out_10[15], out_17[15], out_18[15], out_15[15], out_4[15], out_6[15], out_13[15], out_9[15], out_8[15]} = bit_extender_16_out & v16;  // AND_Gate and_16, 16 bits wide
  assign {out_5[16], out_12[16], out_7[16], out_14[16], out_11[16], out_3[16], out_16[16], out_10[16], out_17[16], out_18[16], out_15[16], out_4[16], out_6[16], out_13[16], out_9[16], out_8[16]} = bit_extender_17_out & v17;  // AND_Gate and_17, 16 bits wide
  assign {out_5[17], out_12[17], out_7[17], out_14[17], out_11[17], out_3[17], out_16[17], out_10[17], out_17[17], out_18[17], out_15[17], out_4[17], out_6[17], out_13[17], out_9[17], out_8[17]} = bit_extender_18_out & v18;  // AND_Gate and_18, 16 bits wide
  assign {out_5[18], out_12[18], out_7[18], out_14[18], out_11[18], out_3[18], out_16[18], out_10[18], out_17[18], out_18[18], out_15[18], out_4[18], out_6[18], out_13[18], out_9[18], out_8[18]} = bit_extender_19_out & v19;  // AND_Gate and_19, 16 bits wide
  assign {out_5[19], out_12[19], out_7[19], out_14[19], out_11[19], out_3[19], out_16[19], out_10[19], out_17[19], out_18[19], out_15[19], out_4[19], out_6[19], out_13[19], out_9[19], out_8[19]} = bit_extender_20_out & v20;  // AND_Gate and_20, 16 bits wide
  assign {out_5[20], out_12[20], out_7[20], out_14[20], out_11[20], out_3[20], out_16[20], out_10[20], out_17[20], out_18[20], out_15[20], out_4[20], out_6[20], out_13[20], out_9[20], out_8[20]} = bit_extender_21_out & v21;  // AND_Gate and_21, 16 bits wide
  assign {out_5[21], out_12[21], out_7[21], out_14[21], out_11[21], out_3[21], out_16[21], out_10[21], out_17[21], out_18[21], out_15[21], out_4[21], out_6[21], out_13[21], out_9[21], out_8[21]} = bit_extender_22_out & v22;  // AND_Gate and_22, 16 bits wide
  assign {out_5[22], out_12[22], out_7[22], out_14[22], out_11[22], out_3[22], out_16[22], out_10[22], out_17[22], out_18[22], out_15[22], out_4[22], out_6[22], out_13[22], out_9[22], out_8[22]} = bit_extender_23_out & v23;  // AND_Gate and_23, 16 bits wide
  assign {out_5[23], out_12[23], out_7[23], out_14[23], out_11[23], out_3[23], out_16[23], out_10[23], out_17[23], out_18[23], out_15[23], out_4[23], out_6[23], out_13[23], out_9[23], out_8[23]} = bit_extender_24_out & v24;  // AND_Gate and_24, 16 bits wide
  assign {out_5[24], out_12[24], out_7[24], out_14[24], out_11[24], out_3[24], out_16[24], out_10[24], out_17[24], out_18[24], out_15[24], out_4[24], out_6[24], out_13[24], out_9[24], out_8[24]} = bit_extender_25_out & v25;  // AND_Gate and_25, 16 bits wide
  assign {out_5[25], out_12[25], out_7[25], out_14[25], out_11[25], out_3[25], out_16[25], out_10[25], out_17[25], out_18[25], out_15[25], out_4[25], out_6[25], out_13[25], out_9[25], out_8[25]} = bit_extender_26_out & v26;  // AND_Gate and_26, 16 bits wide
  assign {out_5[26], out_12[26], out_7[26], out_14[26], out_11[26], out_3[26], out_16[26], out_10[26], out_17[26], out_18[26], out_15[26], out_4[26], out_6[26], out_13[26], out_9[26], out_8[26]} = bit_extender_27_out & v27;  // AND_Gate and_27, 16 bits wide
  assign {out_5[27], out_12[27], out_7[27], out_14[27], out_11[27], out_3[27], out_16[27], out_10[27], out_17[27], out_18[27], out_15[27], out_4[27], out_6[27], out_13[27], out_9[27], out_8[27]} = bit_extender_28_out & v28;  // AND_Gate and_28, 16 bits wide
  assign {out_5[28], out_12[28], out_7[28], out_14[28], out_11[28], out_3[28], out_16[28], out_10[28], out_17[28], out_18[28], out_15[28], out_4[28], out_6[28], out_13[28], out_9[28], out_8[28]} = bit_extender_29_out & v29;  // AND_Gate and_29, 16 bits wide
  assign {out_5[29], out_12[29], out_7[29], out_14[29], out_11[29], out_3[29], out_16[29], out_10[29], out_17[29], out_18[29], out_15[29], out_4[29], out_6[29], out_13[29], out_9[29], out_8[29]} = bit_extender_30_out & v30;  // AND_Gate and_30, 16 bits wide
  assign {out_5[30], out_12[30], out_7[30], out_14[30], out_11[30], out_3[30], out_16[30], out_10[30], out_17[30], out_18[30], out_15[30], out_4[30], out_6[30], out_13[30], out_9[30], out_8[30]} = bit_extender_31_out & v31;  // AND_Gate and_31, 16 bits wide
  assign {out_5[31], out_12[31], out_7[31], out_14[31], out_11[31], out_3[31], out_16[31], out_10[31], out_17[31], out_18[31], out_15[31], out_4[31], out_6[31], out_13[31], out_9[31], out_8[31]} = bit_extender_32_out & v32;  // AND_Gate and_32, 16 bits wide
  Random #(.width(4)) random_1 (.clk(clk), .out(random_1_out));  // open: next, clr
  multi multi_1 (.random(random_1_out), .out_2(v1));
  multi multi_2 (.random(random_2_out), .out_2(v2));
  Random #(.width(4), .seed(30)) random_2 (.clk(clk), .out(random_2_out));  // open: next, clr
  Random #(.width(4), .seed(14)) random_3 (.clk(clk), .out(random_3_out));  // open: next, clr
  multi multi_3 (.random(random_3_out), .out_2(v3));
  Random #(.width(4), .seed(16)) random_4 (.clk(clk), .out(random_4_out));  // open: next, clr
  multi multi_4 (.random(random_4_out), .out_2(v4));
  Random #(.width(4), .seed(8)) random_5 (.clk(clk), .out(random_5_out));  // open: next, clr
  multi multi_5 (.random(random_5_out), .out_2(v5));
  multi multi_6 (.random(random_6_out), .out_2(v6));
  Random #(.width(4), .seed(5)) random_6 (.clk(clk), .out(random_6_out));  // open: next, clr
  Random #(.width(4), .seed(6)) random_7 (.clk(clk), .out(random_7_out));  // open: next, clr
  multi multi_7 (.random(random_7_out), .out_2(v7));
  Random #(.width(4), .seed(4)) random_8 (.clk(clk), .out(random_8_out));  // open: next, clr
  multi multi_8 (.random(random_8_out), .out_2(v8));
  Random #(.width(4), .seed(50)) random_9 (.clk(clk), .out(random_9_out));  // open: next, clr
  multi multi_9 (.random(random_9_out), .out_2(v9));
  Random #(.width(4), .seed(9)) random_10 (.clk(clk), .out(random_10_out));  // open: next, clr
  multi multi_10 (.random(random_10_out), .out_2(v10));
  multi multi_11 (.random(random_11_out), .out_2(v11));
  Random #(.width(4), .seed(10)) random_11 (.clk(clk), .out(random_11_out));  // open: next, clr
  multi multi_12 (.random(random_12_out), .out_2(v12));
  Random #(.width(4), .seed(11)) random_12 (.clk(clk), .out(random_12_out));  // open: next, clr
  multi multi_13 (.random(random_13_out), .out_2(v13));
  Random #(.width(4), .seed(12)) random_13 (.clk(clk), .out(random_13_out));  // open: next, clr
  multi multi_14 (.random(random_14_out), .out_2(v14));
  Random #(.width(4), .seed(13)) random_14 (.clk(clk), .out(random_14_out));  // open: next, clr
  Random #(.width(4), .seed(14)) random_15 (.clk(clk), .out(random_15_out));  // open: next, clr
  multi multi_15 (.random(random_15_out), .out_2(v15));
  multi multi_16 (.random(random_16_out), .out_2(v16));
  Random #(.width(4), .seed(36)) random_16 (.clk(clk), .out(random_16_out));  // open: next, clr
  multi multi_17 (.random(random_17_out), .out_2(v17));
  Random #(.width(4), .seed(16)) random_17 (.clk(clk), .out(random_17_out));  // open: next, clr
  Random #(.width(4), .seed(17)) random_18 (.clk(clk), .out(random_18_out));  // open: next, clr
  multi multi_18 (.random(random_18_out), .out_2(v18));
  multi multi_19 (.random(random_19_out), .out_2(v19));
  Random #(.width(4), .seed(18)) random_19 (.clk(clk), .out(random_19_out));  // open: next, clr
  multi multi_20 (.random(random_20_out), .out_2(v20));
  Random #(.width(4), .seed(19)) random_20 (.clk(clk), .out(random_20_out));  // open: next, clr
  multi multi_21 (.random(random_21_out), .out_2(v21));
  Random #(.width(4), .seed(20)) random_21 (.clk(clk), .out(random_21_out));  // open: next, clr
  Random #(.width(4), .seed(21)) random_22 (.clk(clk), .out(random_22_out));  // open: next, clr
  multi multi_22 (.random(random_22_out), .out_2(v22));
  multi multi_23 (.random(random_23_out), .out_2(v23));
  Random #(.width(4), .seed(22)) random_23 (.clk(clk), .out(random_23_out));  // open: next, clr
  multi multi_24 (.random(random_24_out), .out_2(v24));
  Random #(.width(4), .seed(23)) random_24 (.clk(clk), .out(random_24_out));  // open: next, clr
  multi multi_25 (.random(random_25_out), .out_2(v25));
  Random #(.width(4), .seed(24)) random_25 (.clk(clk), .out(random_25_out));  // open: next, clr
  multi multi_26 (.random(random_26_out), .out_2(v26));
  Random #(.width(4), .seed(25)) random_26 (.clk(clk), .out(random_26_out));  // open: next, clr
  Random #(.width(4), .seed(26)) random_27 (.clk(clk), .out(random_27_out));  // open: next, clr
  multi multi_27 (.random(random_27_out), .out_2(v27));
  multi multi_28 (.random(random_28_out), .out_2(v28));
  Random #(.width(4), .seed(27)) random_28 (.clk(clk), .out(random_28_out));  // open: next, clr
  multi multi_29 (.random(random_29_out), .out_2(v29));
  Random #(.width(4), .seed(28)) random_29 (.clk(clk), .out(random_29_out));  // open: next, clr
  multi multi_30 (.random(random_30_out), .out_2(v30));
  Random #(.width(4), .seed(29)) random_30 (.clk(clk), .out(random_30_out));  // open: next, clr
  Random #(.width(4), .seed(30)) random_31 (.clk(clk), .out(random_31_out));  // open: next, clr
  multi multi_31 (.random(random_31_out), .out_2(v31));
  Random #(.width(4), .seed(31)) random_32 (.clk(clk), .out(random_32_out));  // open: next, clr
  multi multi_32 (.random(random_32_out), .out_2(v32));

  assign out_13[11] = out_9[11];

  // Other names for the same wires on the sheet: m12[15:0] = {out_5[11], out_12[11], out_7[11], out_14[11], out_11[11], out_3[11], out_16[11], out_10[11], out_17[11], out_18[11], out_15[11], out_4[11], out_6[11], _2_12, out_9[11], out_8[11]};
  //   _10_1 = out_3[0];
  //   m1[15:0] = {out_5[0], out_12[0], out_7[0], out_14[0], out_11[0], out_3[0], out_16[0], out_10[0], out_17[0], out_18[0], out_15[0], out_4[0], out_6[0], out_13[0], out_9[0], out_8[0]};
  //   _10_2 = out_3[1];
  //   m2[15:0] = {out_5[1], out_12[1], out_7[1], out_14[1], out_11[1], out_3[1], out_16[1], out_10[1], out_17[1], out_18[1], out_15[1], out_4[1], out_6[1], out_13[1], out_9[1], out_8[1]};
  //   _10_3 = out_3[2];
  //   m3[15:0] = {out_5[2], out_12[2], out_7[2], out_14[2], out_11[2], out_3[2], out_16[2], out_10[2], out_17[2], out_18[2], out_15[2], out_4[2], out_6[2], out_13[2], out_9[2], out_8[2]};
  //   _10_4 = out_3[3];
  //   m4[15:0] = {out_5[3], out_12[3], out_7[3], out_14[3], out_11[3], out_3[3], out_16[3], out_10[3], out_17[3], out_18[3], out_15[3], out_4[3], out_6[3], out_13[3], out_9[3], out_8[3]};
  //   _10_5 = out_3[4];
  //   m5[15:0] = {out_5[4], out_12[4], out_7[4], out_14[4], out_11[4], out_3[4], out_16[4], out_10[4], out_17[4], out_18[4], out_15[4], out_4[4], out_6[4], out_13[4], out_9[4], out_8[4]};
  //   _10_6 = out_3[5];
  //   m6[15:0] = {out_5[5], out_12[5], out_7[5], out_14[5], out_11[5], out_3[5], out_16[5], out_10[5], out_17[5], out_18[5], out_15[5], out_4[5], out_6[5], out_13[5], out_9[5], out_8[5]};
  //   _10_7 = out_3[6];
  //   m7[15:0] = {out_5[6], out_12[6], out_7[6], out_14[6], out_11[6], out_3[6], out_16[6], out_10[6], out_17[6], out_18[6], out_15[6], out_4[6], out_6[6], out_13[6], out_9[6], out_8[6]};
  //   _10_8 = out_3[7];
  //   m8[15:0] = {out_5[7], out_12[7], out_7[7], out_14[7], out_11[7], out_3[7], out_16[7], out_10[7], out_17[7], out_18[7], out_15[7], out_4[7], out_6[7], out_13[7], out_9[7], out_8[7]};
  //   _10_9 = out_3[8];
  //   m9[15:0] = {out_5[8], out_12[8], out_7[8], out_14[8], out_11[8], out_3[8], out_16[8], out_10[8], out_17[8], out_18[8], out_15[8], out_4[8], out_6[8], out_13[8], out_9[8], out_8[8]};
  //   _10_10 = out_3[9];
  //   m10[15:0] = {out_5[9], out_12[9], out_7[9], out_14[9], out_11[9], out_3[9], out_16[9], out_10[9], out_17[9], out_18[9], out_15[9], out_4[9], out_6[9], out_13[9], out_9[9], out_8[9]};
  //   _10_11 = out_3[10];
  //   m11[15:0] = {out_5[10], out_12[10], out_7[10], out_14[10], out_11[10], out_3[10], out_16[10], out_10[10], out_17[10], out_18[10], out_15[10], out_4[10], out_6[10], out_13[10], out_9[10], out_8[10]};
  //   _10_12 = out_3[11]; _10_13 = out_3[12];
  //   m13[15:0] = {out_5[12], out_12[12], out_7[12], out_14[12], out_11[12], out_3[12], out_16[12], out_10[12], out_17[12], out_18[12], out_15[12], out_4[12], out_6[12], out_13[12], out_9[12], out_8[12]};
  //   _10_14 = out_3[13];
  //   m14[15:0] = {out_5[13], out_12[13], out_7[13], out_14[13], out_11[13], out_3[13], out_16[13], out_10[13], out_17[13], out_18[13], out_15[13], out_4[13], out_6[13], out_13[13], out_9[13], out_8[13]};
  //   _10_15 = out_3[14];
  //   m15[15:0] = {out_5[14], out_12[14], out_7[14], out_14[14], out_11[14], out_3[14], out_16[14], out_10[14], out_17[14], out_18[14], out_15[14], out_4[14], out_6[14], out_13[14], out_9[14], out_8[14]};
  //   _10_16 = out_3[15];
  //   m16[15:0] = {out_5[15], out_12[15], out_7[15], out_14[15], out_11[15], out_3[15], out_16[15], out_10[15], out_17[15], out_18[15], out_15[15], out_4[15], out_6[15], out_13[15], out_9[15], out_8[15]};
  //   _10_17 = out_3[16];
  //   m17[15:0] = {out_5[16], out_12[16], out_7[16], out_14[16], out_11[16], out_3[16], out_16[16], out_10[16], out_17[16], out_18[16], out_15[16], out_4[16], out_6[16], out_13[16], out_9[16], out_8[16]};
  //   _10_18 = out_3[17];
  //   m18[15:0] = {out_5[17], out_12[17], out_7[17], out_14[17], out_11[17], out_3[17], out_16[17], out_10[17], out_17[17], out_18[17], out_15[17], out_4[17], out_6[17], out_13[17], out_9[17], out_8[17]};
  //   _10_19 = out_3[18];
  //   m19[15:0] = {out_5[18], out_12[18], out_7[18], out_14[18], out_11[18], out_3[18], out_16[18], out_10[18], out_17[18], out_18[18], out_15[18], out_4[18], out_6[18], out_13[18], out_9[18], out_8[18]};
  //   _10_20 = out_3[19];
  //   m20[15:0] = {out_5[19], out_12[19], out_7[19], out_14[19], out_11[19], out_3[19], out_16[19], out_10[19], out_17[19], out_18[19], out_15[19], out_4[19], out_6[19], out_13[19], out_9[19], out_8[19]};
  //   _10_21 = out_3[20];
  //   m21[15:0] = {out_5[20], out_12[20], out_7[20], out_14[20], out_11[20], out_3[20], out_16[20], out_10[20], out_17[20], out_18[20], out_15[20], out_4[20], out_6[20], out_13[20], out_9[20], out_8[20]};
  //   _10_22 = out_3[21];
  //   m22[15:0] = {out_5[21], out_12[21], out_7[21], out_14[21], out_11[21], out_3[21], out_16[21], out_10[21], out_17[21], out_18[21], out_15[21], out_4[21], out_6[21], out_13[21], out_9[21], out_8[21]};
  //   _10_23 = out_3[22];
  //   m23[15:0] = {out_5[22], out_12[22], out_7[22], out_14[22], out_11[22], out_3[22], out_16[22], out_10[22], out_17[22], out_18[22], out_15[22], out_4[22], out_6[22], out_13[22], out_9[22], out_8[22]};
  //   _10_24 = out_3[23];
  //   m24[15:0] = {out_5[23], out_12[23], out_7[23], out_14[23], out_11[23], out_3[23], out_16[23], out_10[23], out_17[23], out_18[23], out_15[23], out_4[23], out_6[23], out_13[23], out_9[23], out_8[23]};
  //   _10_25 = out_3[24];
  //   m25[15:0] = {out_5[24], out_12[24], out_7[24], out_14[24], out_11[24], out_3[24], out_16[24], out_10[24], out_17[24], out_18[24], out_15[24], out_4[24], out_6[24], out_13[24], out_9[24], out_8[24]};
  //   _10_26 = out_3[25];
  //   m26[15:0] = {out_5[25], out_12[25], out_7[25], out_14[25], out_11[25], out_3[25], out_16[25], out_10[25], out_17[25], out_18[25], out_15[25], out_4[25], out_6[25], out_13[25], out_9[25], out_8[25]};
  //   _10_27 = out_3[26];
  //   m27[15:0] = {out_5[26], out_12[26], out_7[26], out_14[26], out_11[26], out_3[26], out_16[26], out_10[26], out_17[26], out_18[26], out_15[26], out_4[26], out_6[26], out_13[26], out_9[26], out_8[26]};
  //   _10_28 = out_3[27];
  //   m28[15:0] = {out_5[27], out_12[27], out_7[27], out_14[27], out_11[27], out_3[27], out_16[27], out_10[27], out_17[27], out_18[27], out_15[27], out_4[27], out_6[27], out_13[27], out_9[27], out_8[27]};
  //   _10_29 = out_3[28];
  //   m29[15:0] = {out_5[28], out_12[28], out_7[28], out_14[28], out_11[28], out_3[28], out_16[28], out_10[28], out_17[28], out_18[28], out_15[28], out_4[28], out_6[28], out_13[28], out_9[28], out_8[28]};
  //   _10_30 = out_3[29];
  //   m30[15:0] = {out_5[29], out_12[29], out_7[29], out_14[29], out_11[29], out_3[29], out_16[29], out_10[29], out_17[29], out_18[29], out_15[29], out_4[29], out_6[29], out_13[29], out_9[29], out_8[29]};
  //   _10_31 = out_3[30];
  //   m31[15:0] = {out_5[30], out_12[30], out_7[30], out_14[30], out_11[30], out_3[30], out_16[30], out_10[30], out_17[30], out_18[30], out_15[30], out_4[30], out_6[30], out_13[30], out_9[30], out_8[30]};
  //   _10_32 = out_3[31];
  //   m32[15:0] = {out_5[31], out_12[31], out_7[31], out_14[31], out_11[31], out_3[31], out_16[31], out_10[31], out_17[31], out_18[31], out_15[31], out_4[31], out_6[31], out_13[31], out_9[31], out_8[31]};
  //   _4_1 = out_4[0]; _4_2 = out_4[1]; _4_3 = out_4[2]; _4_4 = out_4[3]; _4_5 = out_4[4]; _4_6 = out_4[5];
  //   _4_7 = out_4[6]; _4_8 = out_4[7]; _4_9 = out_4[8]; _4_10 = out_4[9]; _4_11 = out_4[10]; _4_12 = out_4[11];
  //   _4_13 = out_4[12]; _4_14 = out_4[13]; _4_15 = out_4[14]; _4_16 = out_4[15]; _4_17 = out_4[16];
  //   _4_18 = out_4[17]; _4_19 = out_4[18]; _4_20 = out_4[19]; _4_21 = out_4[20]; _4_22 = out_4[21];
  //   _4_23 = out_4[22]; _4_24 = out_4[23]; _4_25 = out_4[24]; _4_26 = out_4[25]; _4_27 = out_4[26];
  //   _4_28 = out_4[27]; _4_29 = out_4[28]; _4_30 = out_4[29]; _4_31 = out_4[30]; _4_32 = out_4[31]; _15_1 = out_5[0];
  //   _15_2 = out_5[1]; _15_3 = out_5[2]; _15_4 = out_5[3]; _15_5 = out_5[4]; _15_6 = out_5[5]; _15_7 = out_5[6];
  //   _15_8 = out_5[7]; _15_9 = out_5[8]; _15_10 = out_5[9]; _15_11 = out_5[10]; _15_12 = out_5[11];
  //   _15_13 = out_5[12]; _15_14 = out_5[13]; _15_15 = out_5[14]; _15_16 = out_5[15]; _15_17 = out_5[16];
  //   _15_18 = out_5[17]; _15_19 = out_5[18]; _15_20 = out_5[19]; _15_21 = out_5[20]; _15_22 = out_5[21];
  //   _15_23 = out_5[22]; _15_24 = out_5[23]; _15_25 = out_5[24]; _15_26 = out_5[25]; _15_27 = out_5[26];
  //   _15_28 = out_5[27]; _15_29 = out_5[28]; _15_30 = out_5[29]; _15_31 = out_5[30]; _15_32 = out_5[31];
  //   _3_1 = out_6[0]; _3_2 = out_6[1]; _3_3 = out_6[2]; _3_4 = out_6[3]; _3_5 = out_6[4]; _3_6 = out_6[5];
  //   _3_7 = out_6[6]; _3_8 = out_6[7]; _3_9 = out_6[8]; _3_10 = out_6[9]; _3_11 = out_6[10]; _3_12 = out_6[11];
  //   _3_13 = out_6[12]; _3_14 = out_6[13]; _3_15 = out_6[14]; _3_16 = out_6[15]; _3_17 = out_6[16];
  //   _3_18 = out_6[17]; _3_19 = out_6[18]; _3_20 = out_6[19]; _3_21 = out_6[20]; _3_22 = out_6[21];
  //   _3_23 = out_6[22]; _3_24 = out_6[23]; _3_25 = out_6[24]; _3_26 = out_6[25]; _3_27 = out_6[26];
  //   _3_28 = out_6[27]; _3_29 = out_6[28]; _3_30 = out_6[29]; _3_31 = out_6[30]; _3_32 = out_6[31]; _13_1 = out_7[0];
  //   _13_2 = out_7[1]; _13_3 = out_7[2]; _13_4 = out_7[3]; _13_5 = out_7[4]; _13_6 = out_7[5]; _13_7 = out_7[6];
  //   _13_8 = out_7[7]; _13_9 = out_7[8]; _13_10 = out_7[9]; _13_11 = out_7[10]; _13_12 = out_7[11];
  //   _13_13 = out_7[12]; _13_14 = out_7[13]; _13_15 = out_7[14]; _13_16 = out_7[15]; _13_17 = out_7[16];
  //   _13_18 = out_7[17]; _13_19 = out_7[18]; _13_20 = out_7[19]; _13_21 = out_7[20]; _13_22 = out_7[21];
  //   _13_23 = out_7[22]; _13_24 = out_7[23]; _13_25 = out_7[24]; _13_26 = out_7[25]; _13_27 = out_7[26];
  //   _13_28 = out_7[27]; _13_29 = out_7[28]; _13_30 = out_7[29]; _13_31 = out_7[30]; _13_32 = out_7[31];
  //   _0_1 = out_8[0]; _0_2 = out_8[1]; _0_3 = out_8[2]; _0_4 = out_8[3]; _0_5 = out_8[4]; _0_6 = out_8[5];
  //   _0_7 = out_8[6]; _0_8 = out_8[7]; _0_9 = out_8[8]; _0_10 = out_8[9]; _0_11 = out_8[10]; _0_12 = out_8[11];
  //   _0_13 = out_8[12]; _0_14 = out_8[13]; _0_15 = out_8[14]; _0_16 = out_8[15]; _0_17 = out_8[16];
  //   _0_18 = out_8[17]; _0_19 = out_8[18]; _0_20 = out_8[19]; _0_21 = out_8[20]; _0_22 = out_8[21];
  //   _0_23 = out_8[22]; _0_24 = out_8[23]; _0_25 = out_8[24]; _0_26 = out_8[25]; _0_27 = out_8[26];
  //   _0_28 = out_8[27]; _0_29 = out_8[28]; _0_30 = out_8[29]; _0_31 = out_8[30]; _0_32 = out_8[31]; _1_1 = out_9[0];
  //   _1_2 = out_9[1]; _1_3 = out_9[2]; _1_4 = out_9[3]; _1_5 = out_9[4]; _1_6 = out_9[5]; _1_7 = out_9[6];
  //   _1_8 = out_9[7]; _1_9 = out_9[8]; _1_10 = out_9[9]; _1_11 = out_9[10]; _1_13 = out_9[12]; _1_14 = out_9[13];
  //   _1_15 = out_9[14]; _1_16 = out_9[15]; _1_17 = out_9[16]; _1_18 = out_9[17]; _1_19 = out_9[18];
  //   _1_20 = out_9[19]; _1_21 = out_9[20]; _1_22 = out_9[21]; _1_23 = out_9[22]; _1_24 = out_9[23];
  //   _1_25 = out_9[24]; _1_26 = out_9[25]; _1_27 = out_9[26]; _1_28 = out_9[27]; _1_29 = out_9[28];
  //   _1_30 = out_9[29]; _1_31 = out_9[30]; _1_32 = out_9[31]; _8_1 = out_10[0]; _8_2 = out_10[1]; _8_3 = out_10[2];
  //   _8_4 = out_10[3]; _8_5 = out_10[4]; _8_6 = out_10[5]; _8_7 = out_10[6]; _8_8 = out_10[7]; _8_9 = out_10[8];
  //   _8_10 = out_10[9]; _8_11 = out_10[10]; _8_12 = out_10[11]; _8_13 = out_10[12]; _8_14 = out_10[13];
  //   _8_15 = out_10[14]; _8_16 = out_10[15]; _8_17 = out_10[16]; _8_18 = out_10[17]; _8_19 = out_10[18];
  //   _8_20 = out_10[19]; _8_21 = out_10[20]; _8_22 = out_10[21]; _8_23 = out_10[22]; _8_24 = out_10[23];
  //   _8_25 = out_10[24]; _8_26 = out_10[25]; _8_27 = out_10[26]; _8_28 = out_10[27]; _8_29 = out_10[28];
  //   _8_30 = out_10[29]; _8_31 = out_10[30]; _8_32 = out_10[31]; _11_1 = out_11[0]; _11_2 = out_11[1];
  //   _11_3 = out_11[2]; _11_4 = out_11[3]; _11_5 = out_11[4]; _11_6 = out_11[5]; _11_7 = out_11[6];
  //   _11_8 = out_11[7]; _11_9 = out_11[8]; _11_10 = out_11[9]; _11_11 = out_11[10]; _11_12 = out_11[11];
  //   _11_13 = out_11[12]; _11_14 = out_11[13]; _11_15 = out_11[14]; _11_16 = out_11[15]; _11_17 = out_11[16];
  //   _11_18 = out_11[17]; _11_19 = out_11[18]; _11_20 = out_11[19]; _11_21 = out_11[20]; _11_22 = out_11[21];
  //   _11_23 = out_11[22]; _11_24 = out_11[23]; _11_25 = out_11[24]; _11_26 = out_11[25]; _11_27 = out_11[26];
  //   _11_28 = out_11[27]; _11_29 = out_11[28]; _11_30 = out_11[29]; _11_31 = out_11[30]; _11_32 = out_11[31];
  //   _14_1 = out_12[0]; _14_2 = out_12[1]; _14_3 = out_12[2]; _14_4 = out_12[3]; _14_5 = out_12[4];
  //   _14_6 = out_12[5]; _14_7 = out_12[6]; _14_8 = out_12[7]; _14_9 = out_12[8]; _14_10 = out_12[9];
  //   _14_11 = out_12[10]; _14_12 = out_12[11]; _14_13 = out_12[12]; _14_14 = out_12[13]; _14_15 = out_12[14];
  //   _14_16 = out_12[15]; _14_17 = out_12[16]; _14_18 = out_12[17]; _14_19 = out_12[18]; _14_20 = out_12[19];
  //   _14_21 = out_12[20]; _14_22 = out_12[21]; _14_23 = out_12[22]; _14_24 = out_12[23]; _14_25 = out_12[24];
  //   _14_26 = out_12[25]; _14_27 = out_12[26]; _14_28 = out_12[27]; _14_29 = out_12[28]; _14_30 = out_12[29];
  //   _14_31 = out_12[30]; _14_32 = out_12[31]; _2_1 = out_13[0]; _2_2 = out_13[1]; _2_3 = out_13[2];
  //   _2_4 = out_13[3]; _2_5 = out_13[4]; _2_6 = out_13[5]; _2_7 = out_13[6]; _2_8 = out_13[7]; _2_9 = out_13[8];
  //   _2_10 = out_13[9]; _2_11 = out_13[10]; _1_12 = out_9[11]; _2_13 = out_13[12]; _2_14 = out_13[13];
  //   _2_15 = out_13[14]; _2_16 = out_13[15]; _2_17 = out_13[16]; _2_18 = out_13[17]; _2_19 = out_13[18];
  //   _2_20 = out_13[19]; _2_21 = out_13[20]; _2_22 = out_13[21]; _2_23 = out_13[22]; _2_24 = out_13[23];
  //   _2_25 = out_13[24]; _2_26 = out_13[25]; _2_27 = out_13[26]; _2_28 = out_13[27]; _2_29 = out_13[28];
  //   _2_30 = out_13[29]; _2_31 = out_13[30]; _2_32 = out_13[31]; _12_1 = out_14[0]; _12_2 = out_14[1];
  //   _12_3 = out_14[2]; _12_4 = out_14[3]; _12_5 = out_14[4]; _12_6 = out_14[5]; _12_7 = out_14[6];
  //   _12_8 = out_14[7]; _12_9 = out_14[8]; _12_10 = out_14[9]; _12_11 = out_14[10]; _12_12 = out_14[11];
  //   _12_13 = out_14[12]; _12_14 = out_14[13]; _12_15 = out_14[14]; _12_16 = out_14[15]; _12_17 = out_14[16];
  //   _12_18 = out_14[17]; _12_19 = out_14[18]; _12_20 = out_14[19]; _12_21 = out_14[20]; _12_22 = out_14[21];
  //   _12_23 = out_14[22]; _12_24 = out_14[23]; _12_25 = out_14[24]; _12_26 = out_14[25]; _12_27 = out_14[26];
  //   _12_28 = out_14[27]; _12_29 = out_14[28]; _12_30 = out_14[29]; _12_31 = out_14[30]; _12_32 = out_14[31];
  //   _5_1 = out_15[0]; _5_2 = out_15[1]; _5_3 = out_15[2]; _5_4 = out_15[3]; _5_5 = out_15[4]; _5_6 = out_15[5];
  //   _5_7 = out_15[6]; _5_8 = out_15[7]; _5_9 = out_15[8]; _5_10 = out_15[9]; _5_11 = out_15[10]; _5_12 = out_15[11];
  //   _5_13 = out_15[12]; _5_14 = out_15[13]; _5_15 = out_15[14]; _5_16 = out_15[15]; _5_17 = out_15[16];
  //   _5_18 = out_15[17]; _5_19 = out_15[18]; _5_20 = out_15[19]; _5_21 = out_15[20]; _5_22 = out_15[21];
  //   _5_23 = out_15[22]; _5_24 = out_15[23]; _5_25 = out_15[24]; _5_26 = out_15[25]; _5_27 = out_15[26];
  //   _5_28 = out_15[27]; _5_29 = out_15[28]; _5_30 = out_15[29]; _5_31 = out_15[30]; _5_32 = out_15[31];
  //   _9_1 = out_16[0]; _9_2 = out_16[1]; _9_3 = out_16[2]; _9_4 = out_16[3]; _9_5 = out_16[4]; _9_6 = out_16[5];
  //   _9_7 = out_16[6]; _9_8 = out_16[7]; _9_9 = out_16[8]; _9_10 = out_16[9]; _9_11 = out_16[10]; _9_12 = out_16[11];
  //   _9_13 = out_16[12]; _9_14 = out_16[13]; _9_15 = out_16[14]; _9_16 = out_16[15]; _9_17 = out_16[16];
  //   _9_18 = out_16[17]; _9_19 = out_16[18]; _9_20 = out_16[19]; _9_21 = out_16[20]; _9_22 = out_16[21];
  //   _9_23 = out_16[22]; _9_24 = out_16[23]; _9_25 = out_16[24]; _9_26 = out_16[25]; _9_27 = out_16[26];
  //   _9_28 = out_16[27]; _9_29 = out_16[28]; _9_30 = out_16[29]; _9_31 = out_16[30]; _9_32 = out_16[31];
  //   _7_1 = out_17[0]; _7_2 = out_17[1]; _7_3 = out_17[2]; _7_4 = out_17[3]; _7_5 = out_17[4]; _7_6 = out_17[5];
  //   _7_7 = out_17[6]; _7_8 = out_17[7]; _7_9 = out_17[8]; _7_10 = out_17[9]; _7_11 = out_17[10]; _7_12 = out_17[11];
  //   _7_13 = out_17[12]; _7_14 = out_17[13]; _7_15 = out_17[14]; _7_16 = out_17[15]; _7_17 = out_17[16];
  //   _7_18 = out_17[17]; _7_19 = out_17[18]; _7_20 = out_17[19]; _7_21 = out_17[20]; _7_22 = out_17[21];
  //   _7_23 = out_17[22]; _7_24 = out_17[23]; _7_25 = out_17[24]; _7_26 = out_17[25]; _7_27 = out_17[26];
  //   _7_28 = out_17[27]; _7_29 = out_17[28]; _7_30 = out_17[29]; _7_31 = out_17[30]; _7_32 = out_17[31];
  //   _6_1 = out_18[0]; _6_2 = out_18[1]; _6_3 = out_18[2]; _6_4 = out_18[3]; _6_5 = out_18[4]; _6_6 = out_18[5];
  //   _6_7 = out_18[6]; _6_8 = out_18[7]; _6_9 = out_18[8]; _6_10 = out_18[9]; _6_11 = out_18[10]; _6_12 = out_18[11];
  //   _6_13 = out_18[12]; _6_14 = out_18[13]; _6_15 = out_18[14]; _6_16 = out_18[15]; _6_17 = out_18[16];
  //   _6_18 = out_18[17]; _6_19 = out_18[18]; _6_20 = out_18[19]; _6_21 = out_18[20]; _6_22 = out_18[21];
  //   _6_23 = out_18[22]; _6_24 = out_18[23]; _6_25 = out_18[24]; _6_26 = out_18[25]; _6_27 = out_18[26];
  //   _6_28 = out_18[27]; _6_29 = out_18[28]; _6_30 = out_18[29]; _6_31 = out_18[30]; _6_32 = out_18[31]
endmodule

module pixel (
  input  R,
  input  arriba,
  input  izq,
  input  der,
  input  Rt,
  input  [1:0] Dir,
  input  _1,
  input  en,
  output salida
);

  wire multiplexer_1_out;

  Multiplexer #(.select(2)) multiplexer_1 (
    .in0(arriba), .in2(izq), .in3(der), .out(multiplexer_1_out), .sel(Dir));  // open: in1, en
  D_Flip_Flop d_ff_1 (.clk(R), .D(multiplexer_1_out), .Q(salida), .preset(_1), .en(en), .reset(Rt));  // open: Qn
endmodule

module teclado (
  input  e6,
  input  e5,
  input  e4,
  input  e3,
  input  e2,
  input  e1,
  input  e0,
  output s1,
  output s0
);

  wire and_1_out, and_2_out, and_3_out, and_4_out, and_5_out, and_6_out, and_7_out, and_8_out, and_9_out,
       and_10_out, and_11_out, and_12_out, not_1_out, not_2_out, not_3_out, not_4_out, not_5_out, not_6_out,
       not_7_out, not_8_out, not_9_out, not_10_out, not_11_out, not_12_out;

  not not_1 (not_1_out, e1);
  not not_2 (not_2_out, e1);
  not not_3 (not_3_out, e1);
  not not_4 (not_4_out, e1);
  not not_5 (not_5_out, e1);
  not not_6 (not_6_out, e1);
  not not_7 (not_7_out, e2);
  not not_8 (not_8_out, e0);
  not not_9 (not_9_out, e0);
  not not_10 (not_10_out, e0);
  not not_11 (not_11_out, e0);
  not not_12 (not_12_out, e0);
  and and_1 (and_1_out, not_1_out, e0);
  and and_2 (and_2_out, e2, not_2_out);
  and and_3 (and_3_out, e3, not_3_out);
  and and_4 (and_4_out, e4, not_4_out);
  and and_5 (and_5_out, e5, not_5_out);
  and and_6 (and_6_out, e6, not_6_out);
  and and_7 (and_7_out, not_7_out, e1);
  and and_8 (and_8_out, e2, not_8_out);
  and and_9 (and_9_out, e3, not_9_out);
  and and_10 (and_10_out, e4, not_10_out);
  and and_11 (and_11_out, e5, not_11_out);
  and and_12 (and_12_out, e6, not_12_out);
  or or_1 (s1, and_1_out, and_2_out, and_3_out, and_4_out, and_5_out, and_6_out);
  or or_2 (s0, and_7_out, and_8_out, and_9_out, and_10_out, and_11_out, and_12_out);
endmodule

module counter (
);

  wire clock_1_out, comparator_1_gt;
  wire [7:0] counter_1_q, divider_1_out, divider_1_rem;

  Clock clock_1 (.out(clock_1_out));
  Counter counter_1 (.Q(counter_1_q), .clk(clock_1_out), .clr(comparator_1_gt));  // open: load, D, count, carry
  Divider divider_1 (.a(counter_1_q), .b(8'ha), .out(divider_1_out), .rem(divider_1_rem));  // open: upper
  Comparator comparator_1 (.a(counter_1_q), .b(8'h63), .gt(comparator_1_gt));  // open: eq, lt
  Hex_Digit_Display hex_digit_display_1 (.value(divider_1_out[3:0]));  // open: dp
  Hex_Digit_Display hex_digit_display_2 (.value(divider_1_rem[3:0]));  // open: dp
endmodule
module player (
  input  Reloj,
  input  en,
  input  Teclado,
  input  [1:0] in_4,
  input  in_5,
  output [31:0] one,
  output [31:0] two,
  output [31:0] three,
  output [31:0] four,
  output [31:0] five,
  output [31:0] six,
  output [31:0] seven,
  output [31:0] eight,
  output [31:0] nine,
  output [31:0] ten,
  output [31:0] eleven,
  output [31:0] twelve,
  output [31:0] thirteen,
  output [31:0] fourteen,
  output [31:0] fifteen,
  output [31:0] sixteen
);

  wire undriven, undriven_2, undriven_3, undriven_4, undriven_5, undriven_6, undriven_7, undriven_8,
       undriven_9, undriven_10, undriven_11, undriven_12, undriven_13, undriven_14, undriven_15, undriven_16,
       undriven_17, undriven_18, undriven_19, undriven_20, undriven_21, undriven_22, undriven_23,
       undriven_24, undriven_25, undriven_26, undriven_27, undriven_28;

  pixel pixel_1 (
    .izq(sixteen[0]), .der(two[0]), .Dir(in_4), .salida(one[0]), .R(Reloj), .arriba(one[31]), ._1(in_5),
    .en(en), .Rt(Teclado));
  pixel pixel_2 (
    .izq(sixteen[1]), .der(two[1]), .Dir(in_4), .salida(one[1]), .R(Reloj), .arriba(one[0]), ._1(in_5),
    .en(en), .Rt(Teclado));
  pixel pixel_3 (
    .izq(sixteen[2]), .der(two[2]), .Dir(in_4), .salida(one[2]), .R(Reloj), .arriba(one[1]), .en(en),
    .Rt(Teclado));  // open: _1
  pixel pixel_4 (
    .izq(sixteen[3]), .der(two[3]), .Dir(in_4), .salida(one[3]), .R(Reloj), .arriba(one[2]), .en(en),
    .Rt(Teclado));  // open: _1
  pixel pixel_5 (
    .izq(sixteen[4]), .der(two[4]), .Dir(in_4), .salida(one[4]), .R(Reloj), .arriba(one[3]), .en(en),
    .Rt(Teclado));  // open: _1
  pixel pixel_6 (
    .izq(sixteen[5]), .der(two[5]), .Dir(in_4), .salida(one[5]), .R(Reloj), .arriba(one[4]), .en(en),
    .Rt(Teclado));  // open: _1
  pixel pixel_7 (
    .izq(sixteen[6]), .der(two[6]), .Dir(in_4), .salida(one[6]), .R(Reloj), .arriba(one[5]), .en(en),
    .Rt(Teclado));  // open: _1
  pixel pixel_8 (
    .izq(sixteen[7]), .der(two[7]), .Dir(in_4), .salida(one[7]), .R(Reloj), .arriba(one[6]), .en(en),
    .Rt(Teclado));  // open: _1
  pixel pixel_9 (
    .izq(sixteen[8]), .der(two[8]), .Dir(in_4), .salida(one[8]), .R(Reloj), .arriba(one[7]), .en(en),
    .Rt(Teclado));  // open: _1
  pixel pixel_10 (
    .izq(sixteen[9]), .der(two[9]), .Dir(in_4), .salida(one[9]), .R(Reloj), .arriba(one[8]), .en(en),
    .Rt(Teclado));  // open: _1
  pixel pixel_11 (
    .izq(sixteen[10]), .der(two[10]), .Dir(in_4), .salida(one[10]), .R(Reloj), .arriba(one[9]), .en(en),
    .Rt(Teclado));  // open: _1
  pixel pixel_12 (
    .izq(sixteen[11]), .der(two[11]), .Dir(in_4), .salida(one[11]), .R(Reloj), .arriba(one[10]), .en(en),
    .Rt(Teclado));  // open: _1
  pixel pixel_13 (
    .izq(sixteen[12]), .der(two[12]), .Dir(in_4), .salida(one[12]), .R(Reloj), .arriba(one[11]), .en(en),
    .Rt(Teclado));  // open: _1
  pixel pixel_14 (
    .izq(sixteen[13]), .der(two[13]), .Dir(in_4), .salida(one[13]), .R(Reloj), .arriba(one[12]), .en(en),
    .Rt(Teclado));  // open: _1
  pixel pixel_15 (
    .izq(sixteen[14]), .der(two[14]), .Dir(in_4), .salida(one[14]), .R(Reloj), .arriba(one[13]), .en(en),
    .Rt(Teclado));  // open: _1
  pixel pixel_16 (
    .izq(sixteen[15]), .der(two[15]), .Dir(in_4), .salida(one[15]), .R(Reloj), .arriba(one[14]), .en(en),
    .Rt(Teclado));  // open: _1
  pixel pixel_17 (
    .izq(sixteen[16]), .der(two[16]), .Dir(in_4), .salida(one[16]), .R(Reloj), .arriba(one[15]), .en(en),
    .Rt(Teclado));  // open: _1
  pixel pixel_18 (
    .izq(sixteen[17]), .der(two[17]), .Dir(in_4), .salida(one[17]), .R(Reloj), .arriba(one[16]), .en(en),
    .Rt(Teclado));  // open: _1
  pixel pixel_19 (
    .izq(sixteen[18]), .der(two[18]), .Dir(in_4), .salida(one[18]), .R(Reloj), .arriba(one[17]), .en(en),
    .Rt(Teclado));  // open: _1
  pixel pixel_20 (
    .izq(sixteen[19]), .der(two[19]), .Dir(in_4), .salida(one[19]), .R(Reloj), .arriba(one[18]), .en(en),
    .Rt(Teclado));  // open: _1
  pixel pixel_21 (
    .izq(sixteen[20]), .der(two[20]), .Dir(in_4), .salida(one[20]), .R(Reloj), .arriba(one[19]), .en(en),
    .Rt(Teclado));  // open: _1
  pixel pixel_22 (
    .izq(sixteen[21]), .der(two[21]), .Dir(in_4), .salida(one[21]), .R(Reloj), .arriba(one[20]), .en(en),
    .Rt(Teclado));  // open: _1
  pixel pixel_23 (
    .izq(sixteen[22]), .der(two[22]), .Dir(in_4), .salida(one[22]), .R(Reloj), .arriba(one[21]), .en(en),
    .Rt(Teclado));  // open: _1
  pixel pixel_24 (
    .izq(sixteen[23]), .der(two[23]), .Dir(in_4), .salida(one[23]), .R(Reloj), .arriba(one[22]), .en(en),
    .Rt(Teclado));  // open: _1
  pixel pixel_25 (
    .izq(sixteen[24]), .der(two[24]), .Dir(in_4), .salida(one[24]), .R(Reloj), .arriba(one[23]), .en(en),
    .Rt(Teclado));  // open: _1
  pixel pixel_26 (
    .izq(sixteen[25]), .der(two[25]), .Dir(in_4), .salida(one[25]), .R(Reloj), .arriba(one[24]), .en(en),
    .Rt(Teclado));  // open: _1
  pixel pixel_27 (
    .izq(sixteen[26]), .der(two[26]), .Dir(in_4), .salida(one[26]), .R(Reloj), .arriba(one[25]), .en(en),
    .Rt(Teclado));  // open: _1
  pixel pixel_28 (
    .izq(sixteen[27]), .der(two[27]), .Dir(in_4), .salida(one[27]), .R(Reloj), .arriba(one[26]), .en(en),
    .Rt(Teclado));  // open: _1
  pixel pixel_29 (
    .izq(sixteen[28]), .der(two[28]), .Dir(in_4), .salida(one[28]), .R(Reloj), .arriba(one[27]), .en(en),
    .Rt(Teclado));  // open: _1
  pixel pixel_30 (
    .izq(sixteen[29]), .der(two[29]), .Dir(in_4), .salida(one[29]), .R(Reloj), .arriba(one[28]), .en(en),
    .Rt(Teclado));  // open: _1
  pixel pixel_31 (
    .izq(sixteen[30]), .der(two[30]), .Dir(in_4), .salida(one[30]), .R(Reloj), .arriba(one[29]), .en(en),
    .Rt(Teclado));  // open: _1
  pixel pixel_32 (
    .izq(sixteen[31]), .der(two[31]), .Dir(in_4), .salida(one[31]), .R(Reloj), .arriba(one[30]), .en(en),
    .Rt(Teclado));  // open: _1
  pixel pixel_33 (
    .izq(one[0]), .der(three[0]), .Dir(in_4), .salida(two[0]), .R(Reloj), .arriba(two[31]), ._1(in_5),
    .en(en), .Rt(Teclado));
  pixel pixel_34 (
    .izq(one[1]), .der(three[1]), .Dir(in_4), .salida(two[1]), .R(Reloj), .arriba(two[0]), ._1(in_5),
    .en(en), .Rt(Teclado));
  pixel pixel_35 (
    .izq(one[2]), .der(three[2]), .Dir(in_4), .salida(two[2]), .R(Reloj), .arriba(two[1]), .en(en),
    .Rt(Teclado));  // open: _1
  pixel pixel_36 (
    .izq(one[3]), .der(three[3]), .Dir(in_4), .salida(two[3]), .R(Reloj), .arriba(two[2]), .en(en),
    .Rt(Teclado));  // open: _1
  pixel pixel_37 (
    .izq(one[4]), .der(three[4]), .Dir(in_4), .salida(two[4]), .R(Reloj), .arriba(two[3]), .en(en),
    .Rt(Teclado));  // open: _1
  pixel pixel_38 (
    .izq(one[5]), .der(three[5]), .Dir(in_4), .salida(two[5]), .R(Reloj), .arriba(two[4]), .en(en),
    .Rt(Teclado));  // open: _1
  pixel pixel_39 (
    .izq(one[6]), .der(three[6]), .Dir(in_4), .salida(two[6]), .R(Reloj), .arriba(two[5]), .en(en),
    .Rt(Teclado));  // open: _1
  pixel pixel_40 (
    .izq(one[7]), .der(three[7]), .Dir(in_4), .salida(two[7]), .R(Reloj), .arriba(two[6]), .en(en),
    .Rt(Teclado));  // open: _1
  pixel pixel_41 (
    .izq(one[8]), .der(three[8]), .Dir(in_4), .salida(two[8]), .R(Reloj), .arriba(two[7]), .en(en),
    .Rt(Teclado));  // open: _1
  pixel pixel_42 (
    .izq(one[9]), .der(three[9]), .Dir(in_4), .salida(two[9]), .R(Reloj), .arriba(two[8]), .en(en),
    .Rt(Teclado));  // open: _1
  pixel pixel_43 (
    .izq(one[10]), .der(three[10]), .Dir(in_4), .salida(two[10]), .R(Reloj), .arriba(two[9]), .en(en),
    .Rt(Teclado));  // open: _1
  pixel pixel_44 (
    .izq(one[11]), .der(three[11]), .Dir(in_4), .salida(two[11]), .R(Reloj), .arriba(two[10]), .en(en),
    .Rt(Teclado));  // open: _1
  pixel pixel_45 (
    .izq(one[12]), .der(three[12]), .Dir(in_4), .salida(two[12]), .R(Reloj), .arriba(two[11]), .en(en),
    .Rt(Teclado));  // open: _1
  pixel pixel_46 (
    .izq(one[13]), .der(three[13]), .Dir(in_4), .salida(two[13]), .R(Reloj), .arriba(two[12]), .en(en),
    .Rt(Teclado));  // open: _1
  pixel pixel_47 (
    .izq(one[14]), .der(three[14]), .Dir(in_4), .salida(two[14]), .R(Reloj), .arriba(two[13]), .en(en),
    .Rt(Teclado));  // open: _1
  pixel pixel_48 (
    .izq(one[15]), .der(three[15]), .Dir(in_4), .salida(two[15]), .R(Reloj), .arriba(two[14]), .en(en),
    .Rt(Teclado));  // open: _1
  pixel pixel_49 (
    .izq(one[16]), .der(three[16]), .Dir(in_4), .salida(two[16]), .R(Reloj), .arriba(two[15]), .en(en),
    .Rt(Teclado));  // open: _1
  pixel pixel_50 (
    .izq(one[17]), .der(three[17]), .Dir(in_4), .salida(two[17]), .R(Reloj), .arriba(two[16]), .en(en),
    .Rt(Teclado));  // open: _1
  pixel pixel_51 (
    .izq(one[18]), .der(three[18]), .Dir(in_4), .salida(two[18]), .R(Reloj), .arriba(two[17]), .en(en),
    .Rt(Teclado));  // open: _1
  pixel pixel_52 (
    .izq(one[19]), .der(three[19]), .Dir(in_4), .salida(two[19]), .R(Reloj), .arriba(two[18]), .en(en),
    .Rt(Teclado));  // open: _1
  pixel pixel_53 (
    .izq(one[20]), .der(three[20]), .Dir(in_4), .salida(two[20]), .R(Reloj), .arriba(two[19]), .en(en),
    .Rt(Teclado));  // open: _1
  pixel pixel_54 (
    .izq(one[21]), .der(three[21]), .Dir(in_4), .salida(two[21]), .R(Reloj), .arriba(two[20]), .en(en),
    .Rt(Teclado));  // open: _1
  pixel pixel_55 (
    .izq(one[22]), .der(three[22]), .Dir(in_4), .salida(two[22]), .R(Reloj), .arriba(two[21]), .en(en),
    .Rt(Teclado));  // open: _1
  pixel pixel_56 (
    .izq(one[23]), .der(three[23]), .Dir(in_4), .salida(two[23]), .R(Reloj), .arriba(two[22]), .en(en),
    .Rt(Teclado));  // open: _1
  pixel pixel_57 (
    .izq(one[24]), .der(three[24]), .Dir(in_4), .salida(two[24]), .R(Reloj), .arriba(two[23]), .en(en),
    .Rt(Teclado));  // open: _1
  pixel pixel_58 (
    .izq(one[25]), .der(three[25]), .Dir(in_4), .salida(two[25]), .R(Reloj), .arriba(two[24]), .en(en),
    .Rt(Teclado));  // open: _1
  pixel pixel_59 (
    .izq(one[26]), .der(three[26]), .Dir(in_4), .salida(two[26]), .R(Reloj), .arriba(two[25]), .en(en),
    .Rt(Teclado));  // open: _1
  pixel pixel_60 (
    .izq(one[27]), .der(three[27]), .Dir(in_4), .salida(two[27]), .R(Reloj), .arriba(two[26]), .en(en),
    .Rt(Teclado));  // open: _1
  pixel pixel_61 (
    .izq(one[28]), .der(three[28]), .Dir(in_4), .salida(two[28]), .R(Reloj), .arriba(two[27]), .en(en),
    .Rt(Teclado));  // open: _1
  pixel pixel_62 (
    .izq(one[29]), .der(three[29]), .Dir(in_4), .salida(two[29]), .R(Reloj), .arriba(two[28]), .en(en),
    .Rt(Teclado));  // open: _1
  pixel pixel_63 (
    .izq(one[30]), .der(three[30]), .Dir(in_4), .salida(two[30]), .R(Reloj), .arriba(two[29]), .en(en),
    .Rt(Teclado));  // open: _1
  pixel pixel_64 (
    .izq(one[31]), .der(three[31]), .Dir(in_4), .salida(two[31]), .R(Reloj), .arriba(two[30]), .en(en),
    .Rt(Teclado));  // open: _1
  pixel pixel_65 (
    .izq(two[0]), .der(four[0]), .Dir(in_4), .salida(three[0]), .R(Reloj), .arriba(three[31]), ._1(undriven),
    .en(en), .Rt(Teclado));
  pixel pixel_66 (
    .izq(two[1]), .der(four[1]), .Dir(in_4), .salida(three[1]), .R(Reloj), .arriba(three[0]),
    ._1(undriven_2), .en(en), .Rt(Teclado));
  pixel pixel_67 (
    .izq(two[2]), .der(four[2]), .Dir(in_4), .salida(three[2]), .R(Reloj), .arriba(three[1]), .en(en),
    .Rt(Teclado));  // open: _1
  pixel pixel_68 (
    .izq(two[3]), .der(four[3]), .Dir(in_4), .salida(three[3]), .R(Reloj), .arriba(three[2]), .en(en),
    .Rt(Teclado));  // open: _1
  pixel pixel_69 (
    .izq(two[4]), .der(four[4]), .Dir(in_4), .salida(three[4]), .R(Reloj), .arriba(three[3]), .en(en),
    .Rt(Teclado));  // open: _1
  pixel pixel_70 (
    .izq(two[5]), .der(four[5]), .Dir(in_4), .salida(three[5]), .R(Reloj), .arriba(three[4]), .en(en),
    .Rt(Teclado));  // open: _1
  pixel pixel_71 (
    .izq(two[6]), .der(four[6]), .Dir(in_4), .salida(three[6]), .R(Reloj), .arriba(three[5]), .en(en),
    .Rt(Teclado));  // open: _1
  pixel pixel_72 (
    .izq(two[7]), .der(four[7]), .Dir(in_4), .salida(three[7]), .R(Reloj), .arriba(three[6]), .en(en),
    .Rt(Teclado));  // open: _1
  pixel pixel_73 (
    .izq(two[8]), .der(four[8]), .Dir(in_4), .salida(three[8]), .R(Reloj), .arriba(three[7]), .en(en),
    .Rt(Teclado));  // open: _1
  pixel pixel_74 (
    .izq(two[9]), .der(four[9]), .Dir(in_4), .salida(three[9]), .R(Reloj), .arriba(three[8]), .en(en),
    .Rt(Teclado));  // open: _1
  pixel pixel_75 (
    .izq(two[10]), .der(four[10]), .Dir(in_4), .salida(three[10]), .R(Reloj), .arriba(three[9]), .en(en),
    .Rt(Teclado));  // open: _1
  pixel pixel_76 (
    .izq(two[11]), .der(four[11]), .Dir(in_4), .salida(three[11]), .R(Reloj), .arriba(three[10]), .en(en),
    .Rt(Teclado));  // open: _1
  pixel pixel_77 (
    .izq(two[12]), .der(four[12]), .Dir(in_4), .salida(three[12]), .R(Reloj), .arriba(three[11]), .en(en),
    .Rt(Teclado));  // open: _1
  pixel pixel_78 (
    .izq(two[13]), .der(four[13]), .Dir(in_4), .salida(three[13]), .R(Reloj), .arriba(three[12]), .en(en),
    .Rt(Teclado));  // open: _1
  pixel pixel_79 (
    .izq(two[14]), .der(four[14]), .Dir(in_4), .salida(three[14]), .R(Reloj), .arriba(three[13]), .en(en),
    .Rt(Teclado));  // open: _1
  pixel pixel_80 (
    .izq(two[15]), .der(four[15]), .Dir(in_4), .salida(three[15]), .R(Reloj), .arriba(three[14]), .en(en),
    .Rt(Teclado));  // open: _1
  pixel pixel_81 (
    .izq(two[16]), .der(four[16]), .Dir(in_4), .salida(three[16]), .R(Reloj), .arriba(three[15]), .en(en),
    .Rt(Teclado));  // open: _1
  pixel pixel_82 (
    .izq(two[17]), .der(four[17]), .Dir(in_4), .salida(three[17]), .R(Reloj), .arriba(three[16]), .en(en),
    .Rt(Teclado));  // open: _1
  pixel pixel_83 (
    .izq(two[18]), .der(four[18]), .Dir(in_4), .salida(three[18]), .R(Reloj), .arriba(three[17]), .en(en),
    .Rt(Teclado));  // open: _1
  pixel pixel_84 (
    .izq(two[19]), .der(four[19]), .Dir(in_4), .salida(three[19]), .R(Reloj), .arriba(three[18]), .en(en),
    .Rt(Teclado));  // open: _1
  pixel pixel_85 (
    .izq(two[20]), .der(four[20]), .Dir(in_4), .salida(three[20]), .R(Reloj), .arriba(three[19]), .en(en),
    .Rt(Teclado));  // open: _1
  pixel pixel_86 (
    .izq(two[21]), .der(four[21]), .Dir(in_4), .salida(three[21]), .R(Reloj), .arriba(three[20]), .en(en),
    .Rt(Teclado));  // open: _1
  pixel pixel_87 (
    .izq(two[22]), .der(four[22]), .Dir(in_4), .salida(three[22]), .R(Reloj), .arriba(three[21]), .en(en),
    .Rt(Teclado));  // open: _1
  pixel pixel_88 (
    .izq(two[23]), .der(four[23]), .Dir(in_4), .salida(three[23]), .R(Reloj), .arriba(three[22]), .en(en),
    .Rt(Teclado));  // open: _1
  pixel pixel_89 (
    .izq(two[24]), .der(four[24]), .Dir(in_4), .salida(three[24]), .R(Reloj), .arriba(three[23]), .en(en),
    .Rt(Teclado));  // open: _1
  pixel pixel_90 (
    .izq(two[25]), .der(four[25]), .Dir(in_4), .salida(three[25]), .R(Reloj), .arriba(three[24]), .en(en),
    .Rt(Teclado));  // open: _1
  pixel pixel_91 (
    .izq(two[26]), .der(four[26]), .Dir(in_4), .salida(three[26]), .R(Reloj), .arriba(three[25]), .en(en),
    .Rt(Teclado));  // open: _1
  pixel pixel_92 (
    .izq(two[27]), .der(four[27]), .Dir(in_4), .salida(three[27]), .R(Reloj), .arriba(three[26]), .en(en),
    .Rt(Teclado));  // open: _1
  pixel pixel_93 (
    .izq(two[28]), .der(four[28]), .Dir(in_4), .salida(three[28]), .R(Reloj), .arriba(three[27]), .en(en),
    .Rt(Teclado));  // open: _1
  pixel pixel_94 (
    .izq(two[29]), .der(four[29]), .Dir(in_4), .salida(three[29]), .R(Reloj), .arriba(three[28]), .en(en),
    .Rt(Teclado));  // open: _1
  pixel pixel_95 (
    .izq(two[30]), .der(four[30]), .Dir(in_4), .salida(three[30]), .R(Reloj), .arriba(three[29]), .en(en),
    .Rt(Teclado));  // open: _1
  pixel pixel_96 (
    .izq(two[31]), .der(four[31]), .Dir(in_4), .salida(three[31]), .R(Reloj), .arriba(three[30]), .en(en),
    .Rt(Teclado));  // open: _1
  pixel pixel_97 (
    .izq(three[0]), .der(five[0]), .Dir(in_4), .salida(four[0]), .R(Reloj), .arriba(four[31]),
    ._1(undriven_3), .en(en), .Rt(Teclado));
  pixel pixel_98 (
    .izq(three[1]), .der(five[1]), .Dir(in_4), .salida(four[1]), .R(Reloj), .arriba(four[0]),
    ._1(undriven_4), .en(en), .Rt(Teclado));
  pixel pixel_99 (
    .izq(three[2]), .der(five[2]), .Dir(in_4), .salida(four[2]), .R(Reloj), .arriba(four[1]), .en(en),
    .Rt(Teclado));  // open: _1
  pixel pixel_100 (
    .izq(three[3]), .der(five[3]), .Dir(in_4), .salida(four[3]), .R(Reloj), .arriba(four[2]), .en(en),
    .Rt(Teclado));  // open: _1
  pixel pixel_101 (
    .izq(three[4]), .der(five[4]), .Dir(in_4), .salida(four[4]), .R(Reloj), .arriba(four[3]), .en(en),
    .Rt(Teclado));  // open: _1
  pixel pixel_102 (
    .izq(three[5]), .der(five[5]), .Dir(in_4), .salida(four[5]), .R(Reloj), .arriba(four[4]), .en(en),
    .Rt(Teclado));  // open: _1
  pixel pixel_103 (
    .izq(three[6]), .der(five[6]), .Dir(in_4), .salida(four[6]), .R(Reloj), .arriba(four[5]), .en(en),
    .Rt(Teclado));  // open: _1
  pixel pixel_104 (
    .izq(three[7]), .der(five[7]), .Dir(in_4), .salida(four[7]), .R(Reloj), .arriba(four[6]), .en(en),
    .Rt(Teclado));  // open: _1
  pixel pixel_105 (
    .izq(three[8]), .der(five[8]), .Dir(in_4), .salida(four[8]), .R(Reloj), .arriba(four[7]), .en(en),
    .Rt(Teclado));  // open: _1
  pixel pixel_106 (
    .izq(three[9]), .der(five[9]), .Dir(in_4), .salida(four[9]), .R(Reloj), .arriba(four[8]), .en(en),
    .Rt(Teclado));  // open: _1
  pixel pixel_107 (
    .izq(three[10]), .der(five[10]), .Dir(in_4), .salida(four[10]), .R(Reloj), .arriba(four[9]), .en(en),
    .Rt(Teclado));  // open: _1
  pixel pixel_108 (
    .izq(three[11]), .der(five[11]), .Dir(in_4), .salida(four[11]), .R(Reloj), .arriba(four[10]), .en(en),
    .Rt(Teclado));  // open: _1
  pixel pixel_109 (
    .izq(three[12]), .der(five[12]), .Dir(in_4), .salida(four[12]), .R(Reloj), .arriba(four[11]), .en(en),
    .Rt(Teclado));  // open: _1
  pixel pixel_110 (
    .izq(three[13]), .der(five[13]), .Dir(in_4), .salida(four[13]), .R(Reloj), .arriba(four[12]), .en(en),
    .Rt(Teclado));  // open: _1
  pixel pixel_111 (
    .izq(three[14]), .der(five[14]), .Dir(in_4), .salida(four[14]), .R(Reloj), .arriba(four[13]), .en(en),
    .Rt(Teclado));  // open: _1
  pixel pixel_112 (
    .izq(three[15]), .der(five[15]), .Dir(in_4), .salida(four[15]), .R(Reloj), .arriba(four[14]), .en(en),
    .Rt(Teclado));  // open: _1
  pixel pixel_113 (
    .izq(three[16]), .der(five[16]), .Dir(in_4), .salida(four[16]), .R(Reloj), .arriba(four[15]), .en(en),
    .Rt(Teclado));  // open: _1
  pixel pixel_114 (
    .izq(three[17]), .der(five[17]), .Dir(in_4), .salida(four[17]), .R(Reloj), .arriba(four[16]), .en(en),
    .Rt(Teclado));  // open: _1
  pixel pixel_115 (
    .izq(three[18]), .der(five[18]), .Dir(in_4), .salida(four[18]), .R(Reloj), .arriba(four[17]), .en(en),
    .Rt(Teclado));  // open: _1
  pixel pixel_116 (
    .izq(three[19]), .der(five[19]), .Dir(in_4), .salida(four[19]), .R(Reloj), .arriba(four[18]), .en(en),
    .Rt(Teclado));  // open: _1
  pixel pixel_117 (
    .izq(three[20]), .der(five[20]), .Dir(in_4), .salida(four[20]), .R(Reloj), .arriba(four[19]), .en(en),
    .Rt(Teclado));  // open: _1
  pixel pixel_118 (
    .izq(three[21]), .der(five[21]), .Dir(in_4), .salida(four[21]), .R(Reloj), .arriba(four[20]), .en(en),
    .Rt(Teclado));  // open: _1
  pixel pixel_119 (
    .izq(three[22]), .der(five[22]), .Dir(in_4), .salida(four[22]), .R(Reloj), .arriba(four[21]), .en(en),
    .Rt(Teclado));  // open: _1
  pixel pixel_120 (
    .izq(three[23]), .der(five[23]), .Dir(in_4), .salida(four[23]), .R(Reloj), .arriba(four[22]), .en(en),
    .Rt(Teclado));  // open: _1
  pixel pixel_121 (
    .izq(three[24]), .der(five[24]), .Dir(in_4), .salida(four[24]), .R(Reloj), .arriba(four[23]), .en(en),
    .Rt(Teclado));  // open: _1
  pixel pixel_122 (
    .izq(three[25]), .der(five[25]), .Dir(in_4), .salida(four[25]), .R(Reloj), .arriba(four[24]), .en(en),
    .Rt(Teclado));  // open: _1
  pixel pixel_123 (
    .izq(three[26]), .der(five[26]), .Dir(in_4), .salida(four[26]), .R(Reloj), .arriba(four[25]), .en(en),
    .Rt(Teclado));  // open: _1
  pixel pixel_124 (
    .izq(three[27]), .der(five[27]), .Dir(in_4), .salida(four[27]), .R(Reloj), .arriba(four[26]), .en(en),
    .Rt(Teclado));  // open: _1
  pixel pixel_125 (
    .izq(three[28]), .der(five[28]), .Dir(in_4), .salida(four[28]), .R(Reloj), .arriba(four[27]), .en(en),
    .Rt(Teclado));  // open: _1
  pixel pixel_126 (
    .izq(three[29]), .der(five[29]), .Dir(in_4), .salida(four[29]), .R(Reloj), .arriba(four[28]), .en(en),
    .Rt(Teclado));  // open: _1
  pixel pixel_127 (
    .izq(three[30]), .der(five[30]), .Dir(in_4), .salida(four[30]), .R(Reloj), .arriba(four[29]), .en(en),
    .Rt(Teclado));  // open: _1
  pixel pixel_128 (
    .izq(three[31]), .der(five[31]), .Dir(in_4), .salida(four[31]), .R(Reloj), .arriba(four[30]), .en(en),
    .Rt(Teclado));  // open: _1
  pixel pixel_129 (
    .izq(four[0]), .der(six[0]), .Dir(in_4), .salida(five[0]), .R(Reloj), .arriba(five[31]), ._1(undriven_5),
    .en(en), .Rt(Teclado));
  pixel pixel_130 (
    .izq(four[1]), .der(six[1]), .Dir(in_4), .salida(five[1]), .R(Reloj), .arriba(five[0]), ._1(undriven_6),
    .en(en), .Rt(Teclado));
  pixel pixel_131 (
    .izq(four[2]), .der(six[2]), .Dir(in_4), .salida(five[2]), .R(Reloj), .arriba(five[1]), .en(en),
    .Rt(Teclado));  // open: _1
  pixel pixel_132 (
    .izq(four[3]), .der(six[3]), .Dir(in_4), .salida(five[3]), .R(Reloj), .arriba(five[2]), .en(en),
    .Rt(Teclado));  // open: _1
  pixel pixel_133 (
    .izq(four[4]), .der(six[4]), .Dir(in_4), .salida(five[4]), .R(Reloj), .arriba(five[3]), .en(en),
    .Rt(Teclado));  // open: _1
  pixel pixel_134 (
    .izq(four[5]), .der(six[5]), .Dir(in_4), .salida(five[5]), .R(Reloj), .arriba(five[4]), .en(en),
    .Rt(Teclado));  // open: _1
  pixel pixel_135 (
    .izq(four[6]), .der(six[6]), .Dir(in_4), .salida(five[6]), .R(Reloj), .arriba(five[5]), .en(en),
    .Rt(Teclado));  // open: _1
  pixel pixel_136 (
    .izq(four[7]), .der(six[7]), .Dir(in_4), .salida(five[7]), .R(Reloj), .arriba(five[6]), .en(en),
    .Rt(Teclado));  // open: _1
  pixel pixel_137 (
    .izq(four[8]), .der(six[8]), .Dir(in_4), .salida(five[8]), .R(Reloj), .arriba(five[7]), .en(en),
    .Rt(Teclado));  // open: _1
  pixel pixel_138 (
    .izq(four[9]), .der(six[9]), .Dir(in_4), .salida(five[9]), .R(Reloj), .arriba(five[8]), .en(en),
    .Rt(Teclado));  // open: _1
  pixel pixel_139 (
    .izq(four[10]), .der(six[10]), .Dir(in_4), .salida(five[10]), .R(Reloj), .arriba(five[9]), .en(en),
    .Rt(Teclado));  // open: _1
  pixel pixel_140 (
    .izq(four[11]), .der(six[11]), .Dir(in_4), .salida(five[11]), .R(Reloj), .arriba(five[10]), .en(en),
    .Rt(Teclado));  // open: _1
  pixel pixel_141 (
    .izq(four[12]), .der(six[12]), .Dir(in_4), .salida(five[12]), .R(Reloj), .arriba(five[11]), .en(en),
    .Rt(Teclado));  // open: _1
  pixel pixel_142 (
    .izq(four[13]), .der(six[13]), .Dir(in_4), .salida(five[13]), .R(Reloj), .arriba(five[12]), .en(en),
    .Rt(Teclado));  // open: _1
  pixel pixel_143 (
    .izq(four[14]), .der(six[14]), .Dir(in_4), .salida(five[14]), .R(Reloj), .arriba(five[13]), .en(en),
    .Rt(Teclado));  // open: _1
  pixel pixel_144 (
    .izq(four[15]), .der(six[15]), .Dir(in_4), .salida(five[15]), .R(Reloj), .arriba(five[14]), .en(en),
    .Rt(Teclado));  // open: _1
  pixel pixel_145 (
    .izq(four[16]), .der(six[16]), .Dir(in_4), .salida(five[16]), .R(Reloj), .arriba(five[15]), .en(en),
    .Rt(Teclado));  // open: _1
  pixel pixel_146 (
    .izq(four[17]), .der(six[17]), .Dir(in_4), .salida(five[17]), .R(Reloj), .arriba(five[16]), .en(en),
    .Rt(Teclado));  // open: _1
  pixel pixel_147 (
    .izq(four[18]), .der(six[18]), .Dir(in_4), .salida(five[18]), .R(Reloj), .arriba(five[17]), .en(en),
    .Rt(Teclado));  // open: _1
  pixel pixel_148 (
    .izq(four[19]), .der(six[19]), .Dir(in_4), .salida(five[19]), .R(Reloj), .arriba(five[18]), .en(en),
    .Rt(Teclado));  // open: _1
  pixel pixel_149 (
    .izq(four[20]), .der(six[20]), .Dir(in_4), .salida(five[20]), .R(Reloj), .arriba(five[19]), .en(en),
    .Rt(Teclado));  // open: _1
  pixel pixel_150 (
    .izq(four[21]), .der(six[21]), .Dir(in_4), .salida(five[21]), .R(Reloj), .arriba(five[20]), .en(en),
    .Rt(Teclado));  // open: _1
  pixel pixel_151 (
    .izq(four[22]), .der(six[22]), .Dir(in_4), .salida(five[22]), .R(Reloj), .arriba(five[21]), .en(en),
    .Rt(Teclado));  // open: _1
  pixel pixel_152 (
    .izq(four[23]), .der(six[23]), .Dir(in_4), .salida(five[23]), .R(Reloj), .arriba(five[22]), .en(en),
    .Rt(Teclado));  // open: _1
  pixel pixel_153 (
    .izq(four[24]), .der(six[24]), .Dir(in_4), .salida(five[24]), .R(Reloj), .arriba(five[23]), .en(en),
    .Rt(Teclado));  // open: _1
  pixel pixel_154 (
    .izq(four[25]), .der(six[25]), .Dir(in_4), .salida(five[25]), .R(Reloj), .arriba(five[24]), .en(en),
    .Rt(Teclado));  // open: _1
  pixel pixel_155 (
    .izq(four[26]), .der(six[26]), .Dir(in_4), .salida(five[26]), .R(Reloj), .arriba(five[25]), .en(en),
    .Rt(Teclado));  // open: _1
  pixel pixel_156 (
    .izq(four[27]), .der(six[27]), .Dir(in_4), .salida(five[27]), .R(Reloj), .arriba(five[26]), .en(en),
    .Rt(Teclado));  // open: _1
  pixel pixel_157 (
    .izq(four[28]), .der(six[28]), .Dir(in_4), .salida(five[28]), .R(Reloj), .arriba(five[27]), .en(en),
    .Rt(Teclado));  // open: _1
  pixel pixel_158 (
    .izq(four[29]), .der(six[29]), .Dir(in_4), .salida(five[29]), .R(Reloj), .arriba(five[28]), .en(en),
    .Rt(Teclado));  // open: _1
  pixel pixel_159 (
    .izq(four[30]), .der(six[30]), .Dir(in_4), .salida(five[30]), .R(Reloj), .arriba(five[29]), .en(en),
    .Rt(Teclado));  // open: _1
  pixel pixel_160 (
    .izq(four[31]), .der(six[31]), .Dir(in_4), .salida(five[31]), .R(Reloj), .arriba(five[30]), .en(en),
    .Rt(Teclado));  // open: _1
  pixel pixel_161 (
    .izq(five[0]), .der(seven[0]), .Dir(in_4), .salida(six[0]), .R(Reloj), .arriba(six[31]), ._1(undriven_7),
    .en(en), .Rt(Teclado));
  pixel pixel_162 (
    .izq(five[1]), .der(seven[1]), .Dir(in_4), .salida(six[1]), .R(Reloj), .arriba(six[0]), ._1(undriven_8),
    .en(en), .Rt(Teclado));
  pixel pixel_163 (
    .izq(five[2]), .der(seven[2]), .Dir(in_4), .salida(six[2]), .R(Reloj), .arriba(six[1]), .en(en),
    .Rt(Teclado));  // open: _1
  pixel pixel_164 (
    .izq(five[3]), .der(seven[3]), .Dir(in_4), .salida(six[3]), .R(Reloj), .arriba(six[2]), .en(en),
    .Rt(Teclado));  // open: _1
  pixel pixel_165 (
    .izq(five[4]), .der(seven[4]), .Dir(in_4), .salida(six[4]), .R(Reloj), .arriba(six[3]), .en(en),
    .Rt(Teclado));  // open: _1
  pixel pixel_166 (
    .izq(five[5]), .der(seven[5]), .Dir(in_4), .salida(six[5]), .R(Reloj), .arriba(six[4]), .en(en),
    .Rt(Teclado));  // open: _1
  pixel pixel_167 (
    .izq(five[6]), .der(seven[6]), .Dir(in_4), .salida(six[6]), .R(Reloj), .arriba(six[5]), .en(en),
    .Rt(Teclado));  // open: _1
  pixel pixel_168 (
    .izq(five[7]), .der(seven[7]), .Dir(in_4), .salida(six[7]), .R(Reloj), .arriba(six[6]), .en(en),
    .Rt(Teclado));  // open: _1
  pixel pixel_169 (
    .izq(five[8]), .der(seven[8]), .Dir(in_4), .salida(six[8]), .R(Reloj), .arriba(six[7]), .en(en),
    .Rt(Teclado));  // open: _1
  pixel pixel_170 (
    .izq(five[9]), .der(seven[9]), .Dir(in_4), .salida(six[9]), .R(Reloj), .arriba(six[8]), .en(en),
    .Rt(Teclado));  // open: _1
  pixel pixel_171 (
    .izq(five[10]), .der(seven[10]), .Dir(in_4), .salida(six[10]), .R(Reloj), .arriba(six[9]), .en(en),
    .Rt(Teclado));  // open: _1
  pixel pixel_172 (
    .izq(five[11]), .der(seven[11]), .Dir(in_4), .salida(six[11]), .R(Reloj), .arriba(six[10]), .en(en),
    .Rt(Teclado));  // open: _1
  pixel pixel_173 (
    .izq(five[12]), .der(seven[12]), .Dir(in_4), .salida(six[12]), .R(Reloj), .arriba(six[11]), .en(en),
    .Rt(Teclado));  // open: _1
  pixel pixel_174 (
    .izq(five[13]), .der(seven[13]), .Dir(in_4), .salida(six[13]), .R(Reloj), .arriba(six[12]), .en(en),
    .Rt(Teclado));  // open: _1
  pixel pixel_175 (
    .izq(five[14]), .der(seven[14]), .Dir(in_4), .salida(six[14]), .R(Reloj), .arriba(six[13]), .en(en),
    .Rt(Teclado));  // open: _1
  pixel pixel_176 (
    .izq(five[15]), .der(seven[15]), .Dir(in_4), .salida(six[15]), .R(Reloj), .arriba(six[14]), .en(en),
    .Rt(Teclado));  // open: _1
  pixel pixel_177 (
    .izq(five[16]), .der(seven[16]), .Dir(in_4), .salida(six[16]), .R(Reloj), .arriba(six[15]), .en(en),
    .Rt(Teclado));  // open: _1
  pixel pixel_178 (
    .izq(five[17]), .der(seven[17]), .Dir(in_4), .salida(six[17]), .R(Reloj), .arriba(six[16]), .en(en),
    .Rt(Teclado));  // open: _1
  pixel pixel_179 (
    .izq(five[18]), .der(seven[18]), .Dir(in_4), .salida(six[18]), .R(Reloj), .arriba(six[17]), .en(en),
    .Rt(Teclado));  // open: _1
  pixel pixel_180 (
    .izq(five[19]), .der(seven[19]), .Dir(in_4), .salida(six[19]), .R(Reloj), .arriba(six[18]), .en(en),
    .Rt(Teclado));  // open: _1
  pixel pixel_181 (
    .izq(five[20]), .der(seven[20]), .Dir(in_4), .salida(six[20]), .R(Reloj), .arriba(six[19]), .en(en),
    .Rt(Teclado));  // open: _1
  pixel pixel_182 (
    .izq(five[21]), .der(seven[21]), .Dir(in_4), .salida(six[21]), .R(Reloj), .arriba(six[20]), .en(en),
    .Rt(Teclado));  // open: _1
  pixel pixel_183 (
    .izq(five[22]), .der(seven[22]), .Dir(in_4), .salida(six[22]), .R(Reloj), .arriba(six[21]), .en(en),
    .Rt(Teclado));  // open: _1
  pixel pixel_184 (
    .izq(five[23]), .der(seven[23]), .Dir(in_4), .salida(six[23]), .R(Reloj), .arriba(six[22]), .en(en),
    .Rt(Teclado));  // open: _1
  pixel pixel_185 (
    .izq(five[24]), .der(seven[24]), .Dir(in_4), .salida(six[24]), .R(Reloj), .arriba(six[23]), .en(en),
    .Rt(Teclado));  // open: _1
  pixel pixel_186 (
    .izq(five[25]), .der(seven[25]), .Dir(in_4), .salida(six[25]), .R(Reloj), .arriba(six[24]), .en(en),
    .Rt(Teclado));  // open: _1
  pixel pixel_187 (
    .izq(five[26]), .der(seven[26]), .Dir(in_4), .salida(six[26]), .R(Reloj), .arriba(six[25]), .en(en),
    .Rt(Teclado));  // open: _1
  pixel pixel_188 (
    .izq(five[27]), .der(seven[27]), .Dir(in_4), .salida(six[27]), .R(Reloj), .arriba(six[26]), .en(en),
    .Rt(Teclado));  // open: _1
  pixel pixel_189 (
    .izq(five[28]), .der(seven[28]), .Dir(in_4), .salida(six[28]), .R(Reloj), .arriba(six[27]), .en(en),
    .Rt(Teclado));  // open: _1
  pixel pixel_190 (
    .izq(five[29]), .der(seven[29]), .Dir(in_4), .salida(six[29]), .R(Reloj), .arriba(six[28]), .en(en),
    .Rt(Teclado));  // open: _1
  pixel pixel_191 (
    .izq(five[30]), .der(seven[30]), .Dir(in_4), .salida(six[30]), .R(Reloj), .arriba(six[29]), .en(en),
    .Rt(Teclado));  // open: _1
  pixel pixel_192 (
    .izq(five[31]), .der(seven[31]), .Dir(in_4), .salida(six[31]), .R(Reloj), .arriba(six[30]), .en(en),
    .Rt(Teclado));  // open: _1
  pixel pixel_193 (
    .izq(six[0]), .der(eight[0]), .Dir(in_4), .salida(seven[0]), .R(Reloj), .arriba(seven[31]),
    ._1(undriven_9), .en(en), .Rt(Teclado));
  pixel pixel_194 (
    .izq(six[1]), .der(eight[1]), .Dir(in_4), .salida(seven[1]), .R(Reloj), .arriba(seven[0]),
    ._1(undriven_10), .en(en), .Rt(Teclado));
  pixel pixel_195 (
    .izq(six[2]), .der(eight[2]), .Dir(in_4), .salida(seven[2]), .R(Reloj), .arriba(seven[1]), .en(en),
    .Rt(Teclado));  // open: _1
  pixel pixel_196 (
    .izq(six[3]), .der(eight[3]), .Dir(in_4), .salida(seven[3]), .R(Reloj), .arriba(seven[2]), .en(en),
    .Rt(Teclado));  // open: _1
  pixel pixel_197 (
    .izq(six[4]), .der(eight[4]), .Dir(in_4), .salida(seven[4]), .R(Reloj), .arriba(seven[3]), .en(en),
    .Rt(Teclado));  // open: _1
  pixel pixel_198 (
    .izq(six[5]), .der(eight[5]), .Dir(in_4), .salida(seven[5]), .R(Reloj), .arriba(seven[4]), .en(en),
    .Rt(Teclado));  // open: _1
  pixel pixel_199 (
    .izq(six[6]), .der(eight[6]), .Dir(in_4), .salida(seven[6]), .R(Reloj), .arriba(seven[5]), .en(en),
    .Rt(Teclado));  // open: _1
  pixel pixel_200 (
    .izq(six[7]), .der(eight[7]), .Dir(in_4), .salida(seven[7]), .R(Reloj), .arriba(seven[6]), .en(en),
    .Rt(Teclado));  // open: _1
  pixel pixel_201 (
    .izq(six[8]), .der(eight[8]), .Dir(in_4), .salida(seven[8]), .R(Reloj), .arriba(seven[7]), .en(en),
    .Rt(Teclado));  // open: _1
  pixel pixel_202 (
    .izq(six[9]), .der(eight[9]), .Dir(in_4), .salida(seven[9]), .R(Reloj), .arriba(seven[8]), .en(en),
    .Rt(Teclado));  // open: _1
  pixel pixel_203 (
    .izq(six[10]), .der(eight[10]), .Dir(in_4), .salida(seven[10]), .R(Reloj), .arriba(seven[9]), .en(en),
    .Rt(Teclado));  // open: _1
  pixel pixel_204 (
    .izq(six[11]), .der(eight[11]), .Dir(in_4), .salida(seven[11]), .R(Reloj), .arriba(seven[10]), .en(en),
    .Rt(Teclado));  // open: _1
  pixel pixel_205 (
    .izq(six[12]), .der(eight[12]), .Dir(in_4), .salida(seven[12]), .R(Reloj), .arriba(seven[11]), .en(en),
    .Rt(Teclado));  // open: _1
  pixel pixel_206 (
    .izq(six[13]), .der(eight[13]), .Dir(in_4), .salida(seven[13]), .R(Reloj), .arriba(seven[12]), .en(en),
    .Rt(Teclado));  // open: _1
  pixel pixel_207 (
    .izq(six[14]), .der(eight[14]), .Dir(in_4), .salida(seven[14]), .R(Reloj), .arriba(seven[13]), .en(en),
    .Rt(Teclado));  // open: _1
  pixel pixel_208 (
    .izq(six[15]), .der(eight[15]), .Dir(in_4), .salida(seven[15]), .R(Reloj), .arriba(seven[14]), .en(en),
    .Rt(Teclado));  // open: _1
  pixel pixel_209 (
    .izq(six[16]), .der(eight[16]), .Dir(in_4), .salida(seven[16]), .R(Reloj), .arriba(seven[15]), .en(en),
    .Rt(Teclado));  // open: _1
  pixel pixel_210 (
    .izq(six[17]), .der(eight[17]), .Dir(in_4), .salida(seven[17]), .R(Reloj), .arriba(seven[16]), .en(en),
    .Rt(Teclado));  // open: _1
  pixel pixel_211 (
    .izq(six[18]), .der(eight[18]), .Dir(in_4), .salida(seven[18]), .R(Reloj), .arriba(seven[17]), .en(en),
    .Rt(Teclado));  // open: _1
  pixel pixel_212 (
    .izq(six[19]), .der(eight[19]), .Dir(in_4), .salida(seven[19]), .R(Reloj), .arriba(seven[18]), .en(en),
    .Rt(Teclado));  // open: _1
  pixel pixel_213 (
    .izq(six[20]), .der(eight[20]), .Dir(in_4), .salida(seven[20]), .R(Reloj), .arriba(seven[19]), .en(en),
    .Rt(Teclado));  // open: _1
  pixel pixel_214 (
    .izq(six[21]), .der(eight[21]), .Dir(in_4), .salida(seven[21]), .R(Reloj), .arriba(seven[20]), .en(en),
    .Rt(Teclado));  // open: _1
  pixel pixel_215 (
    .izq(six[22]), .der(eight[22]), .Dir(in_4), .salida(seven[22]), .R(Reloj), .arriba(seven[21]), .en(en),
    .Rt(Teclado));  // open: _1
  pixel pixel_216 (
    .izq(six[23]), .der(eight[23]), .Dir(in_4), .salida(seven[23]), .R(Reloj), .arriba(seven[22]), .en(en),
    .Rt(Teclado));  // open: _1
  pixel pixel_217 (
    .izq(six[24]), .der(eight[24]), .Dir(in_4), .salida(seven[24]), .R(Reloj), .arriba(seven[23]), .en(en),
    .Rt(Teclado));  // open: _1
  pixel pixel_218 (
    .izq(six[25]), .der(eight[25]), .Dir(in_4), .salida(seven[25]), .R(Reloj), .arriba(seven[24]), .en(en),
    .Rt(Teclado));  // open: _1
  pixel pixel_219 (
    .izq(six[26]), .der(eight[26]), .Dir(in_4), .salida(seven[26]), .R(Reloj), .arriba(seven[25]), .en(en),
    .Rt(Teclado));  // open: _1
  pixel pixel_220 (
    .izq(six[27]), .der(eight[27]), .Dir(in_4), .salida(seven[27]), .R(Reloj), .arriba(seven[26]), .en(en),
    .Rt(Teclado));  // open: _1
  pixel pixel_221 (
    .izq(six[28]), .der(eight[28]), .Dir(in_4), .salida(seven[28]), .R(Reloj), .arriba(seven[27]), .en(en),
    .Rt(Teclado));  // open: _1
  pixel pixel_222 (
    .izq(six[29]), .der(eight[29]), .Dir(in_4), .salida(seven[29]), .R(Reloj), .arriba(seven[28]), .en(en),
    .Rt(Teclado));  // open: _1
  pixel pixel_223 (
    .izq(six[30]), .der(eight[30]), .Dir(in_4), .salida(seven[30]), .R(Reloj), .arriba(seven[29]), .en(en),
    .Rt(Teclado));  // open: _1
  pixel pixel_224 (
    .izq(six[31]), .der(eight[31]), .Dir(in_4), .salida(seven[31]), .R(Reloj), .arriba(seven[30]), .en(en),
    .Rt(Teclado));  // open: _1
  pixel pixel_225 (
    .izq(seven[0]), .der(nine[0]), .Dir(in_4), .salida(eight[0]), .R(Reloj), .arriba(eight[31]),
    ._1(undriven_11), .en(en), .Rt(Teclado));
  pixel pixel_226 (
    .izq(seven[1]), .der(nine[1]), .Dir(in_4), .salida(eight[1]), .R(Reloj), .arriba(eight[0]),
    ._1(undriven_12), .en(en), .Rt(Teclado));
  pixel pixel_227 (
    .izq(seven[2]), .der(nine[2]), .Dir(in_4), .salida(eight[2]), .R(Reloj), .arriba(eight[1]), .en(en),
    .Rt(Teclado));  // open: _1
  pixel pixel_228 (
    .izq(seven[3]), .der(nine[3]), .Dir(in_4), .salida(eight[3]), .R(Reloj), .arriba(eight[2]), .en(en),
    .Rt(Teclado));  // open: _1
  pixel pixel_229 (
    .izq(seven[4]), .der(nine[4]), .Dir(in_4), .salida(eight[4]), .R(Reloj), .arriba(eight[3]), .en(en),
    .Rt(Teclado));  // open: _1
  pixel pixel_230 (
    .izq(seven[5]), .der(nine[5]), .Dir(in_4), .salida(eight[5]), .R(Reloj), .arriba(eight[4]), .en(en),
    .Rt(Teclado));  // open: _1
  pixel pixel_231 (
    .izq(seven[6]), .der(nine[6]), .Dir(in_4), .salida(eight[6]), .R(Reloj), .arriba(eight[5]), .en(en),
    .Rt(Teclado));  // open: _1
  pixel pixel_232 (
    .izq(seven[7]), .der(nine[7]), .Dir(in_4), .salida(eight[7]), .R(Reloj), .arriba(eight[6]), .en(en),
    .Rt(Teclado));  // open: _1
  pixel pixel_233 (
    .izq(seven[8]), .der(nine[8]), .Dir(in_4), .salida(eight[8]), .R(Reloj), .arriba(eight[7]), .en(en),
    .Rt(Teclado));  // open: _1
  pixel pixel_234 (
    .izq(seven[9]), .der(nine[9]), .Dir(in_4), .salida(eight[9]), .R(Reloj), .arriba(eight[8]), .en(en),
    .Rt(Teclado));  // open: _1
  pixel pixel_235 (
    .izq(seven[10]), .der(nine[10]), .Dir(in_4), .salida(eight[10]), .R(Reloj), .arriba(eight[9]), .en(en),
    .Rt(Teclado));  // open: _1
  pixel pixel_236 (
    .izq(seven[11]), .der(nine[11]), .Dir(in_4), .salida(eight[11]), .R(Reloj), .arriba(eight[10]), .en(en),
    .Rt(Teclado));  // open: _1
  pixel pixel_237 (
    .izq(seven[12]), .der(nine[12]), .Dir(in_4), .salida(eight[12]), .R(Reloj), .arriba(eight[11]), .en(en),
    .Rt(Teclado));  // open: _1
  pixel pixel_238 (
    .izq(seven[13]), .der(nine[13]), .Dir(in_4), .salida(eight[13]), .R(Reloj), .arriba(eight[12]), .en(en),
    .Rt(Teclado));  // open: _1
  pixel pixel_239 (
    .izq(seven[14]), .der(nine[14]), .Dir(in_4), .salida(eight[14]), .R(Reloj), .arriba(eight[13]), .en(en),
    .Rt(Teclado));  // open: _1
  pixel pixel_240 (
    .izq(seven[15]), .der(nine[15]), .Dir(in_4), .salida(eight[15]), .R(Reloj), .arriba(eight[14]), .en(en),
    .Rt(Teclado));  // open: _1
  pixel pixel_241 (
    .izq(seven[16]), .der(nine[16]), .Dir(in_4), .salida(eight[16]), .R(Reloj), .arriba(eight[15]), .en(en),
    .Rt(Teclado));  // open: _1
  pixel pixel_242 (
    .izq(seven[17]), .der(nine[17]), .Dir(in_4), .salida(eight[17]), .R(Reloj), .arriba(eight[16]), .en(en),
    .Rt(Teclado));  // open: _1
  pixel pixel_243 (
    .izq(seven[18]), .der(nine[18]), .Dir(in_4), .salida(eight[18]), .R(Reloj), .arriba(eight[17]), .en(en),
    .Rt(Teclado));  // open: _1
  pixel pixel_244 (
    .izq(seven[19]), .der(nine[19]), .Dir(in_4), .salida(eight[19]), .R(Reloj), .arriba(eight[18]), .en(en),
    .Rt(Teclado));  // open: _1
  pixel pixel_245 (
    .izq(seven[20]), .der(nine[20]), .Dir(in_4), .salida(eight[20]), .R(Reloj), .arriba(eight[19]), .en(en),
    .Rt(Teclado));  // open: _1
  pixel pixel_246 (
    .izq(seven[21]), .der(nine[21]), .Dir(in_4), .salida(eight[21]), .R(Reloj), .arriba(eight[20]), .en(en),
    .Rt(Teclado));  // open: _1
  pixel pixel_247 (
    .izq(seven[22]), .der(nine[22]), .Dir(in_4), .salida(eight[22]), .R(Reloj), .arriba(eight[21]), .en(en),
    .Rt(Teclado));  // open: _1
  pixel pixel_248 (
    .izq(seven[23]), .der(nine[23]), .Dir(in_4), .salida(eight[23]), .R(Reloj), .arriba(eight[22]), .en(en),
    .Rt(Teclado));  // open: _1
  pixel pixel_249 (
    .izq(seven[24]), .der(nine[24]), .Dir(in_4), .salida(eight[24]), .R(Reloj), .arriba(eight[23]), .en(en),
    .Rt(Teclado));  // open: _1
  pixel pixel_250 (
    .izq(seven[25]), .der(nine[25]), .Dir(in_4), .salida(eight[25]), .R(Reloj), .arriba(eight[24]), .en(en),
    .Rt(Teclado));  // open: _1
  pixel pixel_251 (
    .izq(seven[26]), .der(nine[26]), .Dir(in_4), .salida(eight[26]), .R(Reloj), .arriba(eight[25]), .en(en),
    .Rt(Teclado));  // open: _1
  pixel pixel_252 (
    .izq(seven[27]), .der(nine[27]), .Dir(in_4), .salida(eight[27]), .R(Reloj), .arriba(eight[26]), .en(en),
    .Rt(Teclado));  // open: _1
  pixel pixel_253 (
    .izq(seven[28]), .der(nine[28]), .Dir(in_4), .salida(eight[28]), .R(Reloj), .arriba(eight[27]), .en(en),
    .Rt(Teclado));  // open: _1
  pixel pixel_254 (
    .izq(seven[29]), .der(nine[29]), .Dir(in_4), .salida(eight[29]), .R(Reloj), .arriba(eight[28]), .en(en),
    .Rt(Teclado));  // open: _1
  pixel pixel_255 (
    .izq(seven[30]), .der(nine[30]), .Dir(in_4), .salida(eight[30]), .R(Reloj), .arriba(eight[29]), .en(en),
    .Rt(Teclado));  // open: _1
  pixel pixel_256 (
    .izq(seven[31]), .der(nine[31]), .Dir(in_4), .salida(eight[31]), .R(Reloj), .arriba(eight[30]), .en(en),
    .Rt(Teclado));  // open: _1
  pixel pixel_257 (
    .izq(eight[0]), .der(ten[0]), .Dir(in_4), .salida(nine[0]), .R(Reloj), .arriba(nine[31]),
    ._1(undriven_13), .en(en), .Rt(Teclado));
  pixel pixel_258 (
    .izq(eight[1]), .der(ten[1]), .Dir(in_4), .salida(nine[1]), .R(Reloj), .arriba(nine[0]),
    ._1(undriven_14), .en(en), .Rt(Teclado));
  pixel pixel_259 (
    .izq(eight[2]), .der(ten[2]), .Dir(in_4), .salida(nine[2]), .R(Reloj), .arriba(nine[1]), .en(en),
    .Rt(Teclado));  // open: _1
  pixel pixel_260 (
    .izq(eight[3]), .der(ten[3]), .Dir(in_4), .salida(nine[3]), .R(Reloj), .arriba(nine[2]), .en(en),
    .Rt(Teclado));  // open: _1
  pixel pixel_261 (
    .izq(eight[4]), .der(ten[4]), .Dir(in_4), .salida(nine[4]), .R(Reloj), .arriba(nine[3]), .en(en),
    .Rt(Teclado));  // open: _1
  pixel pixel_262 (
    .izq(eight[5]), .der(ten[5]), .Dir(in_4), .salida(nine[5]), .R(Reloj), .arriba(nine[4]), .en(en),
    .Rt(Teclado));  // open: _1
  pixel pixel_263 (
    .izq(eight[6]), .der(ten[6]), .Dir(in_4), .salida(nine[6]), .R(Reloj), .arriba(nine[5]), .en(en),
    .Rt(Teclado));  // open: _1
  pixel pixel_264 (
    .izq(eight[7]), .der(ten[7]), .Dir(in_4), .salida(nine[7]), .R(Reloj), .arriba(nine[6]), .en(en),
    .Rt(Teclado));  // open: _1
  pixel pixel_265 (
    .izq(eight[8]), .der(ten[8]), .Dir(in_4), .salida(nine[8]), .R(Reloj), .arriba(nine[7]), .en(en),
    .Rt(Teclado));  // open: _1
  pixel pixel_266 (
    .izq(eight[9]), .der(ten[9]), .Dir(in_4), .salida(nine[9]), .R(Reloj), .arriba(nine[8]), .en(en),
    .Rt(Teclado));  // open: _1
  pixel pixel_267 (
    .izq(eight[10]), .der(ten[10]), .Dir(in_4), .salida(nine[10]), .R(Reloj), .arriba(nine[9]), .en(en),
    .Rt(Teclado));  // open: _1
  pixel pixel_268 (
    .izq(eight[11]), .der(ten[11]), .Dir(in_4), .salida(nine[11]), .R(Reloj), .arriba(nine[10]), .en(en),
    .Rt(Teclado));  // open: _1
  pixel pixel_269 (
    .izq(eight[12]), .der(ten[12]), .Dir(in_4), .salida(nine[12]), .R(Reloj), .arriba(nine[11]), .en(en),
    .Rt(Teclado));  // open: _1
  pixel pixel_270 (
    .izq(eight[13]), .der(ten[13]), .Dir(in_4), .salida(nine[13]), .R(Reloj), .arriba(nine[12]), .en(en),
    .Rt(Teclado));  // open: _1
  pixel pixel_271 (
    .izq(eight[14]), .der(ten[14]), .Dir(in_4), .salida(nine[14]), .R(Reloj), .arriba(nine[13]), .en(en),
    .Rt(Teclado));  // open: _1
  pixel pixel_272 (
    .izq(eight[15]), .der(ten[15]), .Dir(in_4), .salida(nine[15]), .R(Reloj), .arriba(nine[14]), .en(en),
    .Rt(Teclado));  // open: _1
  pixel pixel_273 (
    .izq(eight[16]), .der(ten[16]), .Dir(in_4), .salida(nine[16]), .R(Reloj), .arriba(nine[15]), .en(en),
    .Rt(Teclado));  // open: _1
  pixel pixel_274 (
    .izq(eight[17]), .der(ten[17]), .Dir(in_4), .salida(nine[17]), .R(Reloj), .arriba(nine[16]), .en(en),
    .Rt(Teclado));  // open: _1
  pixel pixel_275 (
    .izq(eight[18]), .der(ten[18]), .Dir(in_4), .salida(nine[18]), .R(Reloj), .arriba(nine[17]), .en(en),
    .Rt(Teclado));  // open: _1
  pixel pixel_276 (
    .izq(eight[19]), .der(ten[19]), .Dir(in_4), .salida(nine[19]), .R(Reloj), .arriba(nine[18]), .en(en),
    .Rt(Teclado));  // open: _1
  pixel pixel_277 (
    .izq(eight[20]), .der(ten[20]), .Dir(in_4), .salida(nine[20]), .R(Reloj), .arriba(nine[19]), .en(en),
    .Rt(Teclado));  // open: _1
  pixel pixel_278 (
    .izq(eight[21]), .der(ten[21]), .Dir(in_4), .salida(nine[21]), .R(Reloj), .arriba(nine[20]), .en(en),
    .Rt(Teclado));  // open: _1
  pixel pixel_279 (
    .izq(eight[22]), .der(ten[22]), .Dir(in_4), .salida(nine[22]), .R(Reloj), .arriba(nine[21]), .en(en),
    .Rt(Teclado));  // open: _1
  pixel pixel_280 (
    .izq(eight[23]), .der(ten[23]), .Dir(in_4), .salida(nine[23]), .R(Reloj), .arriba(nine[22]), .en(en),
    .Rt(Teclado));  // open: _1
  pixel pixel_281 (
    .izq(eight[24]), .der(ten[24]), .Dir(in_4), .salida(nine[24]), .R(Reloj), .arriba(nine[23]), .en(en),
    .Rt(Teclado));  // open: _1
  pixel pixel_282 (
    .izq(eight[25]), .der(ten[25]), .Dir(in_4), .salida(nine[25]), .R(Reloj), .arriba(nine[24]), .en(en),
    .Rt(Teclado));  // open: _1
  pixel pixel_283 (
    .izq(eight[26]), .der(ten[26]), .Dir(in_4), .salida(nine[26]), .R(Reloj), .arriba(nine[25]), .en(en),
    .Rt(Teclado));  // open: _1
  pixel pixel_284 (
    .izq(eight[27]), .der(ten[27]), .Dir(in_4), .salida(nine[27]), .R(Reloj), .arriba(nine[26]), .en(en),
    .Rt(Teclado));  // open: _1
  pixel pixel_285 (
    .izq(eight[28]), .der(ten[28]), .Dir(in_4), .salida(nine[28]), .R(Reloj), .arriba(nine[27]), .en(en),
    .Rt(Teclado));  // open: _1
  pixel pixel_286 (
    .izq(eight[29]), .der(ten[29]), .Dir(in_4), .salida(nine[29]), .R(Reloj), .arriba(nine[28]), .en(en),
    .Rt(Teclado));  // open: _1
  pixel pixel_287 (
    .izq(eight[30]), .der(ten[30]), .Dir(in_4), .salida(nine[30]), .R(Reloj), .arriba(nine[29]), .en(en),
    .Rt(Teclado));  // open: _1
  pixel pixel_288 (
    .izq(eight[31]), .der(ten[31]), .Dir(in_4), .salida(nine[31]), .R(Reloj), .arriba(nine[30]), .en(en),
    .Rt(Teclado));  // open: _1
  pixel pixel_289 (
    .izq(nine[0]), .der(eleven[0]), .Dir(in_4), .salida(ten[0]), .R(Reloj), .arriba(ten[31]),
    ._1(undriven_15), .en(en), .Rt(Teclado));
  pixel pixel_290 (
    .izq(nine[1]), .der(eleven[1]), .Dir(in_4), .salida(ten[1]), .R(Reloj), .arriba(ten[0]),
    ._1(undriven_16), .en(en), .Rt(Teclado));
  pixel pixel_291 (
    .izq(nine[2]), .der(eleven[2]), .Dir(in_4), .salida(ten[2]), .R(Reloj), .arriba(ten[1]), .en(en),
    .Rt(Teclado));  // open: _1
  pixel pixel_292 (
    .izq(nine[3]), .der(eleven[3]), .Dir(in_4), .salida(ten[3]), .R(Reloj), .arriba(ten[2]), .en(en),
    .Rt(Teclado));  // open: _1
  pixel pixel_293 (
    .izq(nine[4]), .der(eleven[4]), .Dir(in_4), .salida(ten[4]), .R(Reloj), .arriba(ten[3]), .en(en),
    .Rt(Teclado));  // open: _1
  pixel pixel_294 (
    .izq(nine[5]), .der(eleven[5]), .Dir(in_4), .salida(ten[5]), .R(Reloj), .arriba(ten[4]), .en(en),
    .Rt(Teclado));  // open: _1
  pixel pixel_295 (
    .izq(nine[6]), .der(eleven[6]), .Dir(in_4), .salida(ten[6]), .R(Reloj), .arriba(ten[5]), .en(en),
    .Rt(Teclado));  // open: _1
  pixel pixel_296 (
    .izq(nine[7]), .der(eleven[7]), .Dir(in_4), .salida(ten[7]), .R(Reloj), .arriba(ten[6]), .en(en),
    .Rt(Teclado));  // open: _1
  pixel pixel_297 (
    .izq(nine[8]), .der(eleven[8]), .Dir(in_4), .salida(ten[8]), .R(Reloj), .arriba(ten[7]), .en(en),
    .Rt(Teclado));  // open: _1
  pixel pixel_298 (
    .izq(nine[9]), .der(eleven[9]), .Dir(in_4), .salida(ten[9]), .R(Reloj), .arriba(ten[8]), .en(en),
    .Rt(Teclado));  // open: _1
  pixel pixel_299 (
    .izq(nine[10]), .der(eleven[10]), .Dir(in_4), .salida(ten[10]), .R(Reloj), .arriba(ten[9]), .en(en),
    .Rt(Teclado));  // open: _1
  pixel pixel_300 (
    .izq(nine[11]), .der(eleven[11]), .Dir(in_4), .salida(ten[11]), .R(Reloj), .arriba(ten[10]), .en(en),
    .Rt(Teclado));  // open: _1
  pixel pixel_301 (
    .izq(nine[12]), .der(eleven[12]), .Dir(in_4), .salida(ten[12]), .R(Reloj), .arriba(ten[11]), .en(en),
    .Rt(Teclado));  // open: _1
  pixel pixel_302 (
    .izq(nine[13]), .der(eleven[13]), .Dir(in_4), .salida(ten[13]), .R(Reloj), .arriba(ten[12]), .en(en),
    .Rt(Teclado));  // open: _1
  pixel pixel_303 (
    .izq(nine[14]), .der(eleven[14]), .Dir(in_4), .salida(ten[14]), .R(Reloj), .arriba(ten[13]), .en(en),
    .Rt(Teclado));  // open: _1
  pixel pixel_304 (
    .izq(nine[15]), .der(eleven[15]), .Dir(in_4), .salida(ten[15]), .R(Reloj), .arriba(ten[14]), .en(en),
    .Rt(Teclado));  // open: _1
  pixel pixel_305 (
    .izq(nine[16]), .der(eleven[16]), .Dir(in_4), .salida(ten[16]), .R(Reloj), .arriba(ten[15]), .en(en),
    .Rt(Teclado));  // open: _1
  pixel pixel_306 (
    .izq(nine[17]), .der(eleven[17]), .Dir(in_4), .salida(ten[17]), .R(Reloj), .arriba(ten[16]), .en(en),
    .Rt(Teclado));  // open: _1
  pixel pixel_307 (
    .izq(nine[18]), .der(eleven[18]), .Dir(in_4), .salida(ten[18]), .R(Reloj), .arriba(ten[17]), .en(en),
    .Rt(Teclado));  // open: _1
  pixel pixel_308 (
    .izq(nine[19]), .der(eleven[19]), .Dir(in_4), .salida(ten[19]), .R(Reloj), .arriba(ten[18]), .en(en),
    .Rt(Teclado));  // open: _1
  pixel pixel_309 (
    .izq(nine[20]), .der(eleven[20]), .Dir(in_4), .salida(ten[20]), .R(Reloj), .arriba(ten[19]), .en(en),
    .Rt(Teclado));  // open: _1
  pixel pixel_310 (
    .izq(nine[21]), .der(eleven[21]), .Dir(in_4), .salida(ten[21]), .R(Reloj), .arriba(ten[20]), .en(en),
    .Rt(Teclado));  // open: _1
  pixel pixel_311 (
    .izq(nine[22]), .der(eleven[22]), .Dir(in_4), .salida(ten[22]), .R(Reloj), .arriba(ten[21]), .en(en),
    .Rt(Teclado));  // open: _1
  pixel pixel_312 (
    .izq(nine[23]), .der(eleven[23]), .Dir(in_4), .salida(ten[23]), .R(Reloj), .arriba(ten[22]), .en(en),
    .Rt(Teclado));  // open: _1
  pixel pixel_313 (
    .izq(nine[24]), .der(eleven[24]), .Dir(in_4), .salida(ten[24]), .R(Reloj), .arriba(ten[23]), .en(en),
    .Rt(Teclado));  // open: _1
  pixel pixel_314 (
    .izq(nine[25]), .der(eleven[25]), .Dir(in_4), .salida(ten[25]), .R(Reloj), .arriba(ten[24]), .en(en),
    .Rt(Teclado));  // open: _1
  pixel pixel_315 (
    .izq(nine[26]), .der(eleven[26]), .Dir(in_4), .salida(ten[26]), .R(Reloj), .arriba(ten[25]), .en(en),
    .Rt(Teclado));  // open: _1
  pixel pixel_316 (
    .izq(nine[27]), .der(eleven[27]), .Dir(in_4), .salida(ten[27]), .R(Reloj), .arriba(ten[26]), .en(en),
    .Rt(Teclado));  // open: _1
  pixel pixel_317 (
    .izq(nine[28]), .der(eleven[28]), .Dir(in_4), .salida(ten[28]), .R(Reloj), .arriba(ten[27]), .en(en),
    .Rt(Teclado));  // open: _1
  pixel pixel_318 (
    .izq(nine[29]), .der(eleven[29]), .Dir(in_4), .salida(ten[29]), .R(Reloj), .arriba(ten[28]), .en(en),
    .Rt(Teclado));  // open: _1
  pixel pixel_319 (
    .izq(nine[30]), .der(eleven[30]), .Dir(in_4), .salida(ten[30]), .R(Reloj), .arriba(ten[29]), .en(en),
    .Rt(Teclado));  // open: _1
  pixel pixel_320 (
    .izq(nine[31]), .der(eleven[31]), .Dir(in_4), .salida(ten[31]), .R(Reloj), .arriba(ten[30]), .en(en),
    .Rt(Teclado));  // open: _1
  pixel pixel_321 (
    .izq(ten[0]), .der(twelve[0]), .Dir(in_4), .salida(eleven[0]), .R(Reloj), .arriba(eleven[31]),
    ._1(undriven_17), .en(en), .Rt(Teclado));
  pixel pixel_322 (
    .izq(ten[1]), .der(twelve[1]), .Dir(in_4), .salida(eleven[1]), .R(Reloj), .arriba(eleven[0]),
    ._1(undriven_18), .en(en), .Rt(Teclado));
  pixel pixel_323 (
    .izq(ten[2]), .der(twelve[2]), .Dir(in_4), .salida(eleven[2]), .R(Reloj), .arriba(eleven[1]), .en(en),
    .Rt(Teclado));  // open: _1
  pixel pixel_324 (
    .izq(ten[3]), .der(twelve[3]), .Dir(in_4), .salida(eleven[3]), .R(Reloj), .arriba(eleven[2]), .en(en),
    .Rt(Teclado));  // open: _1
  pixel pixel_325 (
    .izq(ten[4]), .der(twelve[4]), .Dir(in_4), .salida(eleven[4]), .R(Reloj), .arriba(eleven[3]), .en(en),
    .Rt(Teclado));  // open: _1
  pixel pixel_326 (
    .izq(ten[5]), .der(twelve[5]), .Dir(in_4), .salida(eleven[5]), .R(Reloj), .arriba(eleven[4]), .en(en),
    .Rt(Teclado));  // open: _1
  pixel pixel_327 (
    .izq(ten[6]), .der(twelve[6]), .Dir(in_4), .salida(eleven[6]), .R(Reloj), .arriba(eleven[5]), .en(en),
    .Rt(Teclado));  // open: _1
  pixel pixel_328 (
    .izq(ten[7]), .der(twelve[7]), .Dir(in_4), .salida(eleven[7]), .R(Reloj), .arriba(eleven[6]), .en(en),
    .Rt(Teclado));  // open: _1
  pixel pixel_329 (
    .izq(ten[8]), .der(twelve[8]), .Dir(in_4), .salida(eleven[8]), .R(Reloj), .arriba(eleven[7]), .en(en),
    .Rt(Teclado));  // open: _1
  pixel pixel_330 (
    .izq(ten[9]), .der(twelve[9]), .Dir(in_4), .salida(eleven[9]), .R(Reloj), .arriba(eleven[8]), .en(en),
    .Rt(Teclado));  // open: _1
  pixel pixel_331 (
    .izq(ten[10]), .der(twelve[10]), .Dir(in_4), .salida(eleven[10]), .R(Reloj), .arriba(eleven[9]), .en(en),
    .Rt(Teclado));  // open: _1
  pixel pixel_332 (
    .izq(ten[11]), .der(twelve[11]), .Dir(in_4), .salida(eleven[11]), .R(Reloj), .arriba(eleven[10]),
    .en(en), .Rt(Teclado));  // open: _1
  pixel pixel_333 (
    .izq(ten[12]), .der(twelve[12]), .Dir(in_4), .salida(eleven[12]), .R(Reloj), .arriba(eleven[11]),
    .en(en), .Rt(Teclado));  // open: _1
  pixel pixel_334 (
    .izq(ten[13]), .der(twelve[13]), .Dir(in_4), .salida(eleven[13]), .R(Reloj), .arriba(eleven[12]),
    .en(en), .Rt(Teclado));  // open: _1
  pixel pixel_335 (
    .izq(ten[14]), .der(twelve[14]), .Dir(in_4), .salida(eleven[14]), .R(Reloj), .arriba(eleven[13]),
    .en(en), .Rt(Teclado));  // open: _1
  pixel pixel_336 (
    .izq(ten[15]), .der(twelve[15]), .Dir(in_4), .salida(eleven[15]), .R(Reloj), .arriba(eleven[14]),
    .en(en), .Rt(Teclado));  // open: _1
  pixel pixel_337 (
    .izq(ten[16]), .der(twelve[16]), .Dir(in_4), .salida(eleven[16]), .R(Reloj), .arriba(eleven[15]),
    .en(en), .Rt(Teclado));  // open: _1
  pixel pixel_338 (
    .izq(ten[17]), .der(twelve[17]), .Dir(in_4), .salida(eleven[17]), .R(Reloj), .arriba(eleven[16]),
    .en(en), .Rt(Teclado));  // open: _1
  pixel pixel_339 (
    .izq(ten[18]), .der(twelve[18]), .Dir(in_4), .salida(eleven[18]), .R(Reloj), .arriba(eleven[17]),
    .en(en), .Rt(Teclado));  // open: _1
  pixel pixel_340 (
    .izq(ten[19]), .der(twelve[19]), .Dir(in_4), .salida(eleven[19]), .R(Reloj), .arriba(eleven[18]),
    .en(en), .Rt(Teclado));  // open: _1
  pixel pixel_341 (
    .izq(ten[20]), .der(twelve[20]), .Dir(in_4), .salida(eleven[20]), .R(Reloj), .arriba(eleven[19]),
    .en(en), .Rt(Teclado));  // open: _1
  pixel pixel_342 (
    .izq(ten[21]), .der(twelve[21]), .Dir(in_4), .salida(eleven[21]), .R(Reloj), .arriba(eleven[20]),
    .en(en), .Rt(Teclado));  // open: _1
  pixel pixel_343 (
    .izq(ten[22]), .der(twelve[22]), .Dir(in_4), .salida(eleven[22]), .R(Reloj), .arriba(eleven[21]),
    .en(en), .Rt(Teclado));  // open: _1
  pixel pixel_344 (
    .izq(ten[23]), .der(twelve[23]), .Dir(in_4), .salida(eleven[23]), .R(Reloj), .arriba(eleven[22]),
    .en(en), .Rt(Teclado));  // open: _1
  pixel pixel_345 (
    .izq(ten[24]), .der(twelve[24]), .Dir(in_4), .salida(eleven[24]), .R(Reloj), .arriba(eleven[23]),
    .en(en), .Rt(Teclado));  // open: _1
  pixel pixel_346 (
    .izq(ten[25]), .der(twelve[25]), .Dir(in_4), .salida(eleven[25]), .R(Reloj), .arriba(eleven[24]),
    .en(en), .Rt(Teclado));  // open: _1
  pixel pixel_347 (
    .izq(ten[26]), .der(twelve[26]), .Dir(in_4), .salida(eleven[26]), .R(Reloj), .arriba(eleven[25]),
    .en(en), .Rt(Teclado));  // open: _1
  pixel pixel_348 (
    .izq(ten[27]), .der(twelve[27]), .Dir(in_4), .salida(eleven[27]), .R(Reloj), .arriba(eleven[26]),
    .en(en), .Rt(Teclado));  // open: _1
  pixel pixel_349 (
    .izq(ten[28]), .der(twelve[28]), .Dir(in_4), .salida(eleven[28]), .R(Reloj), .arriba(eleven[27]),
    .en(en), .Rt(Teclado));  // open: _1
  pixel pixel_350 (
    .izq(ten[29]), .der(twelve[29]), .Dir(in_4), .salida(eleven[29]), .R(Reloj), .arriba(eleven[28]),
    .en(en), .Rt(Teclado));  // open: _1
  pixel pixel_351 (
    .izq(ten[30]), .der(twelve[30]), .Dir(in_4), .salida(eleven[30]), .R(Reloj), .arriba(eleven[29]),
    .en(en), .Rt(Teclado));  // open: _1
  pixel pixel_352 (
    .izq(ten[31]), .der(twelve[31]), .Dir(in_4), .salida(eleven[31]), .R(Reloj), .arriba(eleven[30]),
    .en(en), .Rt(Teclado));  // open: _1
  pixel pixel_353 (
    .izq(eleven[0]), .der(thirteen[0]), .Dir(in_4), .salida(twelve[0]), .R(Reloj), .arriba(twelve[31]),
    ._1(undriven_19), .en(en), .Rt(Teclado));
  pixel pixel_354 (
    .izq(eleven[1]), .der(thirteen[1]), .Dir(in_4), .salida(twelve[1]), .R(Reloj), .arriba(twelve[0]),
    ._1(undriven_20), .en(en), .Rt(Teclado));
  pixel pixel_355 (
    .izq(eleven[2]), .der(thirteen[2]), .Dir(in_4), .salida(twelve[2]), .R(Reloj), .arriba(twelve[1]),
    .en(en), .Rt(Teclado));  // open: _1
  pixel pixel_356 (
    .izq(eleven[3]), .der(thirteen[3]), .Dir(in_4), .salida(twelve[3]), .R(Reloj), .arriba(twelve[2]),
    .en(en), .Rt(Teclado));  // open: _1
  pixel pixel_357 (
    .izq(eleven[4]), .der(thirteen[4]), .Dir(in_4), .salida(twelve[4]), .R(Reloj), .arriba(twelve[3]),
    .en(en), .Rt(Teclado));  // open: _1
  pixel pixel_358 (
    .izq(eleven[5]), .der(thirteen[5]), .Dir(in_4), .salida(twelve[5]), .R(Reloj), .arriba(twelve[4]),
    .en(en), .Rt(Teclado));  // open: _1
  pixel pixel_359 (
    .izq(eleven[6]), .der(thirteen[6]), .Dir(in_4), .salida(twelve[6]), .R(Reloj), .arriba(twelve[5]),
    .en(en), .Rt(Teclado));  // open: _1
  pixel pixel_360 (
    .izq(eleven[7]), .der(thirteen[7]), .Dir(in_4), .salida(twelve[7]), .R(Reloj), .arriba(twelve[6]),
    .en(en), .Rt(Teclado));  // open: _1
  pixel pixel_361 (
    .izq(eleven[8]), .der(thirteen[8]), .Dir(in_4), .salida(twelve[8]), .R(Reloj), .arriba(twelve[7]),
    .en(en), .Rt(Teclado));  // open: _1
  pixel pixel_362 (
    .izq(eleven[9]), .der(thirteen[9]), .Dir(in_4), .salida(twelve[9]), .R(Reloj), .arriba(twelve[8]),
    .en(en), .Rt(Teclado));  // open: _1
  pixel pixel_363 (
    .izq(eleven[10]), .der(thirteen[10]), .Dir(in_4), .salida(twelve[10]), .R(Reloj), .arriba(twelve[9]),
    .en(en), .Rt(Teclado));  // open: _1
  pixel pixel_364 (
    .izq(eleven[11]), .der(thirteen[11]), .Dir(in_4), .salida(twelve[11]), .R(Reloj), .arriba(twelve[10]),
    .en(en), .Rt(Teclado));  // open: _1
  pixel pixel_365 (
    .izq(eleven[12]), .der(thirteen[12]), .Dir(in_4), .salida(twelve[12]), .R(Reloj), .arriba(twelve[11]),
    .en(en), .Rt(Teclado));  // open: _1
  pixel pixel_366 (
    .izq(eleven[13]), .der(thirteen[13]), .Dir(in_4), .salida(twelve[13]), .R(Reloj), .arriba(twelve[12]),
    .en(en), .Rt(Teclado));  // open: _1
  pixel pixel_367 (
    .izq(eleven[14]), .der(thirteen[14]), .Dir(in_4), .salida(twelve[14]), .R(Reloj), .arriba(twelve[13]),
    .en(en), .Rt(Teclado));  // open: _1
  pixel pixel_368 (
    .izq(eleven[15]), .der(thirteen[15]), .Dir(in_4), .salida(twelve[15]), .R(Reloj), .arriba(twelve[14]),
    .en(en), .Rt(Teclado));  // open: _1
  pixel pixel_369 (
    .izq(eleven[16]), .der(thirteen[16]), .Dir(in_4), .salida(twelve[16]), .R(Reloj), .arriba(twelve[15]),
    .en(en), .Rt(Teclado));  // open: _1
  pixel pixel_370 (
    .izq(eleven[17]), .der(thirteen[17]), .Dir(in_4), .salida(twelve[17]), .R(Reloj), .arriba(twelve[16]),
    .en(en), .Rt(Teclado));  // open: _1
  pixel pixel_371 (
    .izq(eleven[18]), .der(thirteen[18]), .Dir(in_4), .salida(twelve[18]), .R(Reloj), .arriba(twelve[17]),
    .en(en), .Rt(Teclado));  // open: _1
  pixel pixel_372 (
    .izq(eleven[19]), .der(thirteen[19]), .Dir(in_4), .salida(twelve[19]), .R(Reloj), .arriba(twelve[18]),
    .en(en), .Rt(Teclado));  // open: _1
  pixel pixel_373 (
    .izq(eleven[20]), .der(thirteen[20]), .Dir(in_4), .salida(twelve[20]), .R(Reloj), .arriba(twelve[19]),
    .en(en), .Rt(Teclado));  // open: _1
  pixel pixel_374 (
    .izq(eleven[21]), .der(thirteen[21]), .Dir(in_4), .salida(twelve[21]), .R(Reloj), .arriba(twelve[20]),
    .en(en), .Rt(Teclado));  // open: _1
  pixel pixel_375 (
    .izq(eleven[22]), .der(thirteen[22]), .Dir(in_4), .salida(twelve[22]), .R(Reloj), .arriba(twelve[21]),
    .en(en), .Rt(Teclado));  // open: _1
  pixel pixel_376 (
    .izq(eleven[23]), .der(thirteen[23]), .Dir(in_4), .salida(twelve[23]), .R(Reloj), .arriba(twelve[22]),
    .en(en), .Rt(Teclado));  // open: _1
  pixel pixel_377 (
    .izq(eleven[24]), .der(thirteen[24]), .Dir(in_4), .salida(twelve[24]), .R(Reloj), .arriba(twelve[23]),
    .en(en), .Rt(Teclado));  // open: _1
  pixel pixel_378 (
    .izq(eleven[25]), .der(thirteen[25]), .Dir(in_4), .salida(twelve[25]), .R(Reloj), .arriba(twelve[24]),
    .en(en), .Rt(Teclado));  // open: _1
  pixel pixel_379 (
    .izq(eleven[26]), .der(thirteen[26]), .Dir(in_4), .salida(twelve[26]), .R(Reloj), .arriba(twelve[25]),
    .en(en), .Rt(Teclado));  // open: _1
  pixel pixel_380 (
    .izq(eleven[27]), .der(thirteen[27]), .Dir(in_4), .salida(twelve[27]), .R(Reloj), .arriba(twelve[26]),
    .en(en), .Rt(Teclado));  // open: _1
  pixel pixel_381 (
    .izq(eleven[28]), .der(thirteen[28]), .Dir(in_4), .salida(twelve[28]), .R(Reloj), .arriba(twelve[27]),
    .en(en), .Rt(Teclado));  // open: _1
  pixel pixel_382 (
    .izq(eleven[29]), .der(thirteen[29]), .Dir(in_4), .salida(twelve[29]), .R(Reloj), .arriba(twelve[28]),
    .en(en), .Rt(Teclado));  // open: _1
  pixel pixel_383 (
    .izq(eleven[30]), .der(thirteen[30]), .Dir(in_4), .salida(twelve[30]), .R(Reloj), .arriba(twelve[29]),
    .en(en), .Rt(Teclado));  // open: _1
  pixel pixel_384 (
    .izq(eleven[31]), .der(thirteen[31]), .Dir(in_4), .salida(twelve[31]), .R(Reloj), .arriba(twelve[30]),
    .en(en), .Rt(Teclado));  // open: _1
  pixel pixel_385 (
    .izq(twelve[0]), .der(fourteen[0]), .Dir(in_4), .salida(thirteen[0]), .R(Reloj), .arriba(thirteen[31]),
    ._1(undriven_21), .en(en), .Rt(Teclado));
  pixel pixel_386 (
    .izq(twelve[1]), .der(fourteen[1]), .Dir(in_4), .salida(thirteen[1]), .R(Reloj), .arriba(thirteen[0]),
    ._1(undriven_22), .en(en), .Rt(Teclado));
  pixel pixel_387 (
    .izq(twelve[2]), .der(fourteen[2]), .Dir(in_4), .salida(thirteen[2]), .R(Reloj), .arriba(thirteen[1]),
    .en(en), .Rt(Teclado));  // open: _1
  pixel pixel_388 (
    .izq(twelve[3]), .der(fourteen[3]), .Dir(in_4), .salida(thirteen[3]), .R(Reloj), .arriba(thirteen[2]),
    .en(en), .Rt(Teclado));  // open: _1
  pixel pixel_389 (
    .izq(twelve[4]), .der(fourteen[4]), .Dir(in_4), .salida(thirteen[4]), .R(Reloj), .arriba(thirteen[3]),
    .en(en), .Rt(Teclado));  // open: _1
  pixel pixel_390 (
    .izq(twelve[5]), .der(fourteen[5]), .Dir(in_4), .salida(thirteen[5]), .R(Reloj), .arriba(thirteen[4]),
    .en(en), .Rt(Teclado));  // open: _1
  pixel pixel_391 (
    .izq(twelve[6]), .der(fourteen[6]), .Dir(in_4), .salida(thirteen[6]), .R(Reloj), .arriba(thirteen[5]),
    .en(en), .Rt(Teclado));  // open: _1
  pixel pixel_392 (
    .izq(twelve[7]), .der(fourteen[7]), .Dir(in_4), .salida(thirteen[7]), .R(Reloj), .arriba(thirteen[6]),
    .en(en), .Rt(Teclado));  // open: _1
  pixel pixel_393 (
    .izq(twelve[8]), .der(fourteen[8]), .Dir(in_4), .salida(thirteen[8]), .R(Reloj), .arriba(thirteen[7]),
    .en(en), .Rt(Teclado));  // open: _1
  pixel pixel_394 (
    .izq(twelve[9]), .der(fourteen[9]), .Dir(in_4), .salida(thirteen[9]), .R(Reloj), .arriba(thirteen[8]),
    .en(en), .Rt(Teclado));  // open: _1
  pixel pixel_395 (
    .izq(twelve[10]), .der(fourteen[10]), .Dir(in_4), .salida(thirteen[10]), .R(Reloj), .arriba(thirteen[9]),
    .en(en), .Rt(Teclado));  // open: _1
  pixel pixel_396 (
    .izq(twelve[11]), .der(fourteen[11]), .Dir(in_4), .salida(thirteen[11]), .R(Reloj),
    .arriba(thirteen[10]), .en(en), .Rt(Teclado));  // open: _1
  pixel pixel_397 (
    .izq(twelve[12]), .der(fourteen[12]), .Dir(in_4), .salida(thirteen[12]), .R(Reloj),
    .arriba(thirteen[11]), .en(en), .Rt(Teclado));  // open: _1
  pixel pixel_398 (
    .izq(twelve[13]), .der(fourteen[13]), .Dir(in_4), .salida(thirteen[13]), .R(Reloj),
    .arriba(thirteen[12]), .en(en), .Rt(Teclado));  // open: _1
  pixel pixel_399 (
    .izq(twelve[14]), .der(fourteen[14]), .Dir(in_4), .salida(thirteen[14]), .R(Reloj),
    .arriba(thirteen[13]), .en(en), .Rt(Teclado));  // open: _1
  pixel pixel_400 (
    .izq(twelve[15]), .der(fourteen[15]), .Dir(in_4), .salida(thirteen[15]), .R(Reloj),
    .arriba(thirteen[14]), .en(en), .Rt(Teclado));  // open: _1
  pixel pixel_401 (
    .izq(twelve[16]), .der(fourteen[16]), .Dir(in_4), .salida(thirteen[16]), .R(Reloj),
    .arriba(thirteen[15]), .en(en), .Rt(Teclado));  // open: _1
  pixel pixel_402 (
    .izq(twelve[17]), .der(fourteen[17]), .Dir(in_4), .salida(thirteen[17]), .R(Reloj),
    .arriba(thirteen[16]), .en(en), .Rt(Teclado));  // open: _1
  pixel pixel_403 (
    .izq(twelve[18]), .der(fourteen[18]), .Dir(in_4), .salida(thirteen[18]), .R(Reloj),
    .arriba(thirteen[17]), .en(en), .Rt(Teclado));  // open: _1
  pixel pixel_404 (
    .izq(twelve[19]), .der(fourteen[19]), .Dir(in_4), .salida(thirteen[19]), .R(Reloj),
    .arriba(thirteen[18]), .en(en), .Rt(Teclado));  // open: _1
  pixel pixel_405 (
    .izq(twelve[20]), .der(fourteen[20]), .Dir(in_4), .salida(thirteen[20]), .R(Reloj),
    .arriba(thirteen[19]), .en(en), .Rt(Teclado));  // open: _1
  pixel pixel_406 (
    .izq(twelve[21]), .der(fourteen[21]), .Dir(in_4), .salida(thirteen[21]), .R(Reloj),
    .arriba(thirteen[20]), .en(en), .Rt(Teclado));  // open: _1
  pixel pixel_407 (
    .izq(twelve[22]), .der(fourteen[22]), .Dir(in_4), .salida(thirteen[22]), .R(Reloj),
    .arriba(thirteen[21]), .en(en), .Rt(Teclado));  // open: _1
  pixel pixel_408 (
    .izq(twelve[23]), .der(fourteen[23]), .Dir(in_4), .salida(thirteen[23]), .R(Reloj),
    .arriba(thirteen[22]), .en(en), .Rt(Teclado));  // open: _1
  pixel pixel_409 (
    .izq(twelve[24]), .der(fourteen[24]), .Dir(in_4), .salida(thirteen[24]), .R(Reloj),
    .arriba(thirteen[23]), .en(en), .Rt(Teclado));  // open: _1
  pixel pixel_410 (
    .izq(twelve[25]), .der(fourteen[25]), .Dir(in_4), .salida(thirteen[25]), .R(Reloj),
    .arriba(thirteen[24]), .en(en), .Rt(Teclado));  // open: _1
  pixel pixel_411 (
    .izq(twelve[26]), .der(fourteen[26]), .Dir(in_4), .salida(thirteen[26]), .R(Reloj),
    .arriba(thirteen[25]), .en(en), .Rt(Teclado));  // open: _1
  pixel pixel_412 (
    .izq(twelve[27]), .der(fourteen[27]), .Dir(in_4), .salida(thirteen[27]), .R(Reloj),
    .arriba(thirteen[26]), .en(en), .Rt(Teclado));  // open: _1
  pixel pixel_413 (
    .izq(twelve[28]), .der(fourteen[28]), .Dir(in_4), .salida(thirteen[28]), .R(Reloj),
    .arriba(thirteen[27]), .en(en), .Rt(Teclado));  // open: _1
  pixel pixel_414 (
    .izq(twelve[29]), .der(fourteen[29]), .Dir(in_4), .salida(thirteen[29]), .R(Reloj),
    .arriba(thirteen[28]), .en(en), .Rt(Teclado));  // open: _1
  pixel pixel_415 (
    .izq(twelve[30]), .der(fourteen[30]), .Dir(in_4), .salida(thirteen[30]), .R(Reloj),
    .arriba(thirteen[29]), .en(en), .Rt(Teclado));  // open: _1
  pixel pixel_416 (
    .izq(twelve[31]), .der(fourteen[31]), .Dir(in_4), .salida(thirteen[31]), .R(Reloj),
    .arriba(thirteen[30]), .en(en), .Rt(Teclado));  // open: _1
  pixel pixel_417 (
    .izq(thirteen[0]), .der(fifteen[0]), .Dir(in_4), .salida(fourteen[0]), .R(Reloj), .arriba(fourteen[31]),
    ._1(undriven_23), .en(en), .Rt(Teclado));
  pixel pixel_418 (
    .izq(thirteen[1]), .der(fifteen[1]), .Dir(in_4), .salida(fourteen[1]), .R(Reloj), .arriba(fourteen[0]),
    ._1(undriven_24), .en(en), .Rt(Teclado));
  pixel pixel_419 (
    .izq(thirteen[2]), .der(fifteen[2]), .Dir(in_4), .salida(fourteen[2]), .R(Reloj), .arriba(fourteen[1]),
    .en(en), .Rt(Teclado));  // open: _1
  pixel pixel_420 (
    .izq(thirteen[3]), .der(fifteen[3]), .Dir(in_4), .salida(fourteen[3]), .R(Reloj), .arriba(fourteen[2]),
    .en(en), .Rt(Teclado));  // open: _1
  pixel pixel_421 (
    .izq(thirteen[4]), .der(fifteen[4]), .Dir(in_4), .salida(fourteen[4]), .R(Reloj), .arriba(fourteen[3]),
    .en(en), .Rt(Teclado));  // open: _1
  pixel pixel_422 (
    .izq(thirteen[5]), .der(fifteen[5]), .Dir(in_4), .salida(fourteen[5]), .R(Reloj), .arriba(fourteen[4]),
    .en(en), .Rt(Teclado));  // open: _1
  pixel pixel_423 (
    .izq(thirteen[6]), .der(fifteen[6]), .Dir(in_4), .salida(fourteen[6]), .R(Reloj), .arriba(fourteen[5]),
    .en(en), .Rt(Teclado));  // open: _1
  pixel pixel_424 (
    .izq(thirteen[7]), .der(fifteen[7]), .Dir(in_4), .salida(fourteen[7]), .R(Reloj), .arriba(fourteen[6]),
    .en(en), .Rt(Teclado));  // open: _1
  pixel pixel_425 (
    .izq(thirteen[8]), .der(fifteen[8]), .Dir(in_4), .salida(fourteen[8]), .R(Reloj), .arriba(fourteen[7]),
    .en(en), .Rt(Teclado));  // open: _1
  pixel pixel_426 (
    .izq(thirteen[9]), .der(fifteen[9]), .Dir(in_4), .salida(fourteen[9]), .R(Reloj), .arriba(fourteen[8]),
    .en(en), .Rt(Teclado));  // open: _1
  pixel pixel_427 (
    .izq(thirteen[10]), .der(fifteen[10]), .Dir(in_4), .salida(fourteen[10]), .R(Reloj),
    .arriba(fourteen[9]), .en(en), .Rt(Teclado));  // open: _1
  pixel pixel_428 (
    .izq(thirteen[11]), .der(fifteen[11]), .Dir(in_4), .salida(fourteen[11]), .R(Reloj),
    .arriba(fourteen[10]), .en(en), .Rt(Teclado));  // open: _1
  pixel pixel_429 (
    .izq(thirteen[12]), .der(fifteen[12]), .Dir(in_4), .salida(fourteen[12]), .R(Reloj),
    .arriba(fourteen[11]), .en(en), .Rt(Teclado));  // open: _1
  pixel pixel_430 (
    .izq(thirteen[13]), .der(fifteen[13]), .Dir(in_4), .salida(fourteen[13]), .R(Reloj),
    .arriba(fourteen[12]), .en(en), .Rt(Teclado));  // open: _1
  pixel pixel_431 (
    .izq(thirteen[14]), .der(fifteen[14]), .Dir(in_4), .salida(fourteen[14]), .R(Reloj),
    .arriba(fourteen[13]), .en(en), .Rt(Teclado));  // open: _1
  pixel pixel_432 (
    .izq(thirteen[15]), .der(fifteen[15]), .Dir(in_4), .salida(fourteen[15]), .R(Reloj),
    .arriba(fourteen[14]), .en(en), .Rt(Teclado));  // open: _1
  pixel pixel_433 (
    .izq(thirteen[16]), .der(fifteen[16]), .Dir(in_4), .salida(fourteen[16]), .R(Reloj),
    .arriba(fourteen[15]), .en(en), .Rt(Teclado));  // open: _1
  pixel pixel_434 (
    .izq(thirteen[17]), .der(fifteen[17]), .Dir(in_4), .salida(fourteen[17]), .R(Reloj),
    .arriba(fourteen[16]), .en(en), .Rt(Teclado));  // open: _1
  pixel pixel_435 (
    .izq(thirteen[18]), .der(fifteen[18]), .Dir(in_4), .salida(fourteen[18]), .R(Reloj),
    .arriba(fourteen[17]), .en(en), .Rt(Teclado));  // open: _1
  pixel pixel_436 (
    .izq(thirteen[19]), .der(fifteen[19]), .Dir(in_4), .salida(fourteen[19]), .R(Reloj),
    .arriba(fourteen[18]), .en(en), .Rt(Teclado));  // open: _1
  pixel pixel_437 (
    .izq(thirteen[20]), .der(fifteen[20]), .Dir(in_4), .salida(fourteen[20]), .R(Reloj),
    .arriba(fourteen[19]), .en(en), .Rt(Teclado));  // open: _1
  pixel pixel_438 (
    .izq(thirteen[21]), .der(fifteen[21]), .Dir(in_4), .salida(fourteen[21]), .R(Reloj),
    .arriba(fourteen[20]), .en(en), .Rt(Teclado));  // open: _1
  pixel pixel_439 (
    .izq(thirteen[22]), .der(fifteen[22]), .Dir(in_4), .salida(fourteen[22]), .R(Reloj),
    .arriba(fourteen[21]), .en(en), .Rt(Teclado));  // open: _1
  pixel pixel_440 (
    .izq(thirteen[23]), .der(fifteen[23]), .Dir(in_4), .salida(fourteen[23]), .R(Reloj),
    .arriba(fourteen[22]), .en(en), .Rt(Teclado));  // open: _1
  pixel pixel_441 (
    .izq(thirteen[24]), .der(fifteen[24]), .Dir(in_4), .salida(fourteen[24]), .R(Reloj),
    .arriba(fourteen[23]), .en(en), .Rt(Teclado));  // open: _1
  pixel pixel_442 (
    .izq(thirteen[25]), .der(fifteen[25]), .Dir(in_4), .salida(fourteen[25]), .R(Reloj),
    .arriba(fourteen[24]), .en(en), .Rt(Teclado));  // open: _1
  pixel pixel_443 (
    .izq(thirteen[26]), .der(fifteen[26]), .Dir(in_4), .salida(fourteen[26]), .R(Reloj),
    .arriba(fourteen[25]), .en(en), .Rt(Teclado));  // open: _1
  pixel pixel_444 (
    .izq(thirteen[27]), .der(fifteen[27]), .Dir(in_4), .salida(fourteen[27]), .R(Reloj),
    .arriba(fourteen[26]), .en(en), .Rt(Teclado));  // open: _1
  pixel pixel_445 (
    .izq(thirteen[28]), .der(fifteen[28]), .Dir(in_4), .salida(fourteen[28]), .R(Reloj),
    .arriba(fourteen[27]), .en(en), .Rt(Teclado));  // open: _1
  pixel pixel_446 (
    .izq(thirteen[29]), .der(fifteen[29]), .Dir(in_4), .salida(fourteen[29]), .R(Reloj),
    .arriba(fourteen[28]), .en(en), .Rt(Teclado));  // open: _1
  pixel pixel_447 (
    .izq(thirteen[30]), .der(fifteen[30]), .Dir(in_4), .salida(fourteen[30]), .R(Reloj),
    .arriba(fourteen[29]), .en(en), .Rt(Teclado));  // open: _1
  pixel pixel_448 (
    .izq(thirteen[31]), .der(fifteen[31]), .Dir(in_4), .salida(fourteen[31]), .R(Reloj),
    .arriba(fourteen[30]), .en(en), .Rt(Teclado));  // open: _1
  pixel pixel_449 (
    .izq(fourteen[0]), .der(sixteen[0]), .Dir(in_4), .salida(fifteen[0]), .R(Reloj), .arriba(fifteen[31]),
    ._1(undriven_25), .en(en), .Rt(Teclado));
  pixel pixel_450 (
    .izq(fourteen[1]), .der(sixteen[1]), .Dir(in_4), .salida(fifteen[1]), .R(Reloj), .arriba(fifteen[0]),
    ._1(undriven_26), .en(en), .Rt(Teclado));
  pixel pixel_451 (
    .izq(fourteen[2]), .der(sixteen[2]), .Dir(in_4), .salida(fifteen[2]), .R(Reloj), .arriba(fifteen[1]),
    .en(en), .Rt(Teclado));  // open: _1
  pixel pixel_452 (
    .izq(fourteen[3]), .der(sixteen[3]), .Dir(in_4), .salida(fifteen[3]), .R(Reloj), .arriba(fifteen[2]),
    .en(en), .Rt(Teclado));  // open: _1
  pixel pixel_453 (
    .izq(fourteen[4]), .der(sixteen[4]), .Dir(in_4), .salida(fifteen[4]), .R(Reloj), .arriba(fifteen[3]),
    .en(en), .Rt(Teclado));  // open: _1
  pixel pixel_454 (
    .izq(fourteen[5]), .der(sixteen[5]), .Dir(in_4), .salida(fifteen[5]), .R(Reloj), .arriba(fifteen[4]),
    .en(en), .Rt(Teclado));  // open: _1
  pixel pixel_455 (
    .izq(fourteen[6]), .der(sixteen[6]), .Dir(in_4), .salida(fifteen[6]), .R(Reloj), .arriba(fifteen[5]),
    .en(en), .Rt(Teclado));  // open: _1
  pixel pixel_456 (
    .izq(fourteen[7]), .der(sixteen[7]), .Dir(in_4), .salida(fifteen[7]), .R(Reloj), .arriba(fifteen[6]),
    .en(en), .Rt(Teclado));  // open: _1
  pixel pixel_457 (
    .izq(fourteen[8]), .der(sixteen[8]), .Dir(in_4), .salida(fifteen[8]), .R(Reloj), .arriba(fifteen[7]),
    .en(en), .Rt(Teclado));  // open: _1
  pixel pixel_458 (
    .izq(fourteen[9]), .der(sixteen[9]), .Dir(in_4), .salida(fifteen[9]), .R(Reloj), .arriba(fifteen[8]),
    .en(en), .Rt(Teclado));  // open: _1
  pixel pixel_459 (
    .izq(fourteen[10]), .der(sixteen[10]), .Dir(in_4), .salida(fifteen[10]), .R(Reloj), .arriba(fifteen[9]),
    .en(en), .Rt(Teclado));  // open: _1
  pixel pixel_460 (
    .izq(fourteen[11]), .der(sixteen[11]), .Dir(in_4), .salida(fifteen[11]), .R(Reloj), .arriba(fifteen[10]),
    .en(en), .Rt(Teclado));  // open: _1
  pixel pixel_461 (
    .izq(fourteen[12]), .der(sixteen[12]), .Dir(in_4), .salida(fifteen[12]), .R(Reloj), .arriba(fifteen[11]),
    .en(en), .Rt(Teclado));  // open: _1
  pixel pixel_462 (
    .izq(fourteen[13]), .der(sixteen[13]), .Dir(in_4), .salida(fifteen[13]), .R(Reloj), .arriba(fifteen[12]),
    .en(en), .Rt(Teclado));  // open: _1
  pixel pixel_463 (
    .izq(fourteen[14]), .der(sixteen[14]), .Dir(in_4), .salida(fifteen[14]), .R(Reloj), .arriba(fifteen[13]),
    .en(en), .Rt(Teclado));  // open: _1
  pixel pixel_464 (
    .izq(fourteen[15]), .der(sixteen[15]), .Dir(in_4), .salida(fifteen[15]), .R(Reloj), .arriba(fifteen[14]),
    .en(en), .Rt(Teclado));  // open: _1
  pixel pixel_465 (
    .izq(fourteen[16]), .der(sixteen[16]), .Dir(in_4), .salida(fifteen[16]), .R(Reloj), .arriba(fifteen[15]),
    .en(en), .Rt(Teclado));  // open: _1
  pixel pixel_466 (
    .izq(fourteen[17]), .der(sixteen[17]), .Dir(in_4), .salida(fifteen[17]), .R(Reloj), .arriba(fifteen[16]),
    .en(en), .Rt(Teclado));  // open: _1
  pixel pixel_467 (
    .izq(fourteen[18]), .der(sixteen[18]), .Dir(in_4), .salida(fifteen[18]), .R(Reloj), .arriba(fifteen[17]),
    .en(en), .Rt(Teclado));  // open: _1
  pixel pixel_468 (
    .izq(fourteen[19]), .der(sixteen[19]), .Dir(in_4), .salida(fifteen[19]), .R(Reloj), .arriba(fifteen[18]),
    .en(en), .Rt(Teclado));  // open: _1
  pixel pixel_469 (
    .izq(fourteen[20]), .der(sixteen[20]), .Dir(in_4), .salida(fifteen[20]), .R(Reloj), .arriba(fifteen[19]),
    .en(en), .Rt(Teclado));  // open: _1
  pixel pixel_470 (
    .izq(fourteen[21]), .der(sixteen[21]), .Dir(in_4), .salida(fifteen[21]), .R(Reloj), .arriba(fifteen[20]),
    .en(en), .Rt(Teclado));  // open: _1
  pixel pixel_471 (
    .izq(fourteen[22]), .der(sixteen[22]), .Dir(in_4), .salida(fifteen[22]), .R(Reloj), .arriba(fifteen[21]),
    .en(en), .Rt(Teclado));  // open: _1
  pixel pixel_472 (
    .izq(fourteen[23]), .der(sixteen[23]), .Dir(in_4), .salida(fifteen[23]), .R(Reloj), .arriba(fifteen[22]),
    .en(en), .Rt(Teclado));  // open: _1
  pixel pixel_473 (
    .izq(fourteen[24]), .der(sixteen[24]), .Dir(in_4), .salida(fifteen[24]), .R(Reloj), .arriba(fifteen[23]),
    .en(en), .Rt(Teclado));  // open: _1
  pixel pixel_474 (
    .izq(fourteen[25]), .der(sixteen[25]), .Dir(in_4), .salida(fifteen[25]), .R(Reloj), .arriba(fifteen[24]),
    .en(en), .Rt(Teclado));  // open: _1
  pixel pixel_475 (
    .izq(fourteen[26]), .der(sixteen[26]), .Dir(in_4), .salida(fifteen[26]), .R(Reloj), .arriba(fifteen[25]),
    .en(en), .Rt(Teclado));  // open: _1
  pixel pixel_476 (
    .izq(fourteen[27]), .der(sixteen[27]), .Dir(in_4), .salida(fifteen[27]), .R(Reloj), .arriba(fifteen[26]),
    .en(en), .Rt(Teclado));  // open: _1
  pixel pixel_477 (
    .izq(fourteen[28]), .der(sixteen[28]), .Dir(in_4), .salida(fifteen[28]), .R(Reloj), .arriba(fifteen[27]),
    .en(en), .Rt(Teclado));  // open: _1
  pixel pixel_478 (
    .izq(fourteen[29]), .der(sixteen[29]), .Dir(in_4), .salida(fifteen[29]), .R(Reloj), .arriba(fifteen[28]),
    .en(en), .Rt(Teclado));  // open: _1
  pixel pixel_479 (
    .izq(fourteen[30]), .der(sixteen[30]), .Dir(in_4), .salida(fifteen[30]), .R(Reloj), .arriba(fifteen[29]),
    .en(en), .Rt(Teclado));  // open: _1
  pixel pixel_480 (
    .izq(fourteen[31]), .der(sixteen[31]), .Dir(in_4), .salida(fifteen[31]), .R(Reloj), .arriba(fifteen[30]),
    .en(en), .Rt(Teclado));  // open: _1
  pixel pixel_481 (
    .izq(fifteen[0]), .der(one[0]), .Dir(in_4), .salida(sixteen[0]), .R(Reloj), .arriba(sixteen[31]),
    ._1(undriven_27), .en(en), .Rt(Teclado));
  pixel pixel_482 (
    .izq(fifteen[1]), .der(one[1]), .Dir(in_4), .salida(sixteen[1]), .R(Reloj), .arriba(sixteen[0]),
    ._1(undriven_28), .en(en), .Rt(Teclado));
  pixel pixel_483 (
    .izq(fifteen[2]), .der(one[2]), .Dir(in_4), .salida(sixteen[2]), .R(Reloj), .arriba(sixteen[1]), .en(en),
    .Rt(Teclado));  // open: _1
  pixel pixel_484 (
    .izq(fifteen[3]), .der(one[3]), .Dir(in_4), .salida(sixteen[3]), .R(Reloj), .arriba(sixteen[2]), .en(en),
    .Rt(Teclado));  // open: _1
  pixel pixel_485 (
    .izq(fifteen[4]), .der(one[4]), .Dir(in_4), .salida(sixteen[4]), .R(Reloj), .arriba(sixteen[3]), .en(en),
    .Rt(Teclado));  // open: _1
  pixel pixel_486 (
    .izq(fifteen[5]), .der(one[5]), .Dir(in_4), .salida(sixteen[5]), .R(Reloj), .arriba(sixteen[4]), .en(en),
    .Rt(Teclado));  // open: _1
  pixel pixel_487 (
    .izq(fifteen[6]), .der(one[6]), .Dir(in_4), .salida(sixteen[6]), .R(Reloj), .arriba(sixteen[5]), .en(en),
    .Rt(Teclado));  // open: _1
  pixel pixel_488 (
    .izq(fifteen[7]), .der(one[7]), .Dir(in_4), .salida(sixteen[7]), .R(Reloj), .arriba(sixteen[6]), .en(en),
    .Rt(Teclado));  // open: _1
  pixel pixel_489 (
    .izq(fifteen[8]), .der(one[8]), .Dir(in_4), .salida(sixteen[8]), .R(Reloj), .arriba(sixteen[7]), .en(en),
    .Rt(Teclado));  // open: _1
  pixel pixel_490 (
    .izq(fifteen[9]), .der(one[9]), .Dir(in_4), .salida(sixteen[9]), .R(Reloj), .arriba(sixteen[8]), .en(en),
    .Rt(Teclado));  // open: _1
  pixel pixel_491 (
    .izq(fifteen[10]), .der(one[10]), .Dir(in_4), .salida(sixteen[10]), .R(Reloj), .arriba(sixteen[9]),
    .en(en), .Rt(Teclado));  // open: _1
  pixel pixel_492 (
    .izq(fifteen[11]), .der(one[11]), .Dir(in_4), .salida(sixteen[11]), .R(Reloj), .arriba(sixteen[10]),
    .en(en), .Rt(Teclado));  // open: _1
  pixel pixel_493 (
    .izq(fifteen[12]), .der(one[12]), .Dir(in_4), .salida(sixteen[12]), .R(Reloj), .arriba(sixteen[11]),
    .en(en), .Rt(Teclado));  // open: _1
  pixel pixel_494 (
    .izq(fifteen[13]), .der(one[13]), .Dir(in_4), .salida(sixteen[13]), .R(Reloj), .arriba(sixteen[12]),
    .en(en), .Rt(Teclado));  // open: _1
  pixel pixel_495 (
    .izq(fifteen[14]), .der(one[14]), .Dir(in_4), .salida(sixteen[14]), .R(Reloj), .arriba(sixteen[13]),
    .en(en), .Rt(Teclado));  // open: _1
  pixel pixel_496 (
    .izq(fifteen[15]), .der(one[15]), .Dir(in_4), .salida(sixteen[15]), .R(Reloj), .arriba(sixteen[14]),
    .en(en), .Rt(Teclado));  // open: _1
  pixel pixel_497 (
    .izq(fifteen[16]), .der(one[16]), .Dir(in_4), .salida(sixteen[16]), .R(Reloj), .arriba(sixteen[15]),
    .en(en), .Rt(Teclado));  // open: _1
  DotMatrix #(.matrixcols(16), .matrixrows(32)) dotmatrix_1 (
    .col0(one), .col1(two), .col2(three), .col3(four), .col4(five), .col5(six), .col6(seven), .col7(eight),
    .col8(nine), .col9(ten), .col10(eleven), .col11(twelve), .col12(thirteen), .col13(fourteen),
    .col14(fifteen), .col15(sixteen));
  pixel pixel_498 (
    .izq(fifteen[17]), .der(one[17]), .Dir(in_4), .salida(sixteen[17]), .R(Reloj), .arriba(sixteen[16]),
    .en(en), .Rt(Teclado));  // open: _1
  pixel pixel_499 (
    .izq(fifteen[18]), .der(one[18]), .Dir(in_4), .salida(sixteen[18]), .R(Reloj), .arriba(sixteen[17]),
    .en(en), .Rt(Teclado));  // open: _1
  pixel pixel_500 (
    .izq(fifteen[19]), .der(one[19]), .Dir(in_4), .salida(sixteen[19]), .R(Reloj), .arriba(sixteen[18]),
    .en(en), .Rt(Teclado));  // open: _1
  pixel pixel_501 (
    .izq(fifteen[20]), .der(one[20]), .Dir(in_4), .salida(sixteen[20]), .R(Reloj), .arriba(sixteen[19]),
    .en(en), .Rt(Teclado));  // open: _1
  pixel pixel_502 (
    .izq(fifteen[21]), .der(one[21]), .Dir(in_4), .salida(sixteen[21]), .R(Reloj), .arriba(sixteen[20]),
    .en(en), .Rt(Teclado));  // open: _1
  pixel pixel_503 (
    .izq(fifteen[22]), .der(one[22]), .Dir(in_4), .salida(sixteen[22]), .R(Reloj), .arriba(sixteen[21]),
    .en(en), .Rt(Teclado));  // open: _1
  pixel pixel_504 (
    .izq(fifteen[23]), .der(one[23]), .Dir(in_4), .salida(sixteen[23]), .R(Reloj), .arriba(sixteen[22]),
    .en(en), .Rt(Teclado));  // open: _1
  pixel pixel_505 (
    .izq(fifteen[24]), .der(one[24]), .Dir(in_4), .salida(sixteen[24]), .R(Reloj), .arriba(sixteen[23]),
    .en(en), .Rt(Teclado));  // open: _1
  pixel pixel_506 (
    .izq(fifteen[25]), .der(one[25]), .Dir(in_4), .salida(sixteen[25]), .R(Reloj), .arriba(sixteen[24]),
    .en(en), .Rt(Teclado));  // open: _1
  pixel pixel_507 (
    .izq(fifteen[26]), .der(one[26]), .Dir(in_4), .salida(sixteen[26]), .R(Reloj), .arriba(sixteen[25]),
    .en(en), .Rt(Teclado));  // open: _1
  pixel pixel_508 (
    .izq(fifteen[27]), .der(one[27]), .Dir(in_4), .salida(sixteen[27]), .R(Reloj), .arriba(sixteen[26]),
    .en(en), .Rt(Teclado));  // open: _1
  pixel pixel_509 (
    .izq(fifteen[28]), .der(one[28]), .Dir(in_4), .salida(sixteen[28]), .R(Reloj), .arriba(sixteen[27]),
    .en(en), .Rt(Teclado));  // open: _1
  pixel pixel_510 (
    .izq(fifteen[29]), .der(one[29]), .Dir(in_4), .salida(sixteen[29]), .R(Reloj), .arriba(sixteen[28]),
    .en(en), .Rt(Teclado));  // open: _1
  pixel pixel_511 (
    .izq(fifteen[30]), .der(one[30]), .Dir(in_4), .salida(sixteen[30]), .R(Reloj), .arriba(sixteen[29]),
    .en(en), .Rt(Teclado));  // open: _1
  pixel pixel_512 (
    .izq(fifteen[31]), .der(one[31]), .Dir(in_4), .salida(sixteen[31]), .R(Reloj), .arriba(sixteen[30]),
    .en(en), .Rt(Teclado));  // open: _1

  // Other names for the same wires on the sheet: _1[31:0] = one; _1_1 = one[0]; _2_1 = one[1]; _3_1 = one[2];
  //   _4_1 = one[3]; _5_1 = one[4]; _6_1 = one[5]; _7_1 = one[6]; _8_1 = one[7]; _9_1 = one[8]; _10_1 = one[9];
  //   _11_1 = one[10]; _12_1 = one[11]; _13_1 = one[12]; _14_1 = one[13]; _15_1 = one[14]; _16_1 = one[15];
  //   _17_1 = one[16]; _18_1 = one[17]; _19_1 = one[18]; _20_1 = one[19]; _21_1 = one[20]; _22_1 = one[21];
  //   _23_1 = one[22]; _24_1 = one[23]; _25_1 = one[24]; _26_1 = one[25]; _27_1 = one[26]; _28_1 = one[27];
  //   _29_1 = one[28]; _30_1 = one[29]; _31_1 = one[30]; _32_1 = one[31]; _1_2 = two[0]; _2[31:0] = two;
  //   _2_2 = two[1]; _3_2 = two[2]; _4_2 = two[3]; _5_2 = two[4]; _6_2 = two[5]; _7_2 = two[6]; _8_2 = two[7];
  //   _9_2 = two[8]; _10_2 = two[9]; _11_2 = two[10]; _12_2 = two[11]; _13_2 = two[12]; _14_2 = two[13];
  //   _15_2 = two[14]; _16_2 = two[15]; _17_2 = two[16]; _18_2 = two[17]; _19_2 = two[18]; _20_2 = two[19];
  //   _21_2 = two[20]; _22_2 = two[21]; _23_2 = two[22]; _24_2 = two[23]; _25_2 = two[24]; _26_2 = two[25];
  //   _27_2 = two[26]; _28_2 = two[27]; _29_2 = two[28]; _30_2 = two[29]; _31_2 = two[30]; _32_2 = two[31];
  //   _1_3 = three[0]; _3[31:0] = three; _2_3 = three[1]; _3_3 = three[2]; _4_3 = three[3]; _5_3 = three[4];
  //   _6_3 = three[5]; _7_3 = three[6]; _8_3 = three[7]; _9_3 = three[8]; _10_3 = three[9]; _11_3 = three[10];
  //   _12_3 = three[11]; _13_3 = three[12]; _14_3 = three[13]; _15_3 = three[14]; _16_3 = three[15];
  //   _17_3 = three[16]; _18_3 = three[17]; _19_3 = three[18]; _20_3 = three[19]; _21_3 = three[20];
  //   _22_3 = three[21]; _23_3 = three[22]; _24_3 = three[23]; _25_3 = three[24]; _26_3 = three[25];
  //   _27_3 = three[26]; _28_3 = three[27]; _29_3 = three[28]; _30_3 = three[29]; _31_3 = three[30];
  //   _32_3 = three[31]; _1_4 = four[0]; _4[31:0] = four; _2_4 = four[1]; _3_4 = four[2]; _4_4 = four[3];
  //   _5_4 = four[4]; _6_4 = four[5]; _7_4 = four[6]; _8_4 = four[7]; _9_4 = four[8]; _10_4 = four[9];
  //   _11_4 = four[10]; _12_4 = four[11]; _13_4 = four[12]; _14_4 = four[13]; _15_4 = four[14]; _16_4 = four[15];
  //   _17_4 = four[16]; _18_4 = four[17]; _19_4 = four[18]; _20_4 = four[19]; _21_4 = four[20]; _22_4 = four[21];
  //   _23_4 = four[22]; _24_4 = four[23]; _25_4 = four[24]; _26_4 = four[25]; _27_4 = four[26]; _28_4 = four[27];
  //   _29_4 = four[28]; _30_4 = four[29]; _31_4 = four[30]; _32_4 = four[31]; _1_5 = five[0]; _5[31:0] = five;
  //   _2_5 = five[1]; _3_5 = five[2]; _4_5 = five[3]; _5_5 = five[4]; _6_5 = five[5]; _7_5 = five[6]; _8_5 = five[7];
  //   _9_5 = five[8]; _10_5 = five[9]; _11_5 = five[10]; _12_5 = five[11]; _13_5 = five[12]; _14_5 = five[13];
  //   _15_5 = five[14]; _16_5 = five[15]; _17_5 = five[16]; _18_5 = five[17]; _19_5 = five[18]; _20_5 = five[19];
  //   _21_5 = five[20]; _22_5 = five[21]; _23_5 = five[22]; _24_5 = five[23]; _25_5 = five[24]; _26_5 = five[25];
  //   _27_5 = five[26]; _28_5 = five[27]; _29_5 = five[28]; _30_5 = five[29]; _31_5 = five[30]; _32_5 = five[31];
  //   _1_6 = six[0]; _6[31:0] = six; _2_6 = six[1]; _3_6 = six[2]; _4_6 = six[3]; _5_6 = six[4]; _6_6 = six[5];
  //   _7_6 = six[6]; _8_6 = six[7]; _9_6 = six[8]; _10_6 = six[9]; _11_6 = six[10]; _12_6 = six[11]; _13_6 = six[12];
  //   _14_6 = six[13]; _15_6 = six[14]; _16_6 = six[15]; _17_6 = six[16]; _18_6 = six[17]; _19_6 = six[18];
  //   _20_6 = six[19]; _21_6 = six[20]; _22_6 = six[21]; _23_6 = six[22]; _24_6 = six[23]; _25_6 = six[24];
  //   _26_6 = six[25]; _27_6 = six[26]; _28_6 = six[27]; _29_6 = six[28]; _30_6 = six[29]; _31_6 = six[30];
  //   _32_6 = six[31]; _1_7 = seven[0]; _7[31:0] = seven; _2_7 = seven[1]; _3_7 = seven[2]; _4_7 = seven[3];
  //   _5_7 = seven[4]; _6_7 = seven[5]; _7_7 = seven[6]; _8_7 = seven[7]; _9_7 = seven[8]; _10_7 = seven[9];
  //   _11_7 = seven[10]; _12_7 = seven[11]; _13_7 = seven[12]; _14_7 = seven[13]; _15_7 = seven[14];
  //   _16_7 = seven[15]; _17_7 = seven[16]; _18_7 = seven[17]; _19_7 = seven[18]; _20_7 = seven[19];
  //   _21_7 = seven[20]; _22_7 = seven[21]; _23_7 = seven[22]; _24_7 = seven[23]; _25_7 = seven[24];
  //   _26_7 = seven[25]; _27_7 = seven[26]; _28_7 = seven[27]; _29_7 = seven[28]; _30_7 = seven[29];
  //   _31_7 = seven[30]; _32_7 = seven[31]; _1_8 = eight[0]; _8[31:0] = eight; _2_8 = eight[1]; _3_8 = eight[2];
  //   _4_8 = eight[3]; _5_8 = eight[4]; _6_8 = eight[5]; _7_8 = eight[6]; _8_8 = eight[7]; _9_8 = eight[8];
  //   _10_8 = eight[9]; _11_8 = eight[10]; _12_8 = eight[11]; _13_8 = eight[12]; _14_8 = eight[13]; _15_8 = eight[14];
  //   _16_8 = eight[15]; _17_8 = eight[16]; _18_8 = eight[17]; _19_8 = eight[18]; _20_8 = eight[19];
  //   _21_8 = eight[20]; _22_8 = eight[21]; _23_8 = eight[22]; _24_8 = eight[23]; _25_8 = eight[24];
  //   _26_8 = eight[25]; _27_8 = eight[26]; _28_8 = eight[27]; _29_8 = eight[28]; _30_8 = eight[29];
  //   _31_8 = eight[30]; _32_8 = eight[31]; _1_9 = nine[0]; _9[31:0] = nine; _2_9 = nine[1]; _3_9 = nine[2];
  //   _4_9 = nine[3]; _5_9 = nine[4]; _6_9 = nine[5]; _7_9 = nine[6]; _8_9 = nine[7]; _9_9 = nine[8]; _10_9 = nine[9];
  //   _11_9 = nine[10]; _12_9 = nine[11]; _13_9 = nine[12]; _14_9 = nine[13]; _15_9 = nine[14]; _16_9 = nine[15];
  //   _17_9 = nine[16]; _18_9 = nine[17]; _19_9 = nine[18]; _20_9 = nine[19]; _21_9 = nine[20]; _22_9 = nine[21];
  //   _23_9 = nine[22]; _24_9 = nine[23]; _25_9 = nine[24]; _26_9 = nine[25]; _27_9 = nine[26]; _28_9 = nine[27];
  //   _29_9 = nine[28]; _30_9 = nine[29]; _31_9 = nine[30]; _32_9 = nine[31]; _1_10 = ten[0]; _10[31:0] = ten;
  //   _2_10 = ten[1]; _3_10 = ten[2]; _4_10 = ten[3]; _5_10 = ten[4]; _6_10 = ten[5]; _7_10 = ten[6]; _8_10 = ten[7];
  //   _9_10 = ten[8]; _10_10 = ten[9]; _11_10 = ten[10]; _12_10 = ten[11]; _13_10 = ten[12]; _14_10 = ten[13];
  //   _15_10 = ten[14]; _16_10 = ten[15]; _17_10 = ten[16]; _18_10 = ten[17]; _19_10 = ten[18]; _20_10 = ten[19];
  //   _21_10 = ten[20]; _22_10 = ten[21]; _23_10 = ten[22]; _24_10 = ten[23]; _25_10 = ten[24]; _26_10 = ten[25];
  //   _27_10 = ten[26]; _28_10 = ten[27]; _29_10 = ten[28]; _30_10 = ten[29]; _31_10 = ten[30]; _32_10 = ten[31];
  //   _1_11 = eleven[0]; _11[31:0] = eleven; _2_11 = eleven[1]; _3_11 = eleven[2]; _4_11 = eleven[3];
  //   _5_11 = eleven[4]; _6_11 = eleven[5]; _7_11 = eleven[6]; _8_11 = eleven[7]; _9_11 = eleven[8];
  //   _10_11 = eleven[9]; _11_11 = eleven[10]; _12_11 = eleven[11]; _13_11 = eleven[12]; _14_11 = eleven[13];
  //   _15_11 = eleven[14]; _16_11 = eleven[15]; _17_11 = eleven[16]; _18_11 = eleven[17]; _19_11 = eleven[18];
  //   _20_11 = eleven[19]; _21_11 = eleven[20]; _22_11 = eleven[21]; _23_11 = eleven[22]; _24_11 = eleven[23];
  //   _25_11 = eleven[24]; _26_11 = eleven[25]; _27_11 = eleven[26]; _28_11 = eleven[27]; _29_11 = eleven[28];
  //   _30_11 = eleven[29]; _31_11 = eleven[30]; _32_11 = eleven[31]; _1_12 = twelve[0]; _12[31:0] = twelve;
  //   _2_12 = twelve[1]; _3_12 = twelve[2]; _4_12 = twelve[3]; _5_12 = twelve[4]; _6_12 = twelve[5];
  //   _7_12 = twelve[6]; _8_12 = twelve[7]; _9_12 = twelve[8]; _10_12 = twelve[9]; _11_12 = twelve[10];
  //   _12_12 = twelve[11]; _13_12 = twelve[12]; _14_12 = twelve[13]; _15_12 = twelve[14]; _16_12 = twelve[15];
  //   _17_12 = twelve[16]; _18_12 = twelve[17]; _19_12 = twelve[18]; _20_12 = twelve[19]; _21_12 = twelve[20];
  //   _22_12 = twelve[21]; _23_12 = twelve[22]; _24_12 = twelve[23]; _25_12 = twelve[24]; _26_12 = twelve[25];
  //   _27_12 = twelve[26]; _28_12 = twelve[27]; _29_12 = twelve[28]; _30_12 = twelve[29]; _31_12 = twelve[30];
  //   _32_12 = twelve[31]; _1_13 = thirteen[0]; _13[31:0] = thirteen; _2_13 = thirteen[1]; _3_13 = thirteen[2];
  //   _4_13 = thirteen[3]; _5_13 = thirteen[4]; _6_13 = thirteen[5]; _7_13 = thirteen[6]; _8_13 = thirteen[7];
  //   _9_13 = thirteen[8]; _10_13 = thirteen[9]; _11_13 = thirteen[10]; _12_13 = thirteen[11]; _13_13 = thirteen[12];
  //   _14_13 = thirteen[13]; _15_13 = thirteen[14]; _16_13 = thirteen[15]; _17_13 = thirteen[16];
  //   _18_13 = thirteen[17]; _19_13 = thirteen[18]; _20_13 = thirteen[19]; _21_13 = thirteen[20];
  //   _22_13 = thirteen[21]; _23_13 = thirteen[22]; _24_13 = thirteen[23]; _25_13 = thirteen[24];
  //   _26_13 = thirteen[25]; _27_13 = thirteen[26]; _28_13 = thirteen[27]; _29_13 = thirteen[28];
  //   _30_13 = thirteen[29]; _31_13 = thirteen[30]; _32_13 = thirteen[31]; _1_14 = fourteen[0]; _14[31:0] = fourteen;
  //   _2_14 = fourteen[1]; _3_14 = fourteen[2]; _4_14 = fourteen[3]; _5_14 = fourteen[4]; _6_14 = fourteen[5];
  //   _7_14 = fourteen[6]; _8_14 = fourteen[7]; _9_14 = fourteen[8]; _10_14 = fourteen[9]; _11_14 = fourteen[10];
  //   _12_14 = fourteen[11]; _13_14 = fourteen[12]; _14_14 = fourteen[13]; _15_14 = fourteen[14];
  //   _16_14 = fourteen[15]; _17_14 = fourteen[16]; _18_14 = fourteen[17]; _19_14 = fourteen[18];
  //   _20_14 = fourteen[19]; _21_14 = fourteen[20]; _22_14 = fourteen[21]; _23_14 = fourteen[22];
  //   _24_14 = fourteen[23]; _25_14 = fourteen[24]; _26_14 = fourteen[25]; _27_14 = fourteen[26];
  //   _28_14 = fourteen[27]; _29_14 = fourteen[28]; _30_14 = fourteen[29]; _31_14 = fourteen[30];
  //   _32_14 = fourteen[31]; _1_15 = fifteen[0]; _15[31:0] = fifteen; _2_15 = fifteen[1]; _3_15 = fifteen[2];
  //   _4_15 = fifteen[3]; _5_15 = fifteen[4]; _6_15 = fifteen[5]; _7_15 = fifteen[6]; _8_15 = fifteen[7];
  //   _9_15 = fifteen[8]; _10_15 = fifteen[9]; _11_15 = fifteen[10]; _12_15 = fifteen[11]; _13_15 = fifteen[12];
  //   _14_15 = fifteen[13]; _15_15 = fifteen[14]; _16_15 = fifteen[15]; _17_15 = fifteen[16]; _18_15 = fifteen[17];
  //   _19_15 = fifteen[18]; _20_15 = fifteen[19]; _21_15 = fifteen[20]; _22_15 = fifteen[21]; _23_15 = fifteen[22];
  //   _24_15 = fifteen[23]; _25_15 = fifteen[24]; _26_15 = fifteen[25]; _27_15 = fifteen[26]; _28_15 = fifteen[27];
  //   _29_15 = fifteen[28]; _30_15 = fifteen[29]; _31_15 = fifteen[30]; _32_15 = fifteen[31]; _1_16 = sixteen[0];
  //   _16[31:0] = sixteen; _2_16 = sixteen[1]; _3_16 = sixteen[2]; _4_16 = sixteen[3]; _5_16 = sixteen[4];
  //   _6_16 = sixteen[5]; _7_16 = sixteen[6]; _8_16 = sixteen[7]; _9_16 = sixteen[8]; _10_16 = sixteen[9];
  //   _11_16 = sixteen[10]; _12_16 = sixteen[11]; _13_16 = sixteen[12]; _14_16 = sixteen[13]; _15_16 = sixteen[14];
  //   _16_16 = sixteen[15]; _17_16 = sixteen[16]; _18_16 = sixteen[17]; _19_16 = sixteen[18]; _20_16 = sixteen[19];
  //   _21_16 = sixteen[20]; _22_16 = sixteen[21]; _23_16 = sixteen[22]; _24_16 = sixteen[23]; _25_16 = sixteen[24];
  //   _26_16 = sixteen[25]; _27_16 = sixteen[26]; _28_16 = sixteen[27]; _29_16 = sixteen[28]; _30_16 = sixteen[29];
  //   _31_16 = sixteen[30]; _32_16 = sixteen[31]; a = in_5; Dir[1:0] = in_4; R = Reloj; T = Teclado
endmodule

module pixelbar (
  input  CLK,
  input  ENTRADA,
  input  Reset,
  output SALIDA
);

  wire or_1_out;

  or or_1 (or_1_out, SALIDA, ENTRADA);
  D_Flip_Flop d_ff_1 (.clk(CLK), .D(or_1_out), .Q(SALIDA), .reset(Reset));  // open: Qn, preset, en
endmodule

module columna (
  input  in_1,
  input  [31:0] \input ,
  input  clk,
  output [31:0] out_4
);

  pixelbar pixelbar (.CLK(clk), .ENTRADA(\input [0]), .Reset(in_1), .SALIDA(out_4[0]));
  pixelbar pixelbar_2 (.CLK(clk), .ENTRADA(\input [1]), .Reset(in_1), .SALIDA(out_4[1]));
  pixelbar pixelbar_3 (.CLK(clk), .ENTRADA(\input [2]), .Reset(in_1), .SALIDA(out_4[2]));
  pixelbar pixelbar_4 (.CLK(clk), .ENTRADA(\input [3]), .Reset(in_1), .SALIDA(out_4[3]));
  pixelbar pixelbar_5 (.CLK(clk), .ENTRADA(\input [4]), .Reset(in_1), .SALIDA(out_4[4]));
  pixelbar pixelbar_6 (.CLK(clk), .ENTRADA(\input [5]), .Reset(in_1), .SALIDA(out_4[5]));
  pixelbar pixelbar_7 (.CLK(clk), .ENTRADA(\input [6]), .Reset(in_1), .SALIDA(out_4[6]));
  pixelbar pixelbar_8 (.CLK(clk), .ENTRADA(\input [7]), .Reset(in_1), .SALIDA(out_4[7]));
  pixelbar pixelbar_9 (.CLK(clk), .ENTRADA(\input [8]), .Reset(in_1), .SALIDA(out_4[8]));
  pixelbar pixelbar_10 (.CLK(clk), .ENTRADA(\input [9]), .Reset(in_1), .SALIDA(out_4[9]));
  pixelbar pixelbar_11 (.CLK(clk), .ENTRADA(\input [10]), .Reset(in_1), .SALIDA(out_4[10]));
  pixelbar pixelbar_12 (.CLK(clk), .ENTRADA(\input [11]), .Reset(in_1), .SALIDA(out_4[11]));
  pixelbar pixelbar_13 (.CLK(clk), .ENTRADA(\input [12]), .Reset(in_1), .SALIDA(out_4[12]));
  pixelbar pixelbar_14 (.CLK(clk), .ENTRADA(\input [13]), .Reset(in_1), .SALIDA(out_4[13]));
  pixelbar pixelbar_15 (.CLK(clk), .ENTRADA(\input [14]), .Reset(in_1), .SALIDA(out_4[14]));
  pixelbar pixelbar_16 (.CLK(clk), .ENTRADA(\input [15]), .Reset(in_1), .SALIDA(out_4[15]));
  pixelbar pixelbar_17 (.CLK(clk), .ENTRADA(\input [16]), .Reset(in_1), .SALIDA(out_4[16]));
  pixelbar pixelbar_18 (.CLK(clk), .ENTRADA(\input [17]), .Reset(in_1), .SALIDA(out_4[17]));
  pixelbar pixelbar_19 (.CLK(clk), .ENTRADA(\input [18]), .Reset(in_1), .SALIDA(out_4[18]));
  pixelbar pixelbar_20 (.CLK(clk), .ENTRADA(\input [19]), .Reset(in_1), .SALIDA(out_4[19]));
  pixelbar pixelbar_21 (.CLK(clk), .ENTRADA(\input [20]), .Reset(in_1), .SALIDA(out_4[20]));
  pixelbar pixelbar_22 (.CLK(clk), .ENTRADA(\input [21]), .Reset(in_1), .SALIDA(out_4[21]));
  pixelbar pixelbar_23 (.CLK(clk), .ENTRADA(\input [22]), .Reset(in_1), .SALIDA(out_4[22]));
  pixelbar pixelbar_24 (.CLK(clk), .ENTRADA(\input [23]), .Reset(in_1), .SALIDA(out_4[23]));
  pixelbar pixelbar_25 (.CLK(clk), .ENTRADA(\input [24]), .Reset(in_1), .SALIDA(out_4[24]));
  pixelbar pixelbar_26 (.CLK(clk), .ENTRADA(\input [25]), .Reset(in_1), .SALIDA(out_4[25]));
  pixelbar pixelbar_27 (.CLK(clk), .ENTRADA(\input [26]), .Reset(in_1), .SALIDA(out_4[26]));
  pixelbar pixelbar_28 (.CLK(clk), .ENTRADA(\input [27]), .Reset(in_1), .SALIDA(out_4[27]));
  pixelbar pixelbar_29 (.CLK(clk), .ENTRADA(\input [28]), .Reset(in_1), .SALIDA(out_4[28]));
  pixelbar pixelbar_30 (.CLK(clk), .ENTRADA(\input [29]), .Reset(in_1), .SALIDA(out_4[29]));
  pixelbar pixelbar_31 (.CLK(clk), .ENTRADA(\input [30]), .Reset(in_1), .SALIDA(out_4[30]));
  pixelbar pixelbar_32 (.CLK(clk), .ENTRADA(\input [31]), .Reset(in_1), .SALIDA(out_4[31]));

  // Other names for the same wires on the sheet: _1 = \input [0]; _2 = \input [1]; _3 = \input [2]; _4 = \input [3];
  //   _5 = \input [4]; _6 = \input [5]; _7 = \input [6]; _8 = \input [7]; _9 = \input [8]; _10 = \input [9];
  //   _11 = \input [10]; _12 = \input [11]; _13 = \input [12]; _14 = \input [13]; _15 = \input [14];
  //   _16 = \input [15]; _17 = \input [16]; _18 = \input [17]; _19 = \input [18]; _20 = \input [19];
  //   _21 = \input [20]; _22 = \input [21]; _23 = \input [22]; _24 = \input [23]; _25 = \input [24];
  //   _26 = \input [25]; _27 = \input [26]; _28 = \input [27]; _29 = \input [28]; _30 = \input [29];
  //   _31 = \input [30]; _32 = \input [31]; Res = in_1
endmodule
module memoria (
  input  in_1,
  input  CLK,
  input  ACTIV,
  output [31:0] out_4,
  output [31:0] out_5,
  output [31:0] out_6,
  output [31:0] out_7,
  output [31:0] out_8,
  output [31:0] out_9,
  output [31:0] out_10,
  output [31:0] out_11,
  output [31:0] out_12,
  output [31:0] out_13,
  output [31:0] out_14,
  output [31:0] out_15,
  output [31:0] out_16,
  output [31:0] out_17,
  output [31:0] out_18,
  output [31:0] out_19
);

  wire [31:0] _1, _2, _3, _4, _5, _6, _7, _8, _9, _10, _11, _12, _13, _14, _15, _16;

  codificador codificador_1 (
    .out_8(_1), .out_9(_2), .out_13(_3), .out_6(_4), .out_4(_5), .out_15(_6), .out_18(_7), .out_17(_8),
    .out_10(_9), .out_16(_10), .out_3(_11), .out_11(_12), .out_14(_13), .out_7(_14), .out_12(_15),
    .out_5(_16), .clk(CLK), .Reset(in_1));
  columna columna_1 (.clk(CLK), .\input (_1), .out_4(out_5), .in_1(in_1));
  columna columna_2 (.clk(CLK), .\input (_2), .out_4(out_16), .in_1(in_1));
  columna columna_3 (.clk(CLK), .\input (_3), .out_4(out_17), .in_1(in_1));
  columna columna_4 (.clk(CLK), .\input (_4), .out_4(out_18), .in_1(in_1));
  columna columna_5 (.clk(CLK), .\input (_6), .out_4(out_8), .in_1(in_1));
  columna columna_6 (.clk(CLK), .\input (_5), .out_4(out_19), .in_1(in_1));
  columna columna_7 (.clk(CLK), .\input (_7), .out_4(out_4), .in_1(in_1));
  columna columna_8 (.clk(CLK), .\input (_8), .out_4(out_9), .in_1(in_1));
  columna columna_9 (.clk(CLK), .\input (_9), .out_4(out_10), .in_1(in_1));
  columna columna_10 (.clk(CLK), .\input (_10), .out_4(out_11), .in_1(in_1));
  columna columna_11 (.clk(CLK), .\input (_11), .out_4(out_12), .in_1(in_1));
  columna columna_12 (.clk(CLK), .\input (_12), .out_4(out_13), .in_1(in_1));
  columna columna_13 (.clk(CLK), .\input (_13), .out_4(out_6), .in_1(in_1));
  columna columna_14 (.clk(CLK), .\input (_14), .out_4(out_14), .in_1(in_1));
  columna columna_15 (.clk(CLK), .\input (_15), .out_4(out_7), .in_1(in_1));
  columna columna_16 (.clk(CLK), .\input (_16), .out_4(out_15), .in_1(in_1));

  // Other names for the same wires on the sheet: Res = in_1
endmodule

module barreras (
  input  clk,
  input  Reset,
  output out_3,
  output out_4,
  output out_5,
  output out_6,
  output out_7,
  output out_8,
  output out_9,
  output out_10,
  output out_11,
  output out_12,
  output out_13,
  output out_14,
  output out_15,
  output out_16,
  output out_17,
  output out_18,
  output out_19,
  output out_20,
  output out_21,
  output out_22,
  output out_23,
  output out_24,
  output out_25,
  output out_26,
  output out_27,
  output out_28,
  output out_29,
  output out_30,
  output out_31,
  output out_32,
  output out_33,
  output out_34
);

  wire b0, b1, b2, decoder_1_out0, decoder_1_out1, decoder_1_out2, decoder_1_out3, decoder_2_out0,
       decoder_2_out1, decoder_2_out2, decoder_2_out3, multiplexer_1_out, multiplexer_2_out,
       multiplexer_3_out, multiplexer_4_out, multiplexer_5_out, multiplexer_6_out, multiplexer_7_out,
       multiplexer_8_out, multiplexer_9_out, multiplexer_10_out, multiplexer_11_out, multiplexer_12_out,
       multiplexer_13_out, multiplexer_14_out, multiplexer_15_out, multiplexer_16_out, multiplexer_17_out,
       multiplexer_18_out, multiplexer_19_out, multiplexer_20_out, multiplexer_21_out, multiplexer_22_out,
       multiplexer_23_out, multiplexer_24_out, multiplexer_25_out, multiplexer_26_out, multiplexer_27_out,
       not_1_out, or_1_out, or_2_out, or_4_out;
  wire [1:0] random_1_out, random_2_out;
  wire [2:0] distancia;

  Random #(.width(2)) random_1 (.clk(clk), .out(random_1_out));  // open: next, clr
  Decoder #(.select(2), .disabled(0), .enable("false")) decoder_1 (
    .out0(decoder_1_out0), .out1(decoder_1_out1), .out2(decoder_1_out2), .out3(decoder_1_out3),
    .sel(random_1_out));
  Decoder #(.select(2), .disabled(0), .enable("false")) decoder_2 (
    .out0(decoder_2_out0), .out1(decoder_2_out1), .out2(decoder_2_out2), .out3(decoder_2_out3),
    .sel(random_2_out));
  Random #(.width(2)) random_2 (.clk(clk), .out(random_2_out));  // open: next, clr
  or or_1 (or_1_out, decoder_1_out2, decoder_1_out3);
  or or_2 (or_2_out, decoder_2_out2, decoder_2_out3);
  // Probe on distancia
  Priority_Encoder priority_encoder_1 (
    .in0(1'b0), .in1(1'b0), .in2(1'b0), .in3(decoder_1_out0), .in4(decoder_1_out1), .in5(or_1_out),
    .in6(1'b0), .in7(1'b0), .out(distancia));  // open: en_in, gs, en_out
  D_Flip_Flop d_ff_1 (.clk(clk), .D(1'b0), .Q(out_3), .reset(Reset));  // open: Qn, preset, en
  or or_3 (b0, decoder_2_out0, or_4_out);
  or or_4 (or_4_out, out_8, out_9);
  not not_1 (not_1_out, or_4_out);
  and and_1 (b1, decoder_2_out1, not_1_out);
  and and_2 (b2, not_1_out, or_2_out);
  D_Flip_Flop d_ff_2 (.clk(clk), .D(1'b0), .Q(out_4), .reset(Reset));  // open: Qn, preset, en
  DotMatrix #(.matrixcols(1), .matrixrows(32), .dotshape("circle")) dotmatrix_1 (.col0({out_34, out_33, out_32, out_31, out_30, out_29, out_28, out_27, out_26, out_25, out_24, out_23, out_22, out_21, out_20, out_19, out_18, out_17, out_16, out_15, out_14, out_13, out_12, out_11, out_10, out_9, out_8, out_7, out_6, out_5, out_4, out_3}));
  // Probe on nothing
  D_Flip_Flop d_ff_3 (.clk(clk), .D(b0), .Q(out_5), .en(Reset));  // open: Qn, preset, reset
  D_Flip_Flop d_ff_4 (.clk(clk), .D(b1), .Q(out_6), .reset(Reset));  // open: Qn, preset, en
  D_Flip_Flop d_ff_5 (.clk(clk), .D(b2), .Q(out_7), .reset(Reset));  // open: Qn, preset, en
  Multiplexer #(.select(3), .disabled(0), .enable("false")) multiplexer_1 (
    .in0(1'b0), .in1(1'b0), .in2(1'b0), .in3(out_5), .in4(1'b0), .in5(1'b0), .in6(1'b0), .in7(1'b0),
    .out(multiplexer_1_out), .sel(distancia));
  D_Flip_Flop d_ff_6 (.clk(clk), .D(multiplexer_1_out), .Q(out_8), .reset(Reset));  // open: Qn, preset, en
  Multiplexer #(.select(3), .disabled(0), .enable("false")) multiplexer_2 (
    .in0(1'b0), .in1(1'b0), .in2(1'b0), .in3(out_6), .in4(out_5), .in5(1'b0), .in6(1'b0), .in7(1'b0),
    .out(multiplexer_2_out), .sel(distancia));
  D_Flip_Flop d_ff_7 (.clk(clk), .D(multiplexer_2_out), .Q(out_9), .reset(Reset));  // open: Qn, preset, en
  Multiplexer #(.select(3), .disabled(0), .enable("false")) multiplexer_3 (
    .in0(1'b0), .in1(1'b0), .in2(1'b0), .in3(out_7), .in4(out_6), .in5(out_5), .in6(1'b0), .in7(1'b0),
    .out(multiplexer_3_out), .sel(distancia));
  D_Flip_Flop d_ff_8 (.clk(clk), .D(multiplexer_3_out), .Q(out_10), .reset(Reset));  // open: Qn, preset, en
  Multiplexer #(.select(3), .disabled(0), .enable("false")) multiplexer_4 (
    .in0(1'b0), .in1(1'b0), .in2(1'b0), .in3(out_8), .in4(out_7), .in5(out_6), .in6(1'b0), .in7(1'b0),
    .out(multiplexer_4_out), .sel(distancia));
  D_Flip_Flop d_ff_9 (.clk(clk), .D(multiplexer_4_out), .Q(out_11), .reset(Reset));  // open: Qn, preset, en
  Multiplexer #(.select(3), .disabled(0), .enable("false")) multiplexer_5 (
    .in0(1'b0), .in1(1'b0), .in2(1'b0), .in3(out_9), .in4(out_8), .in5(out_7), .in6(1'b0), .in7(1'b0),
    .out(multiplexer_5_out), .sel(distancia));
  D_Flip_Flop d_ff_10 (.clk(clk), .D(multiplexer_5_out), .Q(out_12), .reset(Reset));  // open: Qn, preset, en
  Multiplexer #(.select(3), .disabled(0), .enable("false")) multiplexer_6 (
    .in0(1'b0), .in1(1'b0), .in2(1'b0), .in3(out_10), .in4(out_9), .in5(out_8), .in6(1'b0), .in7(1'b0),
    .out(multiplexer_6_out), .sel(distancia));
  D_Flip_Flop d_ff_11 (.clk(clk), .D(multiplexer_6_out), .Q(out_13), .reset(Reset));  // open: Qn, preset, en
  Multiplexer #(.select(3), .disabled(0), .enable("false")) multiplexer_7 (
    .in0(1'b0), .in1(1'b0), .in2(1'b0), .in3(out_11), .in4(out_10), .in5(out_9), .in6(1'b0), .in7(1'b0),
    .out(multiplexer_7_out), .sel(distancia));
  D_Flip_Flop d_ff_12 (.clk(clk), .D(multiplexer_7_out), .Q(out_14), .reset(Reset));  // open: Qn, preset, en
  Multiplexer #(.select(3), .disabled(0), .enable("false")) multiplexer_8 (
    .in0(1'b0), .in1(1'b0), .in2(1'b0), .in3(out_12), .in4(out_11), .in5(out_10), .in6(1'b0), .in7(1'b0),
    .out(multiplexer_8_out), .sel(distancia));
  D_Flip_Flop d_ff_13 (.clk(clk), .D(multiplexer_8_out), .Q(out_15), .reset(Reset));  // open: Qn, preset, en
  Multiplexer #(.select(3), .disabled(0), .enable("false")) multiplexer_9 (
    .in0(1'b0), .in1(1'b0), .in2(1'b0), .in3(out_13), .in4(out_12), .in5(out_11), .in6(1'b0), .in7(1'b0),
    .out(multiplexer_9_out), .sel(distancia));
  D_Flip_Flop d_ff_14 (.clk(clk), .D(multiplexer_9_out), .Q(out_16), .reset(Reset));  // open: Qn, preset, en
  Multiplexer #(.select(3), .disabled(0), .enable("false")) multiplexer_10 (
    .in0(1'b0), .in1(1'b0), .in2(1'b0), .in3(out_14), .in4(out_13), .in5(out_12), .in6(1'b0), .in7(1'b0),
    .out(multiplexer_10_out), .sel(distancia));
  D_Flip_Flop d_ff_15 (.clk(clk), .D(multiplexer_10_out), .Q(out_17), .reset(Reset));  // open: Qn, preset, en
  Multiplexer #(.select(3), .disabled(0), .enable("false")) multiplexer_11 (
    .in0(1'b0), .in1(1'b0), .in2(1'b0), .in3(out_15), .in4(out_14), .in5(out_13), .in6(1'b0), .in7(1'b0),
    .out(multiplexer_11_out), .sel(distancia));
  D_Flip_Flop d_ff_16 (.clk(clk), .D(multiplexer_11_out), .Q(out_18), .reset(Reset));  // open: Qn, preset, en
  Multiplexer #(.select(3), .disabled(0), .enable("false")) multiplexer_12 (
    .in0(1'b0), .in1(1'b0), .in2(1'b0), .in3(out_16), .in4(out_15), .in5(out_14), .in6(1'b0), .in7(1'b0),
    .out(multiplexer_12_out), .sel(distancia));
  D_Flip_Flop d_ff_17 (.clk(clk), .D(multiplexer_12_out), .Q(out_19), .reset(Reset));  // open: Qn, preset, en
  Multiplexer #(.select(3), .disabled(0), .enable("false")) multiplexer_13 (
    .in0(1'b0), .in1(1'b0), .in2(1'b0), .in3(out_17), .in4(out_16), .in5(out_15), .in6(1'b0), .in7(1'b0),
    .out(multiplexer_13_out), .sel(distancia));
  D_Flip_Flop d_ff_18 (.clk(clk), .D(multiplexer_13_out), .Q(out_20), .reset(Reset));  // open: Qn, preset, en
  Multiplexer #(.select(3), .disabled(0), .enable("false")) multiplexer_14 (
    .in0(1'b0), .in1(1'b0), .in2(1'b0), .in3(out_18), .in4(out_17), .in5(out_16), .in6(1'b0), .in7(1'b0),
    .out(multiplexer_14_out), .sel(distancia));
  D_Flip_Flop d_ff_19 (.clk(clk), .D(multiplexer_14_out), .Q(out_21), .reset(Reset));  // open: Qn, preset, en
  Multiplexer #(.select(3), .disabled(0), .enable("false")) multiplexer_15 (
    .in0(1'b0), .in1(1'b0), .in2(1'b0), .in3(out_19), .in4(out_18), .in5(out_17), .in6(1'b0), .in7(1'b0),
    .out(multiplexer_15_out), .sel(distancia));
  D_Flip_Flop d_ff_20 (.clk(clk), .D(multiplexer_15_out), .Q(out_22), .reset(Reset));  // open: Qn, preset, en
  Multiplexer #(.select(3), .disabled(0), .enable("false")) multiplexer_16 (
    .in0(1'b0), .in1(1'b0), .in2(1'b0), .in3(out_20), .in4(out_19), .in5(out_18), .in6(1'b0), .in7(1'b0),
    .out(multiplexer_16_out), .sel(distancia));
  D_Flip_Flop d_ff_21 (.clk(clk), .D(multiplexer_16_out), .Q(out_23), .reset(Reset));  // open: Qn, preset, en
  Multiplexer #(.select(3), .disabled(0), .enable("false")) multiplexer_17 (
    .in0(1'b0), .in1(1'b0), .in2(1'b0), .in3(out_21), .in4(out_20), .in5(out_19), .in6(1'b0), .in7(1'b0),
    .out(multiplexer_17_out), .sel(distancia));
  D_Flip_Flop d_ff_22 (.clk(clk), .D(multiplexer_17_out), .Q(out_24), .reset(Reset));  // open: Qn, preset, en
  Multiplexer #(.select(3), .disabled(0), .enable("false")) multiplexer_18 (
    .in0(1'b0), .in1(1'b0), .in2(1'b0), .in3(out_22), .in4(out_21), .in5(out_20), .in6(1'b0), .in7(1'b0),
    .out(multiplexer_18_out), .sel(distancia));
  D_Flip_Flop d_ff_23 (.clk(clk), .D(multiplexer_18_out), .Q(out_25), .reset(Reset));  // open: Qn, preset, en
  Multiplexer #(.select(3), .disabled(0), .enable("false")) multiplexer_19 (
    .in0(1'b0), .in1(1'b0), .in2(1'b0), .in3(out_23), .in4(out_22), .in5(out_21), .in6(1'b0), .in7(1'b0),
    .out(multiplexer_19_out), .sel(distancia));
  D_Flip_Flop d_ff_24 (.clk(clk), .D(multiplexer_19_out), .Q(out_26), .reset(Reset));  // open: Qn, preset, en
  Multiplexer #(.select(3), .disabled(0), .enable("false")) multiplexer_20 (
    .in0(1'b0), .in1(1'b0), .in2(1'b0), .in3(out_24), .in4(out_23), .in5(out_22), .in6(1'b0), .in7(1'b0),
    .out(multiplexer_20_out), .sel(distancia));
  D_Flip_Flop d_ff_25 (.clk(clk), .D(multiplexer_20_out), .Q(out_27), .reset(Reset));  // open: Qn, preset, en
  Multiplexer #(.select(3), .disabled(0), .enable("false")) multiplexer_21 (
    .in0(1'b0), .in1(1'b0), .in2(1'b0), .in3(out_25), .in4(out_24), .in5(out_23), .in6(1'b0), .in7(1'b0),
    .out(multiplexer_21_out), .sel(distancia));
  D_Flip_Flop d_ff_26 (.clk(clk), .D(multiplexer_21_out), .Q(out_28), .reset(Reset));  // open: Qn, preset, en
  Multiplexer #(.select(3), .disabled(0), .enable("false")) multiplexer_22 (
    .in0(1'b0), .in1(1'b0), .in2(1'b0), .in3(out_26), .in4(out_25), .in5(out_24), .in6(1'b0), .in7(1'b0),
    .out(multiplexer_22_out), .sel(distancia));
  D_Flip_Flop d_ff_27 (.clk(clk), .D(multiplexer_22_out), .Q(out_29), .reset(Reset));  // open: Qn, preset, en
  Multiplexer #(.select(3), .disabled(0), .enable("false")) multiplexer_23 (
    .in0(1'b0), .in1(1'b0), .in2(1'b0), .in3(out_27), .in4(out_26), .in5(out_25), .in6(1'b0), .in7(1'b0),
    .out(multiplexer_23_out), .sel(distancia));
  D_Flip_Flop d_ff_28 (.clk(clk), .D(multiplexer_23_out), .Q(out_30), .reset(Reset));  // open: Qn, preset, en
  Multiplexer #(.select(3), .disabled(0), .enable("false")) multiplexer_24 (
    .in0(1'b0), .in1(1'b0), .in2(1'b0), .in3(out_28), .in4(out_27), .in5(out_26), .in6(1'b0), .in7(1'b0),
    .out(multiplexer_24_out), .sel(distancia));
  D_Flip_Flop d_ff_29 (.clk(clk), .D(multiplexer_24_out), .Q(out_31), .reset(Reset));  // open: Qn, preset, en
  Multiplexer #(.select(3), .disabled(0), .enable("false")) multiplexer_25 (
    .in0(1'b0), .in1(1'b0), .in2(1'b0), .in3(out_29), .in4(out_28), .in5(out_27), .in6(1'b0), .in7(1'b0),
    .out(multiplexer_25_out), .sel(distancia));
  D_Flip_Flop d_ff_30 (.clk(clk), .D(multiplexer_25_out), .Q(out_32), .reset(Reset));  // open: Qn, preset, en
  Multiplexer #(.select(3), .disabled(0), .enable("false")) multiplexer_26 (
    .in0(1'b0), .in1(1'b0), .in2(1'b0), .in3(out_30), .in4(out_29), .in5(out_28), .in6(1'b0), .in7(1'b0),
    .out(multiplexer_26_out), .sel(distancia));
  D_Flip_Flop d_ff_31 (.clk(clk), .D(multiplexer_26_out), .Q(out_33), .reset(Reset));  // open: Qn, preset, en
  Multiplexer #(.select(3), .disabled(0), .enable("false")) multiplexer_27 (
    .in0(1'b0), .in1(1'b0), .in2(1'b0), .in3(out_31), .in4(out_30), .in5(out_29), .in6(1'b0), .in7(1'b0),
    .out(multiplexer_27_out), .sel(distancia));
  D_Flip_Flop d_ff_32 (.clk(clk), .D(multiplexer_27_out), .Q(out_34), .reset(Reset));  // open: Qn, preset, en

  // Other names for the same wires on the sheet: pantalla[31:0] = {out_34, out_33, out_32, out_31, out_30, out_29, out_28, out_27, out_26, out_25, out_24, out_23, out_22, out_21, out_20, out_19, out_18, out_17, out_16, out_15, out_14, out_13, out_12, out_11, out_10, out_9, out_8, out_7, out_6, out_5, out_4, out_3};
  //   peligro1 = out_8; peligro2 = out_9
endmodule

module validacion (
  input  ac1,
  input  en,
  input  [1:0] in_3,
  input  reloj,
  input  Teclado,
  input  clk,
  input  activ,
  input  reset,
  output aL
);

  wire comparator_1_eq, comparator_2_eq, comparator_3_eq, comparator_4_eq, comparator_5_eq, comparator_6_eq,
       comparator_7_eq, comparator_8_eq, comparator_9_eq, comparator_10_eq, comparator_11_eq,
       comparator_12_eq, comparator_13_eq, comparator_14_eq, comparator_15_eq, comparator_16_eq;
  wire [5:0] bitadder_1_out, bitadder_2_out, bitadder_3_out, bitadder_4_out, bitadder_5_out, bitadder_6_out,
       bitadder_7_out, bitadder_8_out, bitadder_9_out, bitadder_10_out, bitadder_11_out, bitadder_12_out,
       bitadder_13_out, bitadder_14_out, bitadder_15_out, bitadder_16_out;
  wire [31:0] and_1_out, and_2_out, and_3_out, and_4_out, and_5_out, and_6_out, and_7_out, and_8_out,
       and_9_out, and_10_out, and_11_out, and_12_out, and_13_out, and_14_out, and_15_out, and_16_out, b1, b2,
       b3, b4, b5, b6, b7, b8, b9, b10, b11, b12, b13, b14, b15, b16, p1, p2, p3, p4, p5, p6, p7, p8, p9,
       p10, p11, p12, p13, p14, p15, p16;

  assign and_1_out = p1 & b1;  // AND_Gate and_1, 32 bits wide
  assign and_2_out = p2 & b2;  // AND_Gate and_2, 32 bits wide
  assign and_3_out = p3 & b3;  // AND_Gate and_3, 32 bits wide
  assign and_4_out = p4 & b4;  // AND_Gate and_4, 32 bits wide
  assign and_5_out = p5 & b5;  // AND_Gate and_5, 32 bits wide
  assign and_6_out = p6 & b6;  // AND_Gate and_6, 32 bits wide
  assign and_7_out = p7 & b7;  // AND_Gate and_7, 32 bits wide
  assign and_8_out = p8 & b8;  // AND_Gate and_8, 32 bits wide
  assign and_9_out = p9 & b9;  // AND_Gate and_9, 32 bits wide
  assign and_10_out = p10 & b10;  // AND_Gate and_10, 32 bits wide
  assign and_11_out = p11 & b11;  // AND_Gate and_11, 32 bits wide
  assign and_12_out = p12 & b12;  // AND_Gate and_12, 32 bits wide
  assign and_13_out = p13 & b13;  // AND_Gate and_13, 32 bits wide
  assign and_14_out = p14 & b14;  // AND_Gate and_14, 32 bits wide
  assign and_15_out = p15 & b15;  // AND_Gate and_15, 32 bits wide
  assign and_16_out = p16 & b16;  // AND_Gate and_16, 32 bits wide
  Comparator #(.width(6), .mode("unsigned")) comparator_1 (
    .a(6'b000001), .b(bitadder_1_out), .eq(comparator_1_eq));  // open: gt, lt
  BitAdder #(.width(32)) bitadder_1 (.in0(and_1_out), .out(bitadder_1_out));
  Comparator #(.width(6), .mode("unsigned")) comparator_2 (
    .a(6'b000001), .b(bitadder_2_out), .eq(comparator_2_eq));  // open: gt, lt
  BitAdder #(.width(32)) bitadder_2 (.in0(and_2_out), .out(bitadder_2_out));
  Comparator #(.width(6), .mode("unsigned")) comparator_3 (
    .a(6'b000001), .b(bitadder_3_out), .eq(comparator_3_eq));  // open: gt, lt
  BitAdder #(.width(32)) bitadder_3 (.in0(and_3_out), .out(bitadder_3_out));
  Comparator #(.width(6), .mode("unsigned")) comparator_4 (
    .a(6'b000001), .b(bitadder_4_out), .eq(comparator_4_eq));  // open: gt, lt
  BitAdder #(.width(32)) bitadder_4 (.in0(and_4_out), .out(bitadder_4_out));
  Comparator #(.width(6), .mode("unsigned")) comparator_5 (
    .a(6'b000001), .b(bitadder_5_out), .eq(comparator_5_eq));  // open: gt, lt
  BitAdder #(.width(32)) bitadder_5 (.in0(and_5_out), .out(bitadder_5_out));
  Comparator #(.width(6), .mode("unsigned")) comparator_6 (
    .a(6'b000001), .b(bitadder_6_out), .eq(comparator_6_eq));  // open: gt, lt
  BitAdder #(.width(32)) bitadder_6 (.in0(and_6_out), .out(bitadder_6_out));
  Comparator #(.width(6), .mode("unsigned")) comparator_7 (
    .a(6'b000001), .b(bitadder_7_out), .eq(comparator_7_eq));  // open: gt, lt
  BitAdder #(.width(32)) bitadder_7 (.in0(and_7_out), .out(bitadder_7_out));
  Comparator #(.width(6), .mode("unsigned")) comparator_8 (
    .a(6'b000001), .b(bitadder_8_out), .eq(comparator_8_eq));  // open: gt, lt
  BitAdder #(.width(32)) bitadder_8 (.in0(and_8_out), .out(bitadder_8_out));
  Comparator #(.width(6), .mode("unsigned")) comparator_9 (
    .a(6'b000001), .b(bitadder_9_out), .eq(comparator_9_eq));  // open: gt, lt
  BitAdder #(.width(32)) bitadder_9 (.in0(and_9_out), .out(bitadder_9_out));
  Comparator #(.width(6), .mode("unsigned")) comparator_10 (
    .a(6'b000001), .b(bitadder_10_out), .eq(comparator_10_eq));  // open: gt, lt
  BitAdder #(.width(32)) bitadder_10 (.in0(and_10_out), .out(bitadder_10_out));
  Comparator #(.width(6), .mode("unsigned")) comparator_11 (
    .a(6'b000001), .b(bitadder_11_out), .eq(comparator_11_eq));  // open: gt, lt
  BitAdder #(.width(32)) bitadder_11 (.in0(and_11_out), .out(bitadder_11_out));
  Comparator #(.width(6), .mode("unsigned")) comparator_12 (
    .a(6'b000001), .b(bitadder_12_out), .eq(comparator_12_eq));  // open: gt, lt
  BitAdder #(.width(32)) bitadder_12 (.in0(and_12_out), .out(bitadder_12_out));
  Comparator #(.width(6), .mode("unsigned")) comparator_13 (
    .a(6'b000001), .b(bitadder_13_out), .eq(comparator_13_eq));  // open: gt, lt
  BitAdder #(.width(32)) bitadder_13 (.in0(and_13_out), .out(bitadder_13_out));
  Comparator #(.width(6), .mode("unsigned")) comparator_14 (
    .a(6'b000001), .b(bitadder_14_out), .eq(comparator_14_eq));  // open: gt, lt
  BitAdder #(.width(32)) bitadder_14 (.in0(and_14_out), .out(bitadder_14_out));
  Comparator #(.width(6), .mode("unsigned")) comparator_15 (
    .a(6'b000001), .b(bitadder_15_out), .eq(comparator_15_eq));  // open: gt, lt
  BitAdder #(.width(32)) bitadder_15 (.in0(and_15_out), .out(bitadder_15_out));
  Comparator #(.width(6), .mode("unsigned")) comparator_16 (
    .a(6'b000001), .b(bitadder_16_out), .eq(comparator_16_eq));  // open: gt, lt
  BitAdder #(.width(32)) bitadder_16 (.in0(and_16_out), .out(bitadder_16_out));
  or or_1 (aL, comparator_1_eq, comparator_2_eq, comparator_3_eq, comparator_4_eq, comparator_5_eq, comparator_6_eq, comparator_7_eq, comparator_8_eq, comparator_9_eq, comparator_10_eq, comparator_11_eq, comparator_12_eq, comparator_13_eq, comparator_14_eq, comparator_15_eq, comparator_16_eq);
  memoria memoria_1 (
    .CLK(clk), .ACTIV(activ), .out_5(b1), .out_16(b2), .out_17(b3), .out_18(b4), .out_19(b5), .out_8(b6),
    .out_4(b7), .out_9(b8), .out_10(b9), .out_11(b10), .out_12(b11), .out_13(b12), .out_6(b13), .out_14(b14),
    .out_7(b15), .out_15(b16), .in_1(reset));
  // player player_1: pin names not known; wires that end beside it: Teclado, en, reloj, ac1, in_3, p1, p2, p3, p4, p5, p6, p7, p8, p9, p10, p11, p12, p13, p14, p15, p16
endmodule

module multi (
  input  [3:0] random,
  output [15:0] out_2
);

  Multiplexer #(.select(4), .width(16)) multiplexer_1 (
    .in0(16'h7e), .in1(16'h3f), .in2(16'hfc), .in3(16'h1f8), .in4(16'h3f0), .in5(16'h7e0), .in6(16'hfc0),
    .in7(16'h1f80), .in8(16'h3f00), .in9(16'h7e00), .in10(16'hfc00), .in11(16'h3f), .in12(16'hfc),
    .in13(16'h1f8), .in14(16'h7e), .in15(16'h3f0), .out(out_2), .sel(random));  // open: en
endmodule

module BarreraSegura (
  input  [31:0] Entrada,
  output Salida
);

  wire and_1_out, and_2_out, and_3_out, and_4_out, and_5_out, and_6_out, and_7_out, and_8_out, and_9_out,
       and_10_out, and_11_out, and_12_out, and_13_out, and_14_out, and_15_out, and_16_out, and_17_out,
       and_18_out, and_19_out, and_20_out, and_21_out, and_22_out, and_23_out, and_24_out, and_25_out,
       and_26_out, and_27_out, and_28_out, and_29_out, and_30_out;

  and and_1 (and_1_out, Entrada[2], Entrada[1], Entrada[0]);
  and and_2 (and_2_out, Entrada[3], Entrada[2], Entrada[1]);
  and and_3 (and_3_out, Entrada[4], Entrada[3], Entrada[2]);
  and and_4 (and_4_out, Entrada[5], Entrada[4], Entrada[3]);
  and and_5 (and_5_out, Entrada[6], Entrada[5], Entrada[4]);
  and and_6 (and_6_out, Entrada[7], Entrada[6], Entrada[5]);
  and and_7 (and_7_out, Entrada[8], Entrada[7], Entrada[6]);
  and and_8 (and_8_out, Entrada[9], Entrada[8], Entrada[7]);
  and and_9 (and_9_out, Entrada[10], Entrada[9], Entrada[8]);
  and and_10 (and_10_out, Entrada[11], Entrada[10], Entrada[9]);
  and and_11 (and_11_out, Entrada[12], Entrada[11], Entrada[10]);
  and and_12 (and_12_out, Entrada[13], Entrada[12], Entrada[11]);
  and and_13 (and_13_out, Entrada[14], Entrada[13], Entrada[12]);
  and and_14 (and_14_out, Entrada[15], Entrada[14], Entrada[13]);
  and and_15 (and_15_out, Entrada[16], Entrada[15], Entrada[14]);
  or or_1 (Salida, and_1_out, and_2_out, and_3_out, and_4_out, and_5_out, and_6_out, and_7_out, and_8_out, and_9_out, and_10_out, and_11_out, and_12_out, and_13_out, and_14_out, and_15_out, and_16_out, and_17_out, and_18_out, and_19_out, and_20_out, and_21_out, and_22_out, and_23_out, and_24_out, and_25_out, and_26_out, and_27_out, and_29_out, and_28_out, and_30_out);
  and and_16 (and_16_out, Entrada[17], Entrada[16], Entrada[15]);
  and and_17 (and_17_out, Entrada[18], Entrada[17], Entrada[16]);
  and and_18 (and_18_out, Entrada[19], Entrada[18], Entrada[17]);
  and and_19 (and_19_out, Entrada[20], Entrada[19], Entrada[18]);
  and and_20 (and_20_out, Entrada[21], Entrada[20], Entrada[19]);
  and and_21 (and_21_out, Entrada[22], Entrada[21], Entrada[20]);
  and and_22 (and_22_out, Entrada[23], Entrada[22], Entrada[21]);
  and and_23 (and_23_out, Entrada[24], Entrada[23], Entrada[22]);
  and and_24 (and_24_out, Entrada[25], Entrada[24], Entrada[23]);
  and and_25 (and_25_out, Entrada[26], Entrada[25], Entrada[24]);
  and and_26 (and_26_out, Entrada[27], Entrada[26], Entrada[25]);
  and and_27 (and_27_out, Entrada[28], Entrada[27], Entrada[26]);
  and and_28 (and_28_out, Entrada[30], Entrada[29], Entrada[28]);
  and and_29 (and_29_out, Entrada[29], Entrada[28], Entrada[27]);
  and and_30 (and_30_out, Entrada[31], Entrada[30], Entrada[29]);

  // Other names for the same wires on the sheet: _0 = Entrada[0]; _1 = Entrada[1]; _2 = Entrada[2]; _3 = Entrada[3];
  //   _4 = Entrada[4]; _5 = Entrada[5]; _6 = Entrada[6]; _7 = Entrada[7]; _8 = Entrada[8]; _9 = Entrada[9];
  //   _10 = Entrada[10]; _11 = Entrada[11]; _12 = Entrada[12]; _13 = Entrada[13]; _14 = Entrada[14];
  //   _15 = Entrada[15]; _16 = Entrada[16]; _17 = Entrada[17]; _18 = Entrada[18]; _19 = Entrada[19];
  //   _20 = Entrada[20]; _21 = Entrada[21]; _22 = Entrada[22]; _23 = Entrada[23]; _24 = Entrada[24];
  //   _25 = Entrada[25]; _26 = Entrada[26]; _27 = Entrada[27]; _28 = Entrada[28]; _29 = Entrada[29];
  //   _30 = Entrada[30]; _31 = Entrada[31]
endmodule

module BarrerasPEL (
  input  [31:0] Entrada,
  output [31:0] out_2
);

  wire s1, s2, s3, s4, s5, s6, s7, s8, s9, s10, s11, s12, s13, s14, s15, s16, s17, s18, s19, s20, s21, s22,
       s23, s24, s25, s26, s27, s28, s29, s30;

  and and_1 (out_2[2], Entrada[2], s1);
  and and_2 (s1, Entrada[2], Entrada[1], Entrada[0]);
  and and_3 (out_2[3], Entrada[3], s2);
  and and_4 (s2, Entrada[3], Entrada[2], Entrada[1]);
  and and_5 (out_2[4], Entrada[4], s3);
  and and_6 (s3, Entrada[4], Entrada[3], Entrada[2]);
  and and_7 (s4, Entrada[5], Entrada[4], Entrada[3]);
  and and_8 (s5, Entrada[6], Entrada[5], Entrada[4]);
  and and_9 (out_2[5], Entrada[5], s4);
  and and_10 (s6, Entrada[7], Entrada[6], Entrada[5]);
  and and_11 (out_2[6], Entrada[6], s5);
  and and_12 (s7, Entrada[8], Entrada[7], Entrada[6]);
  and and_13 (out_2[7], Entrada[7], s6);
  and and_14 (s8, Entrada[9], Entrada[8], Entrada[7]);
  and and_15 (out_2[8], Entrada[8], s7);
  and and_16 (s9, Entrada[10], Entrada[9], Entrada[8]);
  and and_17 (s10, Entrada[11], Entrada[10], Entrada[9]);
  and and_18 (out_2[9], Entrada[9], s8);
  and and_19 (s11, Entrada[12], Entrada[11], Entrada[10]);
  and and_20 (out_2[10], Entrada[10], s9);
  and and_21 (s13, Entrada[14], Entrada[13], Entrada[12]);
  and and_22 (s12, Entrada[13], Entrada[12], Entrada[11]);
  and and_23 (out_2[11], Entrada[11], s10);
  and and_24 (s14, Entrada[15], Entrada[14], Entrada[13]);
  and and_25 (out_2[12], Entrada[12], s11);
  and and_26 (s15, Entrada[16], Entrada[15], Entrada[14]);
  and and_27 (out_2[13], Entrada[13], s12);
  and and_28 (s16, Entrada[17], Entrada[16], Entrada[15]);
  and and_29 (s17, Entrada[18], Entrada[17], Entrada[16]);
  and and_30 (out_2[14], Entrada[14], s13);
  and and_31 (s18, Entrada[19], Entrada[18], Entrada[17]);
  and and_32 (out_2[15], Entrada[15], s14);
  and and_33 (s19, Entrada[20], Entrada[19], Entrada[18]);
  and and_34 (out_2[16], Entrada[16], s15);
  and and_35 (s21, Entrada[22], Entrada[21], Entrada[20]);
  and and_36 (s20, Entrada[21], Entrada[20], Entrada[19]);
  and and_37 (out_2[17], Entrada[17], s16);
  and and_38 (s22, Entrada[23], Entrada[22], Entrada[21]);
  and and_39 (out_2[18], Entrada[18], s17);
  and and_40 (s23, Entrada[24], Entrada[23], Entrada[22]);
  and and_41 (s24, Entrada[25], Entrada[24], Entrada[23]);
  and and_42 (out_2[19], Entrada[19], s18);
  and and_43 (s25, Entrada[26], Entrada[25], Entrada[24]);
  and and_44 (out_2[20], Entrada[20], s19);
  and and_45 (s26, Entrada[27], Entrada[26], Entrada[25]);
  and and_46 (out_2[21], Entrada[21], s20);
  and and_47 (s27, Entrada[28], Entrada[27], Entrada[26]);
  and and_48 (out_2[22], Entrada[22], s21);
  and and_49 (s28, Entrada[29], Entrada[28], Entrada[27]);
  and and_50 (s29, Entrada[30], Entrada[29], Entrada[28]);
  and and_51 (s30, Entrada[31], Entrada[30], Entrada[29]);
  and and_52 (out_2[23], Entrada[23], s22);
  and and_53 (out_2[24], Entrada[24], s23);
  and and_54 (out_2[25], Entrada[25], s24);
  and and_55 (out_2[26], Entrada[26], s25);
  and and_56 (out_2[27], Entrada[27], s26);
  and and_57 (out_2[28], Entrada[28], s27);
  and and_58 (out_2[29], Entrada[29], s28);
  and and_59 (out_2[30], Entrada[30], s29);
  and and_60 (out_2[31], Entrada[31], s30);

  assign out_2[1:0] = 2'b00;

  // Other names for the same wires on the sheet: _0 = Entrada[0]; _1 = Entrada[1]; _2 = Entrada[2]; _3 = Entrada[3];
  //   _4 = Entrada[4]; _5 = Entrada[5]; _6 = Entrada[6]; _7 = Entrada[7]; _8 = Entrada[8]; _9 = Entrada[9];
  //   _10 = Entrada[10]; _11 = Entrada[11]; _12 = Entrada[12]; _13 = Entrada[13]; _14 = Entrada[14];
  //   _15 = Entrada[15]; _16 = Entrada[16]; _17 = Entrada[17]; _18 = Entrada[18]; _19 = Entrada[19];
  //   _20 = Entrada[20]; _21 = Entrada[21]; _22 = Entrada[22]; _23 = Entrada[23]; _24 = Entrada[24];
  //   _25 = Entrada[25]; _26 = Entrada[26]; _27 = Entrada[27]; _28 = Entrada[28]; _29 = Entrada[29];
  //   _30 = Entrada[30]; _31 = Entrada[31]; v1 = out_2[2]; v2 = out_2[3]; v3 = out_2[4]; v4 = out_2[5]; v5 = out_2[6];
  //   v6 = out_2[7]; v7 = out_2[8]; v8 = out_2[9]; v9 = out_2[10]; v10 = out_2[11]; v11 = out_2[12]; v12 = out_2[13];
  //   v13 = out_2[14]; v14 = out_2[15]; v15 = out_2[16]; v16 = out_2[17]; v17 = out_2[18]; v18 = out_2[19];
  //   v19 = out_2[20]; v20 = out_2[21]; v21 = out_2[22]; v22 = out_2[23]; v23 = out_2[24]; v24 = out_2[25];
  //   v25 = out_2[26]; v26 = out_2[27]; v27 = out_2[28]; v28 = out_2[29]; v29 = out_2[30]; v30 = out_2[31]
endmodule

// 11-10
module ValidacionBarreras (
);

  wire _11_10, and_1_out, Cho13, d_ff_1_q, or_2_out, Rese, Sal13;

  or or_1 (Sal13, _11_10, d_ff_1_q);
  or or_2 (or_2_out, Rese, and_1_out);
  and and_1 (and_1_out, ~Cho13, _11_10);  // AND_Gate
  D_Flip_Flop d_ff_1 (.Q(d_ff_1_q), .preset(or_2_out), .reset(Cho13));  // open: clk, D, Qn, en
endmodule

module \var  (
  input  [31:0] Col,
  output salida
);

  wire [5:0] bitadder_1_out;

  BitAdder #(.width(32)) bitadder_1 (.in0(Col), .out(bitadder_1_out));
  Comparator #(.width(6)) comparator_1 (.a(6'b000001), .b(bitadder_1_out), .eq(salida));  // open: gt, lt
endmodule

module Pantalla_Game_Over (
  input  GAMEOVER,
  input  GANOUSER,
  output [31:0] _0,
  output [31:0] _1,
  output [31:0] _2,
  output [31:0] _3,
  output [31:0] _4
);

  // Probe on {GANOUSER, GAMEOVER}
  Multiplexer #(.select(2), .width(32)) multiplexer_1 (
    .in0(32'h899244c9), .in2({32{1'b0}}), .in3(32'h89924317), .out(_0), .sel({GANOUSER, GAMEOVER}));  // open: in1, en
  Multiplexer #(.select(2), .width(32)) multiplexer_2 (
    .in0(32'h5252452d), .in2({32{1'b0}}), .in3(32'h525244a2), .out(_1), .sel({GANOUSER, GAMEOVER}));  // open: in1, en
  Multiplexer #(.select(2), .width(32)) multiplexer_3 (
    .in0(32'h2252452b), .in2({32{1'b0}}), .in3(32'h22524492), .out(_2), .sel({GANOUSER, GAMEOVER}));  // open: in1, en
  Multiplexer #(.select(2), .width(32)) multiplexer_4 (
    .in0(32'h22525529), .in2({32{1'b0}}), .in3(32'h2252448a), .out(_3), .sel({GANOUSER, GAMEOVER}));  // open: in1, en
  Multiplexer #(.select(2), .width(32)) multiplexer_5 (
    .in0(32'h218c28c9), .in2({32{1'b0}}), .in3(32'h218c7332), .out(_4), .sel({GANOUSER, GAMEOVER}));  // open: in1, en

  // Other names for the same wires on the sheet: GUSER[1:0] = {GANOUSER, GAMEOVER}
endmodule
